// Logisim project scampplusplus.circ as structural Verilog: 11 circuits, main circuit main
module main (
  input  [15:0] in_1
);

  wire A0, A1, AI, ALT, ALTDS, ALTE, and_3_out, and_4_out, and_5_out, and_6_out, and_7_out, and_8_out,
       and_9_out, and_10_out, and_11_out, and_15_out, and_16_out, and_20_out, and_21_out, and_23_out,
       and_24_out, and_25_out, and_28_out, and_29_out, and_32_out, and_33_out, and_34_out, and_35_out,
       and_40_out, and_41_out, and_42_out, and_43_out, and_46_out, and_49_out, and_50_out, and_51_out, B0_0,
       B0_0W, B0_1, B0_1W, B0_2, B0_2W, B0_3, B0_3W, B1_0, B1_0W, B1_1, B1_1W, B1_2, B1_2W, B2_0, B2_0W,
       B2_1, B2_1W, B2_2, B2_2W, B3_0, B3_0W, B3_1, B3_1W, CHIP0, CHIP1, CHIP2, CHIP3, CLK, clock_1_out,
       decoder_1_out0, decoder_1_out1, decoder_1_out2, decoder_1_out3, decoder_2_out0, decoder_2_out1,
       decoder_2_out2, decoder_2_out3, DI, DO, EO, EX, EY, F, FETCH_STEP, GT, IDS, IE, IEN, II, INT_TAKEN,
       inv_CLK, inv_DI, inv_DO, inv_II, inv_MI8, inv_MI16, inv_MI32, inv_MO8H, inv_MO8L, inv_MO16H,
       inv_MO16L, inv_MO32, inv_PP1, inv_PP2, inv_PP4, inv_RT, IOH, IOL, IRQ, IVI, IVO, JGT, JGT_GT, JLT,
       JLT_LT, JMP, JZ, JZ_Z, LOAD_CLK, LT, M_B, M_H, M_W, MI, MI8, MI16, MI32, MO, MO8H, MO8L, MO16H, MO16L,
       MO32, n74138_1_pin4, n74138_1_pin6, n74138_1_pin15, n74138_2_pin4, n74138_2_pin7, n74138_3_pin4,
       n74138_3_pin6, n74138_3_pin15, n74138_4_pin4, n74161_1_pin3, n74161_1_pin7, n_JMP, nA0, nA1,
       nand_4_out, nand_6_out, nand_7_out, nand_8_out, nand_9_out, NO, not_3_out, not_4_out, not_5_out,
       not_7_out, not_19_out, not_20_out, not_21_out, not_22_out, not_26_out, not_27_out, not_28_out,
       not_32_out, not_33_out, not_34_out, not_35_out, NX, NY, or_1_out, or_2_out, or_3_out, or_5_out,
       or_6_out, or_7_out, or_8_out, or_9_out, or_11_out, or_12_out, or_13_out, or_18_out, or_19_out,
       or_20_out, or_21_out, or_22_out, or_23_out, or_24_out, or_25_out, or_26_out, or_27_out, or_28_out,
       or_29_out, or_30_out, or_31_out, or_32_out, or_33_out, or_34_out, or_35_out, or_36_out, or_37_out,
       or_38_out, or_39_out, or_41_out, or_42_out, or_43_out, or_44_out, or_45_out, or_46_out, or_47_out,
       or_48_out, PO, PP1, PP2, PP4, RAM_CLK, RAM_EN, RESET, RESET_T, ROM_EN, RT, SI, SO, XI, YI, Z;
  wire [2:0] rom_5_data;
  wire [6:4] rom_6_data;
  wire [7:0] ram_1_data, ram_2_data, ram_3_data, ram_4_data, rom_1_data, rom_2_data, rom_3_data, rom_4_data;
  wire [8:0] multiplexer_4_out;
  wire [11:0] n74161_1_pin14;
  wire [18:0] multiplexer_2_out, multiplexer_3_out, word_addr_pp;
  wire [18:9] multiplexer_4_out_2;
  wire [31:0] BUSS, multiplexer_1_out, register_1_q;
  wire [31:2] ADDR;

  Adder #(.width(19)) adder_1 (.a(19'h1), .b(ADDR[20:2]), .out(word_addr_pp));  // open: cin, cout
  and and_1 (FETCH_STEP, PP1, inv_II);
  // Probe on word_addr_pp
  and and_2 (INT_TAKEN, IRQ, IE, FETCH_STEP);
  not not_1 (nA1, A1);
  not not_2 (nA0, A0);
  IR ir_1 (
    .D_IN(multiplexer_1_out), .IOL(IOL), .IOH(IOH), .II(II), .CLK(CLK), .D_OUT(BUSS),
    .I_OUT(n74161_1_pin14[11:4]));
  Multiplexer #(.width(32)) multiplexer_1 (.in0(BUSS), .in1(32'h447), .out(multiplexer_1_out), .sel(INT_TAKEN));
  // Probe on multiplexer_1_out
  Register #(.width(32)) register_1 (.D(BUSS), .en(DI), .clk(CLK), .Q(register_1_q));  // open: clr
  // Probe on register_1_q
  // Probe on n74161_1_pin14[11:4]
  TTY tty_1 (.data(register_1_q[6:0]), .clk(CLK), .we(DI));  // open: clr
  or or_1 (or_1_out, A1, A0);
  and and_3 (and_3_out, A0, A1);
  // Probe on BUSS
  // Probe on n74161_1_pin14[11:4]
  IV iv_1 (.CLK(CLK), .IVI(IVI), .VO(IVO), .D_IN(BUSS), .D_OUT(BUSS));
  // Probe on {ADDR, A1, A0}
  _74161 u_74161_1 (
    .pin1(RESET_T), .pin2(inv_CLK), .pin3(n74161_1_pin3), .pin4(n74161_1_pin3), .pin5(n74161_1_pin3),
    .pin6(n74161_1_pin3), .pin7(n74161_1_pin7), .pin14(n74161_1_pin14[0]), .pin13(n74161_1_pin14[1]),
    .pin12(n74161_1_pin14[2]), .pin11(n74161_1_pin14[3]), .pin10(n74161_1_pin7), .pin9(n74161_1_pin7));  // open: pin15
  Multiplexer #(.width(19)) multiplexer_2 (
    .in0(ADDR[20:2]), .in1(word_addr_pp), .out(multiplexer_2_out), .sel(or_1_out));
  and and_4 (and_4_out, RAM_CLK, CHIP0);
  Multiplexer #(.width(19)) multiplexer_3 (.in0(ADDR[20:2]), .in1(word_addr_pp), .out(multiplexer_3_out), .sel(A1));
  and and_5 (and_5_out, RAM_CLK, CHIP1);
  RAM #(.addrWidth(19), .asyncread("true"), .databus("bidir")) ram_1 (
    .addr({multiplexer_4_out_2, multiplexer_4_out}), .we(LOAD_CLK), .oe(RAM_EN), .clk(and_6_out),
    .data(ram_1_data));
  Multiplexer #(.width(19)) multiplexer_4 (
    .in0(ADDR[20:2]), .in1(word_addr_pp), .out({multiplexer_4_out_2, multiplexer_4_out}), .sel(and_3_out));
  and and_6 (and_6_out, RAM_CLK, CHIP2);
  ROM #(.addrWidth(9)) rom_1 (.addr(multiplexer_4_out), .data(rom_1_data));
  RAM #(.addrWidth(19), .asyncread("true"), .databus("bidir")) ram_2 (
    .addr(ADDR[20:2]), .we(LOAD_CLK), .oe(RAM_EN), .clk(and_7_out), .data(ram_2_data));
  and and_7 (and_7_out, RAM_CLK, CHIP3);
  ROM #(.addrWidth(9)) rom_2 (.addr(ADDR[10:2]), .data(rom_2_data));
  RAM #(.addrWidth(19), .asyncread("true"), .databus("bidir")) ram_3 (
    .addr(multiplexer_2_out), .we(LOAD_CLK), .oe(RAM_EN), .clk(and_4_out), .data(ram_3_data));
  ROM #(.addrWidth(9)) rom_3 (.addr(multiplexer_2_out[8:0]), .data(rom_3_data));
  RAM #(.addrWidth(19), .asyncread("true"), .databus("bidir")) ram_4 (
    .addr(multiplexer_3_out), .we(LOAD_CLK), .oe(RAM_EN), .clk(and_5_out), .data(ram_4_data));
  ROM #(.addrWidth(9)) rom_4 (.addr(multiplexer_3_out[8:0]), .data(rom_4_data));
  // Probe on n74161_1_pin14
  ROM #(.addrWidth(12)) rom_5 (.addr(n74161_1_pin14), .data({F, NY, EY, NX, EX, rom_5_data}));
  ROM #(.addrWidth(12)) rom_6 (.addr(n74161_1_pin14), .data({EO, rom_6_data, JZ, JGT, JLT, NO}));
  nand nand_1 (inv_CLK, CLK, CLK);
  nand nand_2 (inv_RT, RT, RT);
  nand nand_3 (RESET_T, inv_RT, RESET);
  // Probe on RESET_T
  // Probe on ram_3_data
  and and_8 (and_8_out, ROM_EN, CHIP0);
  assign ram_3_data = and_8_out ? rom_3_data : 8'bz;  // Controlled_Buffer controlled_buffer_1
  // Probe on ram_4_data
  and and_9 (and_9_out, ROM_EN, CHIP1);
  assign ram_4_data = and_9_out ? rom_4_data : 8'bz;  // Controlled_Buffer controlled_buffer_2
  // Probe on ram_1_data
  and and_10 (and_10_out, ROM_EN, CHIP2);
  assign ram_1_data = and_10_out ? rom_1_data : 8'bz;  // Controlled_Buffer controlled_buffer_3
  // Probe on ram_2_data
  and and_11 (and_11_out, ROM_EN, CHIP3);
  assign ram_2_data = and_11_out ? rom_2_data : 8'bz;  // Controlled_Buffer controlled_buffer_4
  nand nand_4 (nand_4_out, RESET_T, RESET_T);
  // Probe on in_1
  assign BUSS[7:0] = B0_0 ? ram_3_data : 8'bz;  // Controlled_Buffer controlled_buffer_5
  assign BUSS[7:0] = B1_0 ? ram_4_data : 8'bz;  // Controlled_Buffer controlled_buffer_6
  assign BUSS[7:0] = B2_0 ? ram_1_data : 8'bz;  // Controlled_Buffer controlled_buffer_7
  assign BUSS[7:0] = B3_0 ? ram_2_data : 8'bz;  // Controlled_Buffer controlled_buffer_8
  Button u_IRQ (.out(IRQ));
  assign BUSS[15:8] = B0_1 ? ram_3_data : 8'bz;  // Controlled_Buffer controlled_buffer_9
  assign BUSS[23:16] = B0_2 ? ram_3_data : 8'bz;  // Controlled_Buffer controlled_buffer_10
  assign BUSS[15:8] = B1_1 ? ram_4_data : 8'bz;  // Controlled_Buffer controlled_buffer_11
  assign BUSS[23:16] = B1_2 ? ram_4_data : 8'bz;  // Controlled_Buffer controlled_buffer_12
  assign BUSS[31:24] = B0_2 ? ram_4_data : 8'bz;  // Controlled_Buffer controlled_buffer_13
  assign BUSS[15:8] = B2_1 ? ram_1_data : 8'bz;  // Controlled_Buffer controlled_buffer_14
  assign BUSS[23:16] = B2_2 ? ram_1_data : 8'bz;  // Controlled_Buffer controlled_buffer_15
  assign BUSS[31:24] = B1_2 ? ram_1_data : 8'bz;  // Controlled_Buffer controlled_buffer_16
  assign BUSS[15:8] = B3_1 ? ram_2_data : 8'bz;  // Controlled_Buffer controlled_buffer_17
  assign BUSS[23:16] = B0_3 ? ram_2_data : 8'bz;  // Controlled_Buffer controlled_buffer_18
  nand nand_5 (inv_II, II, II);
  and and_12 (JZ_Z, JZ, Z);
  and and_13 (JLT_LT, JLT, LT);
  and and_14 (JGT_GT, JGT, GT);
  or or_2 (or_2_out, Z, LT);
  or or_3 (or_3_out, JZ_Z, JGT_GT);
  assign BUSS[31:24] = B0_3 ? ram_3_data : 8'bz;  // Controlled_Buffer controlled_buffer_19
  assign BUSS[31:24] = B2_2 ? ram_2_data : 8'bz;  // Controlled_Buffer controlled_buffer_20
  J_K_Flip_Flop j_k_ff_1 (.J(not_3_out), .K(not_4_out), .clk(CLK), .Q(IE), .reset(not_5_out));  // open: Qn, preset
  not not_3 (not_3_out, IEN);
  not not_4 (not_4_out, IDS);
  not not_5 (not_5_out, RESET);
  not not_6 (GT, or_2_out);
  or or_4 (JMP, or_3_out, JLT_LT);
  assign ram_3_data = B0_2W ? BUSS[23:16] : 8'bz;  // Controlled_Buffer controlled_buffer_21
  assign ram_3_data = B0_3W ? BUSS[31:24] : 8'bz;  // Controlled_Buffer controlled_buffer_22
  assign ram_4_data = B1_2W ? BUSS[23:16] : 8'bz;  // Controlled_Buffer controlled_buffer_23
  assign ram_4_data = B0_2W ? BUSS[31:24] : 8'bz;  // Controlled_Buffer controlled_buffer_24
  assign ram_1_data = B2_2W ? BUSS[23:16] : 8'bz;  // Controlled_Buffer controlled_buffer_25
  assign ram_1_data = B1_2W ? BUSS[31:24] : 8'bz;  // Controlled_Buffer controlled_buffer_26
  assign ram_2_data = B0_3W ? BUSS[23:16] : 8'bz;  // Controlled_Buffer controlled_buffer_27
  assign ram_2_data = B2_2W ? BUSS[31:24] : 8'bz;  // Controlled_Buffer controlled_buffer_28
  assign BUSS[15:8] = MO8H ? {8{1'b1}} : 8'bz;  // Controlled_Buffer controlled_buffer_29
  assign BUSS[15:8] = MO8L ? {8{1'b0}} : 8'bz;  // Controlled_Buffer controlled_buffer_30
  assign ram_3_data = B0_0W ? BUSS[7:0] : 8'bz;  // Controlled_Buffer controlled_buffer_31
  assign ram_3_data = B0_1W ? BUSS[15:8] : 8'bz;  // Controlled_Buffer controlled_buffer_32
  assign ram_4_data = B1_0W ? BUSS[7:0] : 8'bz;  // Controlled_Buffer controlled_buffer_33
  assign ram_4_data = B1_1W ? BUSS[15:8] : 8'bz;  // Controlled_Buffer controlled_buffer_34
  assign ram_1_data = B2_0W ? BUSS[7:0] : 8'bz;  // Controlled_Buffer controlled_buffer_35
  assign ram_1_data = B2_1W ? BUSS[15:8] : 8'bz;  // Controlled_Buffer controlled_buffer_36
  assign ram_2_data = B3_0W ? BUSS[7:0] : 8'bz;  // Controlled_Buffer controlled_buffer_37
  assign ram_2_data = B3_1W ? BUSS[15:8] : 8'bz;  // Controlled_Buffer controlled_buffer_38
  or or_5 (or_5_out, MO16H, MO8H);
  assign BUSS[31:24] = or_5_out ? {8{1'b1}} : 8'bz;  // Controlled_Buffer controlled_buffer_39
  assign BUSS[23:16] = or_5_out ? {8{1'b1}} : 8'bz;  // Controlled_Buffer controlled_buffer_40
  assign BUSS[23:16] = or_6_out ? {8{1'b0}} : 8'bz;  // Controlled_Buffer controlled_buffer_41
  assign BUSS[31:24] = or_6_out ? {8{1'b0}} : 8'bz;  // Controlled_Buffer controlled_buffer_42
  or or_6 (or_6_out, MO8L, MO16L);
  _74138 #(.ShowInternalStructure("true")) u_74138_1 (
    .pin1(rom_5_data[0]), .pin2(rom_5_data[1]), .pin3(rom_5_data[2]), .pin4(n74138_1_pin4),
    .pin5(n74138_1_pin4), .pin6(n74138_1_pin6), .pin7(SI), .pin15(n74138_1_pin15), .pin14(AI),
    .pin13(inv_DI), .pin12(II), .pin11(XI), .pin10(YI), .pin9(IVI));
  _74138 #(.ShowInternalStructure("true")) u_74138_2 (
    .pin1(EX), .pin2(NX), .pin3(EY), .pin4(n74138_2_pin4), .pin5(n74138_2_pin4), .pin6(EO),
    .pin7(n74138_2_pin7), .pin15(PO), .pin14(inv_DO), .pin13(inv_MO8L), .pin12(inv_MO8H), .pin11(inv_MO16L),
    .pin10(inv_MO16H), .pin9(inv_MO32));
  _74138 #(.ShowInternalStructure("true")) u_74138_3 (
    .pin1(rom_6_data[4]), .pin2(rom_6_data[5]), .pin3(rom_6_data[6]), .pin4(n74138_3_pin4),
    .pin5(n74138_3_pin4), .pin6(n74138_3_pin6), .pin7(inv_MI32), .pin15(n74138_3_pin15), .pin14(inv_PP1),
    .pin13(inv_PP2), .pin12(inv_PP4), .pin11(RT), .pin10(inv_MI8), .pin9(inv_MI16));
  not not_7 (not_7_out, ALTE);
  not not_8 (n_JMP, JMP);
  not not_9 (DO, inv_DO);
  not not_10 (DI, inv_DI);
  not not_11 (MO8L, inv_MO8L);
  not not_12 (MO8H, inv_MO8H);
  not not_13 (MO16L, inv_MO16L);
  not not_14 (MO16H, inv_MO16H);
  not not_15 (MO32, inv_MO32);
  not not_16 (MI8, inv_MI8);
  not not_17 (MI16, inv_MI16);
  not not_18 (MI32, inv_MI32);
  or or_7 (or_7_out, MO8L, MO8H);
  or or_8 (or_8_out, MO16L, MO16H);
  or or_9 (or_9_out, MI8, MI16);
  or or_10 (M_W, MI32, MO32);
  or or_11 (or_11_out, MO16H, MO16L);
  or or_12 (or_12_out, MO8H, MO8L);
  // NoConnect on n74138_1_pin15
  // NoConnect on n74138_3_pin15
  J_K_Flip_Flop j_k_ff_2 (.J(not_7_out), .K(not_19_out), .clk(CLK), .Q(ALT), .reset(not_20_out));  // open: Qn, preset
  not not_19 (not_19_out, ALTDS);
  not not_20 (not_20_out, RESET);
  or or_13 (or_13_out, or_7_out, or_8_out);
  or or_14 (MI, or_9_out, MI32);
  or or_15 (M_H, or_11_out, MI16);
  or or_16 (M_B, or_12_out, MI8);
  // Probe on BUSS
  // Probe on BUSS
  not not_21 (not_21_out, n74138_2_pin7);
  or or_17 (MO, or_13_out, MO32);
  _74138 #(.ShowInternalStructure("true")) u_74138_4 (
    .pin1(NY), .pin2(F), .pin3(NO), .pin4(n74138_4_pin4), .pin5(n74138_4_pin4), .pin6(not_21_out),
    .pin7(IOL), .pin15(SO), .pin14(IEN), .pin13(IDS), .pin12(ALTDS), .pin11(ALTE), .pin10(IVO), .pin9(IOH));
  not not_22 (not_22_out, CHIP3);
  and and_15 (and_15_out, CHIP0, not_22_out);
  and and_16 (and_16_out, not_33_out, and_15_out);
  or or_18 (or_18_out, and_16_out, B2_2);
  and and_17 (B0_0, or_18_out, MO);
  or or_19 (or_19_out, and_16_out, B2_2W);
  and and_18 (B0_0W, MI, or_19_out);
  and and_19 (B0_1W, MI, or_21_out);
  and and_20 (and_20_out, CHIP3, CHIP0);
  and and_21 (and_21_out, not_33_out, and_20_out);
  or or_20 (or_20_out, and_21_out, B1_2);
  and and_22 (B0_1, or_20_out, MO);
  or or_21 (or_21_out, and_21_out, B1_2W);
  or or_22 (or_22_out, ADDR[10], ADDR[11]);
  or or_23 (or_23_out, ADDR[12], ADDR[13]);
  or or_24 (or_24_out, or_23_out, or_25_out);
  or or_25 (or_25_out, ADDR[14], ADDR[15]);
  or or_26 (or_26_out, ADDR[16], ADDR[17]);
  or or_27 (or_27_out, or_26_out, or_28_out);
  or or_28 (or_28_out, ADDR[18], ADDR[19]);
  not not_23 (PP1, inv_PP1);
  not not_24 (PP2, inv_PP2);
  not not_25 (PP4, inv_PP4);
  or or_29 (or_29_out, or_22_out, or_30_out);
  or or_30 (or_30_out, or_24_out, or_27_out);
  not not_26 (not_26_out, CHIP0);
  and and_23 (and_23_out, CHIP1, not_26_out);
  and and_24 (and_24_out, CHIP1, CHIP2);
  or or_31 (or_31_out, and_24_out, and_23_out);
  and and_25 (and_25_out, not_33_out, or_31_out);
  or or_32 (or_32_out, and_25_out, B0_3);
  and and_26 (B1_0, or_32_out, MO);
  or or_33 (or_33_out, and_25_out, B0_3W);
  and and_27 (B1_0W, MI, or_33_out);
  and and_28 (and_28_out, CHIP0, CHIP1);
  and and_29 (and_29_out, not_33_out, and_28_out);
  or or_34 (or_34_out, and_29_out, B2_2);
  and and_30 (B1_1, or_34_out, MO);
  or or_35 (or_35_out, and_29_out, B2_2W);
  and and_31 (B1_1W, MI, or_35_out);
  nand nand_6 (nand_6_out, MI, CLK);
  nand nand_7 (nand_7_out, MO, or_29_out);
  nand nand_8 (nand_8_out, or_29_out, or_29_out);
  not not_27 (not_27_out, CHIP1);
  and and_32 (and_32_out, CHIP2, not_27_out);
  and and_33 (and_33_out, CHIP2, CHIP1, not_28_out);
  and and_34 (and_34_out, not_33_out, and_32_out);
  and and_35 (and_35_out, not_33_out, and_33_out);
  or or_36 (or_36_out, and_34_out, B0_2);
  or or_37 (or_37_out, and_35_out, B0_3);
  and and_36 (B2_0, or_36_out, MO);
  and and_37 (B2_0W, MI, or_38_out);
  nand nand_9 (nand_9_out, MO, nand_8_out);
  not not_28 (not_28_out, CHIP3);
  and and_38 (B2_1, or_37_out, MO);
  or or_38 (or_38_out, and_34_out, B0_2W);
  or or_39 (or_39_out, and_35_out, B0_3W);
  and and_39 (B2_1W, MI, or_39_out);
  not not_29 (LOAD_CLK, nand_6_out);
  not not_30 (RAM_EN, nand_7_out);
  not not_31 (ROM_EN, nand_9_out);
  or or_40 (RAM_CLK, LOAD_CLK, RAM_EN);
  and and_40 (and_40_out, not_33_out, and_41_out);
  not not_32 (not_32_out, CHIP2);
  and and_41 (and_41_out, CHIP3, not_32_out);
  and and_42 (and_42_out, CHIP3, CHIP2);
  and and_43 (and_43_out, not_33_out, and_42_out);
  or or_41 (or_41_out, and_40_out, B1_2);
  or or_42 (or_42_out, and_43_out, B0_2);
  and and_44 (B3_0, or_41_out, MO);
  and and_45 (B3_1, or_42_out, MO);
  and and_46 (and_46_out, CHIP3, CHIP2, CHIP1, CHIP0);
  not not_33 (not_33_out, and_46_out);
  or or_43 (or_43_out, and_40_out, B1_2W);
  and and_47 (B3_0W, MI, or_43_out);
  or or_44 (or_44_out, and_43_out, B0_2W);
  and and_48 (B3_1W, MI, or_44_out);
  _74377 u_74377_1 (
    .pin1(AI), .pin2(A0), .pin3(BUSS[0]), .pin4(BUSS[1]), .pin5(A1), .pin6(ADDR[2]), .pin7(BUSS[2]),
    .pin8(BUSS[3]), .pin9(ADDR[3]), .pin19(ADDR[7]), .pin18(BUSS[7]), .pin17(BUSS[6]), .pin16(ADDR[6]),
    .pin15(ADDR[5]), .pin14(BUSS[5]), .pin13(BUSS[4]), .pin12(ADDR[4]), .pin11(CLK));
  _74377 u_74377_2 (
    .pin1(AI), .pin2(ADDR[8]), .pin3(BUSS[8]), .pin4(BUSS[9]), .pin5(ADDR[9]), .pin6(ADDR[10]),
    .pin7(BUSS[10]), .pin8(BUSS[11]), .pin9(ADDR[11]), .pin19(ADDR[15]), .pin18(BUSS[15]), .pin17(BUSS[14]),
    .pin16(ADDR[14]), .pin15(ADDR[13]), .pin14(BUSS[13]), .pin13(BUSS[12]), .pin12(ADDR[12]), .pin11(CLK));
  _74377 u_74377_3 (
    .pin1(AI), .pin2(ADDR[16]), .pin3(BUSS[16]), .pin4(BUSS[17]), .pin5(ADDR[17]), .pin6(ADDR[18]),
    .pin7(BUSS[18]), .pin8(BUSS[19]), .pin9(ADDR[19]), .pin19(ADDR[23]), .pin18(BUSS[23]), .pin17(BUSS[22]),
    .pin16(ADDR[22]), .pin15(ADDR[21]), .pin14(BUSS[21]), .pin13(BUSS[20]), .pin12(ADDR[20]), .pin11(CLK));
  _74377 u_74377_4 (
    .pin1(AI), .pin2(ADDR[24]), .pin3(BUSS[24]), .pin4(BUSS[25]), .pin5(ADDR[25]), .pin6(ADDR[26]),
    .pin7(BUSS[26]), .pin8(BUSS[27]), .pin9(ADDR[27]), .pin19(ADDR[31]), .pin18(BUSS[31]), .pin17(BUSS[30]),
    .pin16(ADDR[30]), .pin15(ADDR[29]), .pin14(BUSS[29]), .pin13(BUSS[28]), .pin12(ADDR[28]), .pin11(CLK));
  Demultiplexer #(.select(3)) demultiplexer_1 (
    .out0(B2_2), .out1(B0_3), .out2(B0_2), .out3(B1_2), .out4(B2_2W), .out5(B0_3W), .out6(B0_2W),
    .out7(B1_2W), .in(1'b1), .sel({MI, A1, A0}));
  not not_34 (not_34_out, INT_TAKEN);
  Decoder #(.select(2)) decoder_1 (
    .out0(decoder_1_out0), .out1(decoder_1_out1), .out2(decoder_1_out2), .out3(decoder_1_out3),
    .sel({A1, A0}), .en(M_H));
  Clock clock_1 (.out(clock_1_out));
  and and_49 (and_49_out, PP1, not_34_out);
  and and_50 (and_50_out, PP2, not_34_out);
  and and_51 (and_51_out, PP4, not_34_out);
  Decoder #(.select(2)) decoder_2 (
    .out0(decoder_2_out0), .out1(decoder_2_out1), .out2(decoder_2_out2), .out3(decoder_2_out3),
    .sel({A1, A0}), .en(M_B));
  POR #(.PorHighDuration(1), .porTransition(2)) por_1 (.out(RESET));
  not not_35 (not_35_out, JMP);
  or or_45 (or_45_out, decoder_1_out0, decoder_1_out3);
  or or_46 (or_46_out, decoder_1_out0, decoder_1_out1);
  or or_47 (or_47_out, decoder_1_out1, decoder_1_out2);
  or or_48 (or_48_out, decoder_1_out2, decoder_1_out3);
  and and_52 (CLK, RESET, clock_1_out);
  ALU alu_1 (
    .ALT(ALT), .CLK(CLK), .NO(NO), .F(F), .EX(EX), .NX(NX), .EY(EY), .NY(NY), .EO(EO), .X_IN(BUSS),
    .Y_IN(BUSS), .XI(XI), .YI(YI), .ALU_OUT(BUSS), .Z(Z), .LT(LT));
  PC pc_1 (
    .PP1(and_49_out), .PP2(and_50_out), .PP4(and_51_out), .PO(PO), .RESET(RESET), .JMP(not_35_out),
    .CLK(CLK), .D_IN(BUSS), .D_OUT(BUSS));
  // Probe on BUSS
  SP sp_1 (.D_IN(BUSS), .CLK(CLK), .SI(SI), .SO(SO), .D_OUT(BUSS));
  or or_49 (CHIP0, or_45_out, decoder_2_out0, M_W);
  or or_50 (CHIP1, or_46_out, decoder_2_out1, M_W);
  or or_51 (CHIP2, or_47_out, decoder_2_out2, M_W);
  or or_52 (CHIP3, or_48_out, decoder_2_out3, M_W);
  // Probe on BUSS
  // also tied to GND on the sheet: {n74161_1_pin3, n74138_1_pin4, n74138_2_pin4, n74138_3_pin4, n74138_4_pin4}
  // also tied to VCC on the sheet: {n74161_1_pin7, n74138_1_pin6, n74138_3_pin6}

  // Other names for the same wires on the sheet: ADDR[1:0] = {A1, A0}; B1_3 = B0_2; B1_3W = B0_2W; B2_3 = B1_2;
  //   B2_3W = B1_2W; B3_2 = B0_3; B3_2W = B0_3W; B3_3 = B2_2; B3_3W = B2_2W; word_addr[18:0] = ADDR[20:2]

  // Notes on the sheet:
  //   00 = 8 bit, 01 = half word, 10=word, 11 ERROR
  //   contents of rom_1 (hex, n*v repeats v):
  //   8 13 7 2d 0 0 5*10 f 1a 10 0 f 1e 8 0 b 1d 22 5 0 24 2a 0 0 78 10 2e f 38 0 0 0 f8 0 41 0 0 40 0 20
  //   10 f8 0 41 0 0 40 0 2 1 f8 0 11 11 f8 0 2e 0 0 2e 8 5 2e 18 3 2e 28 4 10 34 34 1d 1 0 0 a 0 0 0 15 0
  //   0 0 24 2 a 4 0 8 4 e 5*0 3 4 4*0 2 11 4 0 fc 8 0 0 33 38 0 44 4*0 8 c 0 1 c 0 4 33 38 0 8 4*0 48 6f
  //   6f 21
  //   contents of rom_2 (hex, n*v repeats v):
  //   0 0 f 1a 10 8 0 1 2 3 1 0 5f 5 10 0 f 21 10 f 23 f8 0 24 c 2a 2a 10 0 2a 0 34 7f 3c 0 0 0 80 f8 0 41
  //   0 0 40 0 10 8 f8 0 41 0 0 40 0 1 0 52 43 f 12 0 0 2e 4 2 2e 14 3 2e 24 1 ff 0 30 30 0 0 5 0 42 0 0
  //   2f 42 0 0 24 28 f 0 26 0 0 11 0 43 0 0 26 0 0 42 0 0 5 0 29 2 3a 44 0 33 0 41 0 bf 32 4 c c c 46 31
  //   31 0 d 3b 0 ff 4 f7 46 31 2 34 38 0 65 2c 72 a
  //   contents of rom_3 (hex, n*v repeats v):
  //   5 4*0 45 45 4*f 14 10 f 1b 8 10 0 1 e 0 16 f 8 d 1 1 1 e 0 f 5*0 10 40 0 80 40 f8 0 41 0 0 40 0 8 4
  //   f8 0 41 0 0 3c 0 69 69 0 39 0 0 0 1 2e 10 0 2e 20 0 30 ff 3 34 34 38 0 0 2e b5 4 0 0 b9 4 0 16 1 0 0
  //   5 4 0 d8 4 0 4 0 8 4 0 e9 4 0 0 11 4 0 2 4 2e fc 80 fc 1d 1 0 2e 8 c 10 c 8 4 2e 8 6 4 ff 33 1 8 0 0
  //   0 15 46 6c 20 6c
  //   contents of rom_4 (hex, n*v repeats v):
  //   0 6 0 8 0 f 4 4*0 3 64 0 f 1c 4 10 f 1f 10 0 0 0 1 10 f f 2d 0 0 10 1c 0 0 2f 2e 0 0 40 0 40 20 f8 0
  //   41 0 0 40 0 4 2 f8 0 41 f8 0 13 22 2e 3 3c 0 a 2e c 0 2e 1c 4 2e 30 ff 30 30 30 24 f 8 0 1 3c 0 0 1
  //   3c 0 1 a 26 0 0 26 0 1 0 4 3c 0 0 26 0 1 3c 0 8 26 42 0 33 2e f8 40 0 1 f8 0 fc 0 16 16 16 c c 2e c
  //   20 2 0 ff c 0 c 3d 0 35 2 4 6c 77 64
  //   contents of rom_5 (hex, n*v repeats v):
  //   1 23 19 35 ac 11*0 1 23 b9 31 15 ac 10*0 1 23 b9 31 25 ac 10*0 1 23 b9 31 35 ac 10*0 1 23 0 1 31 34
  //   b9 35 a8 7*0 1 23 1 37 12*0 1 23 1 36 12*0 1 23 7c 13*0 1 23 78 13*0 1 23 b8 13*0 1 23 3d fc ac 89
  //   14 9*0 1 23 3d fc ac 89 24 9*0 1 23 3d fc ac 89 34 9*0 1 23 b9 34 12*0 1 23 1 31 88 11*0 1 23 f9 8a
  //   12*0 1 23 fc 13*0 1 23 1 24 12*0 1 23 1 34 12*0 1 23 8d 13*0 1 23 fd ac 12*0 1 23 0 1 35 b9 34 a8
  //   8*0 1 23 b9 35 a8 11*0 1 23 b9 35 1 14 ac 89 34 7*0 1 23 b9 35 1 14 ac b9 88 a1 14 5*0 1 23 ac 13*0
  //   1 23 fd bc 12*0 1 23 dc 13*0 1 23 cc 13*0 1 23 b9 35 b0 11*0 1 23 8d ac 12*0 1 23 fd 2c 12*0 1 23 b9
  //   35 2c 11*0 1 23 fd 7c 12*0 1 23 b9 78 2d 34 2c 9*0 1 23 1 25 12*0 1 23 3d a1 f8 1 14 ef 8*0 1 23 1
  //   24 3d a1 88 1 14 ef 6*0 1 23 1 34 3d a1 88 1 14 ef 6*0 1 23 3d a1 88 fc ef 9*0 1 23 3d a1 88 fc ef
  //   9*0 1 23 3d a1 88 fc ef 9*0 1 23 3d fc ad a7 a1 14 8*0 1 23 3d fc ad a7 a1 24 8*0 1 23 3d fc ad a7
  //   a1 34 8*0 1 23 1 30 12*0 1 23 0 1 15 b9 a0 9*0 1 23 0 1 25 b9 a0 9*0 1 23 0 1 35 b9 a0 9*0 1 23 b9
  //   88 12*0 1 23 b9 1 19 35 b9 a0 8*0 1 23 b9 34 8d a8 10*0 1 23 b9 35 f0 11*0 1 23 b9 31 15 a0 10*0 1
  //   23 b9 31 25 a0 10*0 1 23 b9 31 35 a0 10*0 1 23 1 30 12*0 1 23 0 5 fc a8 10*0 1 23 0 5 fc e8 10*0 1
  //   23 1 30 12*0 1 23 b9 35 1 31 a2 9*0 1 23 b9 31 15 1 31 a2 8*0 1 23 b9 31 25 1 31 a2 8*0 1 23 b9 31
  //   35 1 31 a2 8*0 1 23 b9 34 1 35 28 9*0 1 23 b9 34 1 15 b9 78 8*0 1 23 0 1 14 3d a1 0 ef 5 bd a1 30 0
  //   0 0 1 23 0 1 14 3d a1 0 ef 5 bd a1 35 a1 30 0 1 23 3d fc ad a7 a1 30 8*0 1 23 3d fc ad a7 a1 f8 78
  //   30 6*0 1 23 3d fc 4*f5 a1 ac 8f 30 4*0 1 23 b8 38 3d a1 0 fc ef 78 6*0 1 23 14*0 1 23 14*0 1 23 14*0
  //   1 23 14*0 1 23 14*0 1 23 14*0 1 23 14*0 1 23 14*0 1 23 14*0 1 23 14*0 1 23 14*0 1 23 14*0 1 23 14*0
  //   1 23 14*0 1 23 14*0 1 23 14*0 1 23 14*0 1 23 14*0 1 23 14*0 1 23 14*0 1 23 14*0 1 23 14*0 1 23 14*0
  //   1 23 14*0 1 23 14*0 1 23 14*0 1 23 14*0 1 23 14*0 1 23 14*0 1 23 14*0 1 23 14*0 1 23 14*0 1 23 14*0
  //   1 23 14*0 1 23 14*0 1 23 14*0 1 23 14*0 1 23 14*0 1 23 14*0 1 23 14*0 1 23 14*0 1 23 14*0 1 23 14*0
  //   1 23 14*0 1 23 14*0 1 23 14*0 1 23 14*0 1 23 14*0 1 23 14*0 1 23 14*0 1 23 14*0 1 23 14*0 1 23 14*0
  //   1 23 14*0 1 23 14*0 1 23 14*0 1 23 14*0 1 23 14*0 1 23 14*0 1 23 14*0 1 23 14*0 1 23 14*0 1 23 14*0
  //   1 23 14*0 1 23 14*0 1 23 14*0 1 23 14*0 1 23 14*0 1 23 14*0 1 23 14*0 1 23 14*0 1 23 14*0 1 23 14*0
  //   1 23 14*0 1 23 14*0 1 23 14*0 1 23 14*0 1 23 14*0 1 23 14*0 1 23 14*0 1 23 14*0 1 23 14*0 1 23 14*0
  //   1 23 14*0 1 23 14*0 1 23 14*0 1 23 14*0 1 23 14*0 1 23 14*0 1 23 14*0 1 23 14*0 1 23 14*0 1 23 14*0
  //   1 23 14*0 1 23 14*0 1 23 14*0 1 23 14*0 1 23 14*0 1 23 14*0 1 23 14*0 1 23 14*0 1 23 14*0 1 23 14*0
  //   1 23 14*0 1 23 14*0 1 23 14*0 1 23 14*0 1 23 14*0 1 23 14*0 1 23 14*0 1 23 14*0 1 23 14*0 1 23 14*0
  //   1 23 14*0 1 23 14*0 1 23 14*0 1 23 14*0 1 23 14*0 1 23 14*0 1 23 14*0 1 23 14*0 1 23 14*0 1 23 14*0
  //   1 23 14*0 1 23 14*0 1 23 14*0 1 23 14*0 1 23 14*0 1 23 14*0 1 23 14*0 1 23 14*0 1 23 14*0 1 23 14*0
  //   1 23 14*0 1 23 14*0 1 23 14*0 1 23 14*0 1 23 14*0 1 23 14*0 1 23 14*0 1 23 14*0 1 23 14*0 1 23 14*0
  //   1 23 14*0 1 23 14*0 1 23 14*0 1 23 14*0 1 23 14*0 1 23 14*0 1 23 14*0 1 23 14*0 1 23 14*0 1 23 14*0
  //   1 23 14*0 1 23 14*0 1 23 14*0 1 23 14*0 1 23 14*0 1 23 14*0 1 23 14*0 1 23 14*0 1 23 14*0 1 23 14*0
  //   1 23 14*0 1 23 14*0 1 23 14*0 1 23 14*0 1 23 14*0 1 23 14*0 1 23 14*0 1 23 14*0 1 23 14*0 1 23 14*0
  //   1 23 14*0 1 23 14*0 1 23 14*0 1 23 14*0 1 23 14*0 1 23 14*0 1 23 14*0 1 23 14*0 1 23 14*0 1 23 14*0
  //   1 23
  //   contents of rom_6 (hex, n*v repeats v):
  //   80 90 90 80 0 11*c0 80 90 91 80 80 0 10*c0 80 90 91 80 80 0 10*c0 80 90 91 80 80 0 10*c0 80 90 90 80
  //   b0 80 81 80 70 7*c0 80 90 80 b0 12*c0 80 90 80 b0 12*c0 80 90 81 13*c0 80 90 80 13*c0 80 90 80 13*c0
  //   80 90 80 91 0 0 80 9*c0 80 90 80 91 0 0 80 9*c0 80 90 80 91 0 0 80 9*c0 80 90 91 80 12*c0 80 90 80
  //   b0 70 11*c0 80 90 91 0 12*c0 80 90 91 13*c0 80 90 80 a0 12*c0 80 90 80 b0 12*c0 80 90 0 13*c0 80 90
  //   91 0 12*c0 80 90 90 80 b0 81 80 70 8*c0 80 90 91 80 70 11*c0 80 90 91 80 80 90 0 0 80 7*c0 80 90 91
  //   80 80 90 0 81 70 0 80 5*c0 80 90 0 13*c0 80 90 91 1 12*c0 80 90 1 13*c0 80 90 0 13*c0 80 90 91 80 70
  //   11*c0 80 90 0 0 12*c0 80 90 91 0 12*c0 80 90 91 80 0 11*c0 80 90 91 1 12*c0 80 90 91 71 1 80 0 9*c0
  //   80 90 80 a0 12*c0 80 90 90 0 d1 90 80 1 8*c0 80 90 80 a0 80 0 60 80 90 1 6*c0 80 90 80 b0 80 0 70 80
  //   90 1 6*c0 80 90 80 0 50 91 1 9*c0 80 90 80 0 60 91 1 9*c0 80 90 80 0 70 91 1 9*c0 80 90 80 91 0 0 0
  //   80 8*c0 80 90 80 91 0 0 0 80 8*c0 80 90 80 91 0 0 0 80 8*c0 80 90 80 8e 12*c0 80 90 90 80 90 81 70
  //   9*c0 80 90 90 80 a0 81 70 9*c0 80 90 90 80 b0 81 70 9*c0 80 90 91 70 12*c0 80 90 91 80 90 80 81 70
  //   8*c0 80 90 91 80 0 70 10*c0 80 90 91 80 71 11*c0 80 90 91 80 80 0 10*c0 80 90 91 80 80 0 10*c0 80 90
  //   91 80 80 0 10*c0 80 90 80 b6 12*c0 80 90 90 80 81 e 10*c0 80 90 90 80 81 f 10*c0 80 90 80 b8 12*c0
  //   80 90 91 80 80 b0 0 9*c0 80 90 91 80 80 80 b0 0 8*c0 80 90 91 80 80 80 b0 0 8*c0 80 90 91 80 80 80
  //   b0 0 8*c0 80 90 91 80 80 b0 0 a6 96 7*c0 80 90 91 80 80 90 81 71 8*c0 80 90 b0 80 90 80 0 f0 1 80 0
  //   0 8e c0 c0 c0 80 90 b0 80 90 80 0 f0 1 80 0 0 80 0 8e c0 80 90 80 91 0 0 0 8e 8*c0 80 90 80 91 0 0 0
  //   80 80 8e 6*c0 80 90 80 91 4*1 0 0 0 8e 4*c0 80 90 80 81 80 0 f0 81 1 8f 6*c0 80 90 14*c0 80 90 14*c0
  //   80 90 14*c0 80 90 14*c0 80 90 14*c0 80 90 14*c0 80 90 14*c0 80 90 14*c0 80 90 14*c0 80 90 14*c0 80
  //   90 14*c0 80 90 14*c0 80 90 14*c0 80 90 14*c0 80 90 14*c0 80 90 14*c0 80 90 14*c0 80 90 14*c0 80 90
  //   14*c0 80 90 14*c0 80 90 14*c0 80 90 14*c0 80 90 14*c0 80 90 14*c0 80 90 14*c0 80 90 14*c0 80 90
  //   14*c0 80 90 14*c0 80 90 14*c0 80 90 14*c0 80 90 14*c0 80 90 14*c0 80 90 14*c0 80 90 14*c0 80 90
  //   14*c0 80 90 14*c0 80 90 14*c0 80 90 14*c0 80 90 14*c0 80 90 14*c0 80 90 14*c0 80 90 14*c0 80 90
  //   14*c0 80 90 14*c0 80 90 14*c0 80 90 14*c0 80 90 14*c0 80 90 14*c0 80 90 14*c0 80 90 14*c0 80 90
  //   14*c0 80 90 14*c0 80 90 14*c0 80 90 14*c0 80 90 14*c0 80 90 14*c0 80 90 14*c0 80 90 14*c0 80 90
  //   14*c0 80 90 14*c0 80 90 14*c0 80 90 14*c0 80 90 14*c0 80 90 14*c0 80 90 14*c0 80 90 14*c0 80 90
  //   14*c0 80 90 14*c0 80 90 14*c0 80 90 14*c0 80 90 14*c0 80 90 14*c0 80 90 14*c0 80 90 14*c0 80 90
  //   14*c0 80 90 14*c0 80 90 14*c0 80 90 14*c0 80 90 14*c0 80 90 14*c0 80 90 14*c0 80 90 14*c0 80 90
  //   14*c0 80 90 14*c0 80 90 14*c0 80 90 14*c0 80 90 14*c0 80 90 14*c0 80 90 14*c0 80 90 14*c0 80 90
  //   14*c0 80 90 14*c0 80 90 14*c0 80 90 14*c0 80 90 14*c0 80 90 14*c0 80 90 14*c0 80 90 14*c0 80 90
  //   14*c0 80 90 14*c0 80 90 14*c0 80 90 14*c0 80 90 14*c0 80 90 14*c0 80 90 14*c0 80 90 14*c0 80 90
  //   14*c0 80 90 14*c0 80 90 14*c0 80 90 14*c0 80 90 14*c0 80 90 14*c0 80 90 14*c0 80 90 14*c0 80 90
  //   14*c0 80 90 14*c0 80 90 14*c0 80 90 14*c0 80 90 14*c0 80 90 14*c0 80 90 14*c0 80 90 14*c0 80 90
  //   14*c0 80 90 14*c0 80 90 14*c0 80 90 14*c0 80 90 14*c0 80 90 14*c0 80 90 14*c0 80 90 14*c0 80 90
  //   14*c0 80 90 14*c0 80 90 14*c0 80 90 14*c0 80 90 14*c0 80 90 14*c0 80 90 14*c0 80 90 14*c0 80 90
  //   14*c0 80 90 14*c0 80 90 14*c0 80 90 14*c0 80 90 14*c0 80 90 14*c0 80 90 14*c0 80 90 14*c0 80 90
  //   14*c0 80 90 14*c0 80 90 14*c0 80 90 14*c0 80 90 14*c0 80 90 14*c0 80 90 14*c0 80 90 14*c0 80 90
  //   14*c0 80 90 14*c0 80 90 14*c0 80 90 14*c0 80 90 14*c0 80 90 14*c0 80 90 14*c0 80 90 14*c0 80 90
  //   14*c0 80 90 14*c0 80 90 14*c0 80 90 14*c0 80 90 14*c0 80 90 14*c0 80 90 14*c0 80 90 14*c0 80 90
  //   14*c0 80 90 14*c0 80 90 14*c0 80 90 14*c0 80 90 14*c0 80 90 14*c0 80 90 14*c0 80 90 14*c0 80 90
  //   14*c0 80 90 14*c0 80 90 14*c0 80 90 14*c0 80 90 14*c0 80 90 14*c0
  //   When done, may not need extra T cycle
  //   may not need MO16H, MO8H
  //   MI = write to memory
  //   MO = output from meory
endmodule

module ALU (
  input  XI,
  input  ALT,
  input  YI,
  input  CLK,
  input  NO,
  input  F,
  input  EX,
  input  NX,
  input  EY,
  input  NY,
  input  EO,
  input  [31:0] X_IN,
  input  [31:0] Y_IN,
  output Z,
  output LT,
  output [31:0] ALU_OUT
);

  wire ALT_t, c1_out, c2_out, c3_out, E16, LT_ALT, LT_STD, n74377_17_pin7, n74377_18_pin7, nor_1_out,
       nor_2_out, NZ1, NZ2, NZ3, NZ4, or_5_out, or_6_out, or_7_out, or_8_out, or_9_out, or_11_out, or_12_out,
       or_13_out, or_14_out, or_15_out, or_16_out, or_17_out, or_18_out, or_20_out, or_21_out, or_22_out,
       or_23_out, or_24_out, or_25_out, or_26_out, or_27_out, or_28_out, or_29_out, or_30_out, or_31_out,
       or_34_out, XI_ALT, XI_STD, YI_ALT, YI_STD, Z_ALT, Z_new, Z_STD;
  wire [6:0] alu_adder_4_out_10;
  wire [7:0] alu_adder_1_out_10, alu_adder_2_out_10, alu_adder_3_out_10, n74244_1_pin18, n74244_3_pin18,
       n74244_5_pin18, n74244_7_pin18, n74244_9_pin18, n74244_11_pin18, n74244_13_pin18, n74244_15_pin18,
       n74377_1_pin2, n74377_2_pin2, n74377_3_pin2, n74377_4_pin2, n74377_5_pin2, n74377_6_pin2,
       n74377_7_pin2, n74377_8_pin2, n74377_9_pin2, n74377_10_pin2, n74377_11_pin2, n74377_12_pin2,
       n74377_13_pin2, n74377_14_pin2, n74377_15_pin2, n74377_16_pin2;

  not not_1 (ALT_t, ALT);
  or or_1 (XI_STD, ALT, XI);
  or or_2 (XI_ALT, XI, ALT_t);
  or or_3 (YI_ALT, ALT_t, YI);
  or or_4 (YI_STD, YI, ALT);
  _74377 u_74377_1 (
    .pin1(XI_STD), .pin2(n74377_1_pin2[0]), .pin3(X_IN[0]), .pin4(X_IN[1]), .pin5(n74377_1_pin2[1]),
    .pin6(n74377_1_pin2[2]), .pin7(X_IN[2]), .pin8(X_IN[3]), .pin9(n74377_1_pin2[3]),
    .pin19(n74377_1_pin2[7]), .pin18(X_IN[7]), .pin17(X_IN[6]), .pin16(n74377_1_pin2[6]),
    .pin15(n74377_1_pin2[5]), .pin14(X_IN[5]), .pin13(X_IN[4]), .pin12(n74377_1_pin2[4]), .pin11(CLK));
  _74377 u_74377_2 (
    .pin1(XI_ALT), .pin2(n74377_2_pin2[0]), .pin3(X_IN[0]), .pin4(X_IN[1]), .pin5(n74377_2_pin2[1]),
    .pin6(n74377_2_pin2[2]), .pin7(X_IN[2]), .pin8(X_IN[3]), .pin9(n74377_2_pin2[3]),
    .pin19(n74377_2_pin2[7]), .pin18(X_IN[7]), .pin17(X_IN[6]), .pin16(n74377_2_pin2[6]),
    .pin15(n74377_2_pin2[5]), .pin14(X_IN[5]), .pin13(X_IN[4]), .pin12(n74377_2_pin2[4]), .pin11(CLK));
  _74377 u_74377_3 (
    .pin1(XI_STD), .pin2(n74377_3_pin2[0]), .pin3(X_IN[8]), .pin4(X_IN[9]), .pin5(n74377_3_pin2[1]),
    .pin6(n74377_3_pin2[2]), .pin7(X_IN[10]), .pin8(X_IN[11]), .pin9(n74377_3_pin2[3]),
    .pin19(n74377_3_pin2[7]), .pin18(X_IN[15]), .pin17(X_IN[14]), .pin16(n74377_3_pin2[6]),
    .pin15(n74377_3_pin2[5]), .pin14(X_IN[13]), .pin13(X_IN[12]), .pin12(n74377_3_pin2[4]), .pin11(CLK));
  _74377 u_74377_4 (
    .pin1(XI_ALT), .pin2(n74377_4_pin2[0]), .pin3(X_IN[8]), .pin4(X_IN[9]), .pin5(n74377_4_pin2[1]),
    .pin6(n74377_4_pin2[2]), .pin7(X_IN[10]), .pin8(X_IN[11]), .pin9(n74377_4_pin2[3]),
    .pin19(n74377_4_pin2[7]), .pin18(X_IN[15]), .pin17(X_IN[14]), .pin16(n74377_4_pin2[6]),
    .pin15(n74377_4_pin2[5]), .pin14(X_IN[13]), .pin13(X_IN[12]), .pin12(n74377_4_pin2[4]), .pin11(CLK));
  _74377 u_74377_5 (
    .pin1(XI_STD), .pin2(n74377_5_pin2[0]), .pin3(X_IN[16]), .pin4(X_IN[17]), .pin5(n74377_5_pin2[1]),
    .pin6(n74377_5_pin2[2]), .pin7(X_IN[18]), .pin8(X_IN[19]), .pin9(n74377_5_pin2[3]),
    .pin19(n74377_5_pin2[7]), .pin18(X_IN[23]), .pin17(X_IN[22]), .pin16(n74377_5_pin2[6]),
    .pin15(n74377_5_pin2[5]), .pin14(X_IN[21]), .pin13(X_IN[20]), .pin12(n74377_5_pin2[4]), .pin11(CLK));
  _74377 u_74377_6 (
    .pin1(XI_ALT), .pin2(n74377_6_pin2[0]), .pin3(X_IN[16]), .pin4(X_IN[17]), .pin5(n74377_6_pin2[1]),
    .pin6(n74377_6_pin2[2]), .pin7(X_IN[18]), .pin8(X_IN[19]), .pin9(n74377_6_pin2[3]),
    .pin19(n74377_6_pin2[7]), .pin18(X_IN[23]), .pin17(X_IN[22]), .pin16(n74377_6_pin2[6]),
    .pin15(n74377_6_pin2[5]), .pin14(X_IN[21]), .pin13(X_IN[20]), .pin12(n74377_6_pin2[4]), .pin11(CLK));
  _74377 u_74377_7 (
    .pin1(XI_STD), .pin2(n74377_7_pin2[0]), .pin3(X_IN[24]), .pin4(X_IN[25]), .pin5(n74377_7_pin2[1]),
    .pin6(n74377_7_pin2[2]), .pin7(X_IN[26]), .pin8(X_IN[27]), .pin9(n74377_7_pin2[3]),
    .pin19(n74377_7_pin2[7]), .pin18(X_IN[31]), .pin17(X_IN[30]), .pin16(n74377_7_pin2[6]),
    .pin15(n74377_7_pin2[5]), .pin14(X_IN[29]), .pin13(X_IN[28]), .pin12(n74377_7_pin2[4]), .pin11(CLK));
  _74377 u_74377_8 (
    .pin1(XI_ALT), .pin2(n74377_8_pin2[0]), .pin3(X_IN[24]), .pin4(X_IN[25]), .pin5(n74377_8_pin2[1]),
    .pin6(n74377_8_pin2[2]), .pin7(X_IN[26]), .pin8(X_IN[27]), .pin9(n74377_8_pin2[3]),
    .pin19(n74377_8_pin2[7]), .pin18(X_IN[31]), .pin17(X_IN[30]), .pin16(n74377_8_pin2[6]),
    .pin15(n74377_8_pin2[5]), .pin14(X_IN[29]), .pin13(X_IN[28]), .pin12(n74377_8_pin2[4]), .pin11(CLK));
  _74377 u_74377_9 (
    .pin1(YI_STD), .pin2(n74377_9_pin2[0]), .pin3(Y_IN[0]), .pin4(Y_IN[1]), .pin5(n74377_9_pin2[1]),
    .pin6(n74377_9_pin2[2]), .pin7(Y_IN[2]), .pin8(Y_IN[3]), .pin9(n74377_9_pin2[3]),
    .pin19(n74377_9_pin2[7]), .pin18(Y_IN[7]), .pin17(Y_IN[6]), .pin16(n74377_9_pin2[6]),
    .pin15(n74377_9_pin2[5]), .pin14(Y_IN[5]), .pin13(Y_IN[4]), .pin12(n74377_9_pin2[4]), .pin11(CLK));
  _74377 u_74377_10 (
    .pin1(YI_ALT), .pin2(n74377_10_pin2[0]), .pin3(Y_IN[0]), .pin4(Y_IN[1]), .pin5(n74377_10_pin2[1]),
    .pin6(n74377_10_pin2[2]), .pin7(Y_IN[2]), .pin8(Y_IN[3]), .pin9(n74377_10_pin2[3]),
    .pin19(n74377_10_pin2[7]), .pin18(Y_IN[7]), .pin17(Y_IN[6]), .pin16(n74377_10_pin2[6]),
    .pin15(n74377_10_pin2[5]), .pin14(Y_IN[5]), .pin13(Y_IN[4]), .pin12(n74377_10_pin2[4]), .pin11(CLK));
  _74377 u_74377_11 (
    .pin1(YI_STD), .pin2(n74377_11_pin2[0]), .pin3(Y_IN[8]), .pin4(Y_IN[9]), .pin5(n74377_11_pin2[1]),
    .pin6(n74377_11_pin2[2]), .pin7(Y_IN[10]), .pin8(Y_IN[11]), .pin9(n74377_11_pin2[3]),
    .pin19(n74377_11_pin2[7]), .pin18(Y_IN[15]), .pin17(Y_IN[14]), .pin16(n74377_11_pin2[6]),
    .pin15(n74377_11_pin2[5]), .pin14(Y_IN[13]), .pin13(Y_IN[12]), .pin12(n74377_11_pin2[4]), .pin11(CLK));
  _74377 u_74377_12 (
    .pin1(YI_ALT), .pin2(n74377_12_pin2[0]), .pin3(Y_IN[8]), .pin4(Y_IN[9]), .pin5(n74377_12_pin2[1]),
    .pin6(n74377_12_pin2[2]), .pin7(Y_IN[10]), .pin8(Y_IN[11]), .pin9(n74377_12_pin2[3]),
    .pin19(n74377_12_pin2[7]), .pin18(Y_IN[15]), .pin17(Y_IN[14]), .pin16(n74377_12_pin2[6]),
    .pin15(n74377_12_pin2[5]), .pin14(Y_IN[13]), .pin13(Y_IN[12]), .pin12(n74377_12_pin2[4]), .pin11(CLK));
  _74377 u_74377_13 (
    .pin1(YI_STD), .pin2(n74377_13_pin2[0]), .pin3(Y_IN[16]), .pin4(Y_IN[17]), .pin5(n74377_13_pin2[1]),
    .pin6(n74377_13_pin2[2]), .pin7(Y_IN[18]), .pin8(Y_IN[19]), .pin9(n74377_13_pin2[3]),
    .pin19(n74377_13_pin2[7]), .pin18(Y_IN[23]), .pin17(Y_IN[22]), .pin16(n74377_13_pin2[6]),
    .pin15(n74377_13_pin2[5]), .pin14(Y_IN[21]), .pin13(Y_IN[20]), .pin12(n74377_13_pin2[4]), .pin11(CLK));
  _74377 u_74377_14 (
    .pin1(YI_ALT), .pin2(n74377_14_pin2[0]), .pin3(Y_IN[16]), .pin4(Y_IN[17]), .pin5(n74377_14_pin2[1]),
    .pin6(n74377_14_pin2[2]), .pin7(Y_IN[18]), .pin8(Y_IN[19]), .pin9(n74377_14_pin2[3]),
    .pin19(n74377_14_pin2[7]), .pin18(Y_IN[23]), .pin17(Y_IN[22]), .pin16(n74377_14_pin2[6]),
    .pin15(n74377_14_pin2[5]), .pin14(Y_IN[21]), .pin13(Y_IN[20]), .pin12(n74377_14_pin2[4]), .pin11(CLK));
  _74377 u_74377_15 (
    .pin1(YI_STD), .pin2(n74377_15_pin2[0]), .pin3(Y_IN[24]), .pin4(Y_IN[25]), .pin5(n74377_15_pin2[1]),
    .pin6(n74377_15_pin2[2]), .pin7(Y_IN[26]), .pin8(Y_IN[27]), .pin9(n74377_15_pin2[3]),
    .pin19(n74377_15_pin2[7]), .pin18(Y_IN[31]), .pin17(Y_IN[30]), .pin16(n74377_15_pin2[6]),
    .pin15(n74377_15_pin2[5]), .pin14(Y_IN[29]), .pin13(Y_IN[28]), .pin12(n74377_15_pin2[4]), .pin11(CLK));
  _74377 u_74377_16 (
    .pin1(YI_ALT), .pin2(n74377_16_pin2[0]), .pin3(Y_IN[24]), .pin4(Y_IN[25]), .pin5(n74377_16_pin2[1]),
    .pin6(n74377_16_pin2[2]), .pin7(Y_IN[26]), .pin8(Y_IN[27]), .pin9(n74377_16_pin2[3]),
    .pin19(n74377_16_pin2[7]), .pin18(Y_IN[31]), .pin17(Y_IN[30]), .pin16(n74377_16_pin2[6]),
    .pin15(n74377_16_pin2[5]), .pin14(Y_IN[29]), .pin13(Y_IN[28]), .pin12(n74377_16_pin2[4]), .pin11(CLK));
  _74244 u_74244_1 (
    .pin1(ALT), .pin2(n74377_1_pin2[0]), .pin3(n74244_1_pin18[7]), .pin4(n74377_1_pin2[1]),
    .pin5(n74244_1_pin18[6]), .pin6(n74377_1_pin2[2]), .pin7(n74244_1_pin18[5]), .pin8(n74377_1_pin2[3]),
    .pin9(n74244_1_pin18[4]), .pin19(ALT), .pin18(n74244_1_pin18[0]), .pin17(n74377_1_pin2[7]),
    .pin16(n74244_1_pin18[1]), .pin15(n74377_1_pin2[6]), .pin14(n74244_1_pin18[2]), .pin13(n74377_1_pin2[5]),
    .pin12(n74244_1_pin18[3]), .pin11(n74377_1_pin2[4]));
  _74244 u_74244_2 (
    .pin1(ALT_t), .pin2(n74377_2_pin2[0]), .pin3(n74244_1_pin18[7]), .pin4(n74377_2_pin2[1]),
    .pin5(n74244_1_pin18[6]), .pin6(n74377_2_pin2[2]), .pin7(n74244_1_pin18[5]), .pin8(n74377_2_pin2[3]),
    .pin9(n74244_1_pin18[4]), .pin19(ALT_t), .pin18(n74244_1_pin18[0]), .pin17(n74377_2_pin2[7]),
    .pin16(n74244_1_pin18[1]), .pin15(n74377_2_pin2[6]), .pin14(n74244_1_pin18[2]), .pin13(n74377_2_pin2[5]),
    .pin12(n74244_1_pin18[3]), .pin11(n74377_2_pin2[4]));
  _74244 u_74244_3 (
    .pin1(ALT), .pin2(n74377_3_pin2[0]), .pin3(n74244_3_pin18[7]), .pin4(n74377_3_pin2[1]),
    .pin5(n74244_3_pin18[6]), .pin6(n74377_3_pin2[2]), .pin7(n74244_3_pin18[5]), .pin8(n74377_3_pin2[3]),
    .pin9(n74244_3_pin18[4]), .pin19(ALT), .pin18(n74244_3_pin18[0]), .pin17(n74377_3_pin2[7]),
    .pin16(n74244_3_pin18[1]), .pin15(n74377_3_pin2[6]), .pin14(n74244_3_pin18[2]), .pin13(n74377_3_pin2[5]),
    .pin12(n74244_3_pin18[3]), .pin11(n74377_3_pin2[4]));
  _74244 u_74244_4 (
    .pin1(ALT_t), .pin2(n74377_4_pin2[0]), .pin3(n74244_3_pin18[7]), .pin4(n74377_4_pin2[1]),
    .pin5(n74244_3_pin18[6]), .pin6(n74377_4_pin2[2]), .pin7(n74244_3_pin18[5]), .pin8(n74377_4_pin2[3]),
    .pin9(n74244_3_pin18[4]), .pin19(ALT_t), .pin18(n74244_3_pin18[0]), .pin17(n74377_4_pin2[7]),
    .pin16(n74244_3_pin18[1]), .pin15(n74377_4_pin2[6]), .pin14(n74244_3_pin18[2]), .pin13(n74377_4_pin2[5]),
    .pin12(n74244_3_pin18[3]), .pin11(n74377_4_pin2[4]));
  _74244 u_74244_5 (
    .pin1(ALT), .pin2(n74377_5_pin2[0]), .pin3(n74244_5_pin18[7]), .pin4(n74377_5_pin2[1]),
    .pin5(n74244_5_pin18[6]), .pin6(n74377_5_pin2[2]), .pin7(n74244_5_pin18[5]), .pin8(n74377_5_pin2[3]),
    .pin9(n74244_5_pin18[4]), .pin19(ALT), .pin18(n74244_5_pin18[0]), .pin17(n74377_5_pin2[7]),
    .pin16(n74244_5_pin18[1]), .pin15(n74377_5_pin2[6]), .pin14(n74244_5_pin18[2]), .pin13(n74377_5_pin2[5]),
    .pin12(n74244_5_pin18[3]), .pin11(n74377_5_pin2[4]));
  _74244 u_74244_6 (
    .pin1(ALT_t), .pin2(n74377_6_pin2[0]), .pin3(n74244_5_pin18[7]), .pin4(n74377_6_pin2[1]),
    .pin5(n74244_5_pin18[6]), .pin6(n74377_6_pin2[2]), .pin7(n74244_5_pin18[5]), .pin8(n74377_6_pin2[3]),
    .pin9(n74244_5_pin18[4]), .pin19(ALT_t), .pin18(n74244_5_pin18[0]), .pin17(n74377_6_pin2[7]),
    .pin16(n74244_5_pin18[1]), .pin15(n74377_6_pin2[6]), .pin14(n74244_5_pin18[2]), .pin13(n74377_6_pin2[5]),
    .pin12(n74244_5_pin18[3]), .pin11(n74377_6_pin2[4]));
  _74244 u_74244_7 (
    .pin1(ALT), .pin2(n74377_7_pin2[0]), .pin3(n74244_7_pin18[7]), .pin4(n74377_7_pin2[1]),
    .pin5(n74244_7_pin18[6]), .pin6(n74377_7_pin2[2]), .pin7(n74244_7_pin18[5]), .pin8(n74377_7_pin2[3]),
    .pin9(n74244_7_pin18[4]), .pin19(ALT), .pin18(n74244_7_pin18[0]), .pin17(n74377_7_pin2[7]),
    .pin16(n74244_7_pin18[1]), .pin15(n74377_7_pin2[6]), .pin14(n74244_7_pin18[2]), .pin13(n74377_7_pin2[5]),
    .pin12(n74244_7_pin18[3]), .pin11(n74377_7_pin2[4]));
  _74244 u_74244_8 (
    .pin1(ALT_t), .pin2(n74377_8_pin2[0]), .pin3(n74244_7_pin18[7]), .pin4(n74377_8_pin2[1]),
    .pin5(n74244_7_pin18[6]), .pin6(n74377_8_pin2[2]), .pin7(n74244_7_pin18[5]), .pin8(n74377_8_pin2[3]),
    .pin9(n74244_7_pin18[4]), .pin19(ALT_t), .pin18(n74244_7_pin18[0]), .pin17(n74377_8_pin2[7]),
    .pin16(n74244_7_pin18[1]), .pin15(n74377_8_pin2[6]), .pin14(n74244_7_pin18[2]), .pin13(n74377_8_pin2[5]),
    .pin12(n74244_7_pin18[3]), .pin11(n74377_8_pin2[4]));
  _74244 u_74244_9 (
    .pin1(ALT), .pin2(n74377_9_pin2[0]), .pin3(n74244_9_pin18[7]), .pin4(n74377_9_pin2[1]),
    .pin5(n74244_9_pin18[6]), .pin6(n74377_9_pin2[2]), .pin7(n74244_9_pin18[5]), .pin8(n74377_9_pin2[3]),
    .pin9(n74244_9_pin18[4]), .pin19(ALT), .pin18(n74244_9_pin18[0]), .pin17(n74377_9_pin2[7]),
    .pin16(n74244_9_pin18[1]), .pin15(n74377_9_pin2[6]), .pin14(n74244_9_pin18[2]), .pin13(n74377_9_pin2[5]),
    .pin12(n74244_9_pin18[3]), .pin11(n74377_9_pin2[4]));
  _74244 u_74244_10 (
    .pin1(ALT_t), .pin2(n74377_10_pin2[0]), .pin3(n74244_9_pin18[7]), .pin4(n74377_10_pin2[1]),
    .pin5(n74244_9_pin18[6]), .pin6(n74377_10_pin2[2]), .pin7(n74244_9_pin18[5]), .pin8(n74377_10_pin2[3]),
    .pin9(n74244_9_pin18[4]), .pin19(ALT_t), .pin18(n74244_9_pin18[0]), .pin17(n74377_10_pin2[7]),
    .pin16(n74244_9_pin18[1]), .pin15(n74377_10_pin2[6]), .pin14(n74244_9_pin18[2]),
    .pin13(n74377_10_pin2[5]), .pin12(n74244_9_pin18[3]), .pin11(n74377_10_pin2[4]));
  _74244 u_74244_11 (
    .pin1(ALT), .pin2(n74377_11_pin2[0]), .pin3(n74244_11_pin18[7]), .pin4(n74377_11_pin2[1]),
    .pin5(n74244_11_pin18[6]), .pin6(n74377_11_pin2[2]), .pin7(n74244_11_pin18[5]), .pin8(n74377_11_pin2[3]),
    .pin9(n74244_11_pin18[4]), .pin19(ALT), .pin18(n74244_11_pin18[0]), .pin17(n74377_11_pin2[7]),
    .pin16(n74244_11_pin18[1]), .pin15(n74377_11_pin2[6]), .pin14(n74244_11_pin18[2]),
    .pin13(n74377_11_pin2[5]), .pin12(n74244_11_pin18[3]), .pin11(n74377_11_pin2[4]));
  _74244 u_74244_12 (
    .pin1(ALT_t), .pin2(n74377_12_pin2[0]), .pin3(n74244_11_pin18[7]), .pin4(n74377_12_pin2[1]),
    .pin5(n74244_11_pin18[6]), .pin6(n74377_12_pin2[2]), .pin7(n74244_11_pin18[5]), .pin8(n74377_12_pin2[3]),
    .pin9(n74244_11_pin18[4]), .pin19(ALT_t), .pin18(n74244_11_pin18[0]), .pin17(n74377_12_pin2[7]),
    .pin16(n74244_11_pin18[1]), .pin15(n74377_12_pin2[6]), .pin14(n74244_11_pin18[2]),
    .pin13(n74377_12_pin2[5]), .pin12(n74244_11_pin18[3]), .pin11(n74377_12_pin2[4]));
  _74244 u_74244_13 (
    .pin1(ALT), .pin2(n74377_13_pin2[0]), .pin3(n74244_13_pin18[7]), .pin4(n74377_13_pin2[1]),
    .pin5(n74244_13_pin18[6]), .pin6(n74377_13_pin2[2]), .pin7(n74244_13_pin18[5]), .pin8(n74377_13_pin2[3]),
    .pin9(n74244_13_pin18[4]), .pin19(ALT), .pin18(n74244_13_pin18[0]), .pin17(n74377_13_pin2[7]),
    .pin16(n74244_13_pin18[1]), .pin15(n74377_13_pin2[6]), .pin14(n74244_13_pin18[2]),
    .pin13(n74377_13_pin2[5]), .pin12(n74244_13_pin18[3]), .pin11(n74377_13_pin2[4]));
  _74244 u_74244_14 (
    .pin1(ALT_t), .pin2(n74377_14_pin2[0]), .pin3(n74244_13_pin18[7]), .pin4(n74377_14_pin2[1]),
    .pin5(n74244_13_pin18[6]), .pin6(n74377_14_pin2[2]), .pin7(n74244_13_pin18[5]), .pin8(n74377_14_pin2[3]),
    .pin9(n74244_13_pin18[4]), .pin19(ALT_t), .pin18(n74244_13_pin18[0]), .pin17(n74377_14_pin2[7]),
    .pin16(n74244_13_pin18[1]), .pin15(n74377_14_pin2[6]), .pin14(n74244_13_pin18[2]),
    .pin13(n74377_14_pin2[5]), .pin12(n74244_13_pin18[3]), .pin11(n74377_14_pin2[4]));
  _74244 u_74244_15 (
    .pin1(ALT), .pin2(n74377_15_pin2[0]), .pin3(n74244_15_pin18[7]), .pin4(n74377_15_pin2[1]),
    .pin5(n74244_15_pin18[6]), .pin6(n74377_15_pin2[2]), .pin7(n74244_15_pin18[5]), .pin8(n74377_15_pin2[3]),
    .pin9(n74244_15_pin18[4]), .pin19(ALT), .pin18(n74244_15_pin18[0]), .pin17(n74377_15_pin2[7]),
    .pin16(n74244_15_pin18[1]), .pin15(n74377_15_pin2[6]), .pin14(n74244_15_pin18[2]),
    .pin13(n74377_15_pin2[5]), .pin12(n74244_15_pin18[3]), .pin11(n74377_15_pin2[4]));
  _74244 u_74244_16 (
    .pin1(ALT_t), .pin2(n74377_16_pin2[0]), .pin3(n74244_15_pin18[7]), .pin4(n74377_16_pin2[1]),
    .pin5(n74244_15_pin18[6]), .pin6(n74377_16_pin2[2]), .pin7(n74244_15_pin18[5]), .pin8(n74377_16_pin2[3]),
    .pin9(n74244_15_pin18[4]), .pin19(ALT_t), .pin18(n74244_15_pin18[0]), .pin17(n74377_16_pin2[7]),
    .pin16(n74244_15_pin18[1]), .pin15(n74377_16_pin2[6]), .pin14(n74244_15_pin18[2]),
    .pin13(n74377_16_pin2[5]), .pin12(n74244_15_pin18[3]), .pin11(n74377_16_pin2[4]));
  // Probe on {n74244_7_pin18, n74244_5_pin18, n74244_3_pin18, n74244_1_pin18}
  // Probe on {n74244_15_pin18, n74244_13_pin18, n74244_11_pin18, n74244_9_pin18}
  ALU_adder alu_adder_1 (
    .NO(NO), .X(n74244_1_pin18), .Y(n74244_9_pin18), .F(F), .EX(EX), .NX(NX), .carry_in(1'b0), .EY(EY),
    .NY(NY), .out_10(alu_adder_1_out_10), .carry_out(c1_out));
  // Probe on alu_adder_1_out_10
  ALU_adder alu_adder_2 (
    .NO(NO), .X(n74244_3_pin18), .Y(n74244_11_pin18), .F(F), .EX(EX), .NX(NX), .carry_in(c1_out), .EY(EY),
    .NY(NY), .out_10(alu_adder_2_out_10), .carry_out(c2_out));
  // Probe on alu_adder_2_out_10
  or or_5 (or_5_out, alu_adder_1_out_10[0], alu_adder_1_out_10[1]);
  or or_6 (or_6_out, alu_adder_1_out_10[2], alu_adder_1_out_10[3]);
  or or_7 (or_7_out, alu_adder_1_out_10[4], alu_adder_1_out_10[5]);
  or or_8 (or_8_out, alu_adder_1_out_10[6], alu_adder_1_out_10[7]);
  or or_9 (or_9_out, or_5_out, or_6_out);
  or or_10 (NZ1, or_9_out, or_11_out);
  or or_11 (or_11_out, or_7_out, or_8_out);
  or or_12 (or_12_out, alu_adder_2_out_10[0], alu_adder_2_out_10[1]);
  or or_13 (or_13_out, alu_adder_2_out_10[2], alu_adder_2_out_10[3]);
  or or_14 (or_14_out, alu_adder_2_out_10[4], alu_adder_2_out_10[5]);
  or or_15 (or_15_out, alu_adder_2_out_10[6], alu_adder_2_out_10[7]);
  ALU_adder alu_adder_3 (
    .NO(NO), .X(n74244_5_pin18), .Y(n74244_13_pin18), .F(F), .EX(EX), .NX(NX), .carry_in(c2_out), .EY(EY),
    .NY(NY), .out_10(alu_adder_3_out_10), .carry_out(c3_out));
  // Probe on alu_adder_3_out_10
  ALU_adder alu_adder_4 (
    .NO(NO), .X(n74244_7_pin18), .Y(n74244_15_pin18), .F(F), .EX(EX), .NX(NX), .carry_in(c3_out), .EY(EY),
    .NY(NY), .out_10({E16, alu_adder_4_out_10}));  // open: carry_out
  // Probe on {E16, alu_adder_4_out_10}
  or or_16 (or_16_out, or_12_out, or_13_out);
  or or_17 (or_17_out, or_14_out, or_15_out);
  or or_18 (or_18_out, ALT_t, EO);
  or or_19 (NZ2, or_16_out, or_17_out);
  or or_20 (or_20_out, alu_adder_3_out_10[0], alu_adder_3_out_10[1]);
  or or_21 (or_21_out, alu_adder_3_out_10[2], alu_adder_3_out_10[3]);
  or or_22 (or_22_out, alu_adder_3_out_10[4], alu_adder_3_out_10[5]);
  or or_23 (or_23_out, alu_adder_3_out_10[6], alu_adder_3_out_10[7]);
  or or_24 (or_24_out, alu_adder_4_out_10[0], alu_adder_4_out_10[1]);
  or or_25 (or_25_out, alu_adder_4_out_10[2], alu_adder_4_out_10[3]);
  or or_26 (or_26_out, alu_adder_4_out_10[4], alu_adder_4_out_10[5]);
  or or_27 (or_27_out, alu_adder_4_out_10[6], E16);
  or or_28 (or_28_out, or_20_out, or_21_out);
  or or_29 (or_29_out, or_22_out, or_23_out);
  nor nor_1 (nor_1_out, NZ1, NZ2);
  nor nor_2 (nor_2_out, NZ3, NZ4);
  or or_30 (or_30_out, or_24_out, or_25_out);
  or or_31 (or_31_out, or_26_out, or_27_out);
  _74377 u_74377_17 (
    .pin1(or_18_out), .pin2(Z_ALT), .pin3(Z_new), .pin4(E16), .pin5(LT_ALT), .pin7(n74377_17_pin7),
    .pin8(n74377_17_pin7), .pin18(n74377_17_pin7), .pin17(n74377_17_pin7), .pin14(n74377_17_pin7),
    .pin13(n74377_17_pin7), .pin11(CLK));  // open: pin6, pin9, pin19, pin16, pin15, pin12
  _74244 u_74244_17 (
    .pin1(EO), .pin2(alu_adder_1_out_10[0]), .pin3(ALU_OUT[7]), .pin4(alu_adder_1_out_10[1]),
    .pin5(ALU_OUT[6]), .pin6(alu_adder_1_out_10[2]), .pin7(ALU_OUT[5]), .pin8(alu_adder_1_out_10[3]),
    .pin9(ALU_OUT[4]), .pin19(EO), .pin18(ALU_OUT[0]), .pin17(alu_adder_1_out_10[7]), .pin16(ALU_OUT[1]),
    .pin15(alu_adder_1_out_10[6]), .pin14(ALU_OUT[2]), .pin13(alu_adder_1_out_10[5]), .pin12(ALU_OUT[3]),
    .pin11(alu_adder_1_out_10[4]));
  or or_32 (NZ3, or_28_out, or_29_out);
  and and_1 (Z_new, nor_1_out, nor_2_out);
  or or_33 (NZ4, or_30_out, or_31_out);
  _74244 u_74244_18 (
    .pin1(EO), .pin2(alu_adder_2_out_10[0]), .pin3(ALU_OUT[15]), .pin4(alu_adder_2_out_10[1]),
    .pin5(ALU_OUT[14]), .pin6(alu_adder_2_out_10[2]), .pin7(ALU_OUT[13]), .pin8(alu_adder_2_out_10[3]),
    .pin9(ALU_OUT[12]), .pin19(EO), .pin18(ALU_OUT[8]), .pin17(alu_adder_2_out_10[7]), .pin16(ALU_OUT[9]),
    .pin15(alu_adder_2_out_10[6]), .pin14(ALU_OUT[10]), .pin13(alu_adder_2_out_10[5]), .pin12(ALU_OUT[11]),
    .pin11(alu_adder_2_out_10[4]));
  _74244 u_74244_19 (
    .pin1(ALT_t), .pin2(Z_ALT), .pin4(LT_ALT), .pin7(Z), .pin9(LT), .pin19(ALT), .pin18(Z), .pin16(LT),
    .pin13(Z_STD), .pin11(LT_STD));  // open: pin3, pin5, pin6, pin8, pin17, pin15, pin14, pin12
  _74244 u_74244_20 (
    .pin1(EO), .pin2(alu_adder_3_out_10[0]), .pin3(ALU_OUT[23]), .pin4(alu_adder_3_out_10[1]),
    .pin5(ALU_OUT[22]), .pin6(alu_adder_3_out_10[2]), .pin7(ALU_OUT[21]), .pin8(alu_adder_3_out_10[3]),
    .pin9(ALU_OUT[20]), .pin19(EO), .pin18(ALU_OUT[16]), .pin17(alu_adder_3_out_10[7]), .pin16(ALU_OUT[17]),
    .pin15(alu_adder_3_out_10[6]), .pin14(ALU_OUT[18]), .pin13(alu_adder_3_out_10[5]), .pin12(ALU_OUT[19]),
    .pin11(alu_adder_3_out_10[4]));
  _74244 u_74244_21 (
    .pin1(EO), .pin2(alu_adder_4_out_10[0]), .pin3(ALU_OUT[31]), .pin4(alu_adder_4_out_10[1]),
    .pin5(ALU_OUT[30]), .pin6(alu_adder_4_out_10[2]), .pin7(ALU_OUT[29]), .pin8(alu_adder_4_out_10[3]),
    .pin9(ALU_OUT[28]), .pin19(EO), .pin18(ALU_OUT[24]), .pin17(E16), .pin16(ALU_OUT[25]),
    .pin15(alu_adder_4_out_10[6]), .pin14(ALU_OUT[26]), .pin13(alu_adder_4_out_10[5]), .pin12(ALU_OUT[27]),
    .pin11(alu_adder_4_out_10[4]));
  or or_34 (or_34_out, ALT, EO);
  _74377 u_74377_18 (
    .pin1(or_34_out), .pin2(Z_STD), .pin3(Z_new), .pin4(E16), .pin5(LT_STD), .pin7(n74377_18_pin7),
    .pin8(n74377_18_pin7), .pin18(n74377_18_pin7), .pin17(n74377_18_pin7), .pin14(n74377_18_pin7),
    .pin13(n74377_18_pin7), .pin11(CLK));  // open: pin6, pin9, pin19, pin16, pin15, pin12
  // also tied to GND on the sheet: {n74377_17_pin7, n74377_18_pin7}

  // Other names for the same wires on the sheet: ALU_OUT_1[7:0] = ALU_OUT[7:0]; ALU_OUT_2[7:0] = ALU_OUT[15:8];
  //   ALU_OUT_3[7:0] = ALU_OUT[23:16]; ALU_OUT_4[7:0] = ALU_OUT[31:24]; STD = ALT; X_1[7:0] = X_IN[7:0];
  //   X_2[7:0] = X_IN[15:8]; X_3[7:0] = X_IN[23:16]; X_4[7:0] = X_IN[31:24]; Y_1[7:0] = Y_IN[7:0];
  //   Y_2[7:0] = Y_IN[15:8]; Y_3[7:0] = Y_IN[23:16]; Y_4[7:0] = Y_IN[31:24]

  // Notes on the sheet:
  //   NOTE: UPDATE THIS!
endmodule

module ALU_adder (
  input  F,
  input  EX,
  input  NX,
  input  [7:0] X,
  input  carry_in,
  input  EY,
  input  NY,
  input  [7:0] Y,
  input  NO,
  output [7:0] out_10,
  output carry_out
);

  wire and_1_out, and_2_out, and_3_out, and_4_out, and_5_out, and_6_out, and_7_out, and_8_out, and_9_out,
       and_10_out, and_11_out, and_12_out, and_13_out, and_14_out, and_15_out, and_16_out, and_17_out,
       and_18_out, and_19_out, and_20_out, and_21_out, and_22_out, and_23_out, and_24_out, carry_out_low,
       n74157_1_pin4, n74157_1_pin7, n74157_1_pin9, n74157_1_pin12, n74157_2_pin4, n74157_2_pin7,
       n74157_2_pin9, n74157_2_pin12, n74283_1_pin1, n74283_1_pin4, n74283_1_pin10, n74283_1_pin13,
       n74283_2_pin1, n74283_2_pin4, n74283_2_pin10, n74283_2_pin13, xor_1_out, xor_2_out, xor_3_out,
       xor_4_out, xor_5_out, xor_6_out, xor_7_out, xor_8_out, xor_9_out, xor_10_out, xor_11_out, xor_12_out,
       xor_13_out, xor_14_out, xor_15_out, xor_16_out;

  and and_1 (and_1_out, X[0], EX);
  and and_2 (and_2_out, X[1], EX);
  and and_3 (and_3_out, X[2], EX);
  and and_4 (and_4_out, X[3], EX);
  and and_5 (and_5_out, Y[0], EY);
  and and_6 (and_6_out, Y[1], EY);
  and and_7 (and_7_out, Y[2], EY);
  and and_8 (and_8_out, Y[3], EY);
  and and_9 (and_9_out, X[4], EX);
  and and_10 (and_10_out, X[5], EX);
  and and_11 (and_11_out, X[6], EX);
  and and_12 (and_12_out, X[7], EX);
  and and_13 (and_13_out, Y[4], EY);
  and and_14 (and_14_out, Y[5], EY);
  and and_15 (and_15_out, Y[6], EY);
  and and_16 (and_16_out, Y[7], EY);
  xor xor_1 (xor_1_out, and_1_out, NX);
  xor xor_2 (xor_2_out, and_2_out, NX);
  xor xor_3 (xor_3_out, and_3_out, NX);
  xor xor_4 (xor_4_out, and_4_out, NX);
  xor xor_5 (xor_5_out, and_5_out, NY);
  xor xor_6 (xor_6_out, and_6_out, NY);
  xor xor_7 (xor_7_out, and_7_out, NY);
  xor xor_8 (xor_8_out, and_8_out, NY);
  xor xor_9 (xor_9_out, and_9_out, NX);
  xor xor_10 (xor_10_out, and_10_out, NX);
  xor xor_11 (xor_11_out, and_11_out, NX);
  xor xor_12 (xor_12_out, and_12_out, NX);
  xor xor_13 (xor_13_out, and_13_out, NY);
  xor xor_14 (xor_14_out, and_14_out, NY);
  xor xor_15 (xor_15_out, and_15_out, NY);
  xor xor_16 (xor_16_out, and_16_out, NY);
  _74283 u_74283_1 (
    .pin1(n74283_1_pin1), .pin2(xor_6_out), .pin3(xor_2_out), .pin4(n74283_1_pin4), .pin5(xor_1_out),
    .pin6(xor_5_out), .pin7(carry_in), .pin15(xor_7_out), .pin14(xor_3_out), .pin13(n74283_1_pin13),
    .pin12(xor_4_out), .pin11(xor_8_out), .pin10(n74283_1_pin10), .pin9(carry_out_low));
  _74283 u_74283_2 (
    .pin1(n74283_2_pin1), .pin2(xor_14_out), .pin3(xor_10_out), .pin4(n74283_2_pin4), .pin5(xor_9_out),
    .pin6(xor_13_out), .pin7(carry_out_low), .pin15(xor_15_out), .pin14(xor_11_out), .pin13(n74283_2_pin13),
    .pin12(xor_12_out), .pin11(xor_16_out), .pin10(n74283_2_pin10), .pin9(carry_out));
  and and_17 (and_17_out, xor_1_out, xor_5_out);
  and and_18 (and_18_out, xor_2_out, xor_6_out);
  and and_19 (and_19_out, xor_3_out, xor_7_out);
  and and_20 (and_20_out, xor_4_out, xor_8_out);
  and and_21 (and_21_out, xor_9_out, xor_13_out);
  and and_22 (and_22_out, xor_10_out, xor_14_out);
  and and_23 (and_23_out, xor_11_out, xor_15_out);
  and and_24 (and_24_out, xor_12_out, xor_16_out);
  _74157 u_74157_1 (
    .pin1(F), .pin2(and_17_out), .pin3(n74283_1_pin4), .pin4(n74157_1_pin4), .pin5(and_18_out),
    .pin6(n74283_1_pin1), .pin7(n74157_1_pin7), .pin14(and_20_out), .pin13(n74283_1_pin10),
    .pin12(n74157_1_pin12), .pin11(and_19_out), .pin10(n74283_1_pin13), .pin9(n74157_1_pin9));  // open: pin15
  _74157 u_74157_2 (
    .pin1(F), .pin2(and_21_out), .pin3(n74283_2_pin4), .pin4(n74157_2_pin4), .pin5(and_22_out),
    .pin6(n74283_2_pin1), .pin7(n74157_2_pin7), .pin14(and_24_out), .pin13(n74283_2_pin10),
    .pin12(n74157_2_pin12), .pin11(and_23_out), .pin10(n74283_2_pin13), .pin9(n74157_2_pin9));  // open: pin15
  xor xor_17 (out_10[0], n74157_1_pin4, NO);
  xor xor_18 (out_10[1], n74157_1_pin7, NO);
  xor xor_19 (out_10[2], n74157_1_pin9, NO);
  xor xor_20 (out_10[3], n74157_1_pin12, NO);
  xor xor_21 (out_10[4], n74157_2_pin4, NO);
  xor xor_22 (out_10[5], n74157_2_pin7, NO);
  xor xor_23 (out_10[6], n74157_2_pin9, NO);
  xor xor_24 (out_10[7], n74157_2_pin12, NO);
  // Probe on out_10

  // Notes on the sheet:
  //   0 = &, 1 = +
endmodule

module PC (
  input  PO,
  input  RESET,
  input  JMP,
  input  PP1,
  input  PP2,
  input  PP4,
  input  CLK,
  input  [31:0] D_IN,
  output [31:0] D_OUT
);

  wire and_1_out, CLK_t, INC, LD, n74161_1_pin15, n74161_2_pin15, n74161_3_pin15, n74161_4_pin15,
       n74161_5_pin15, n74161_6_pin15, n74161_7_pin15, n74283_1_pin9, n74283_1_pin12, n74283_2_pin9,
       n74283_3_pin9, n74283_4_pin9, n74283_5_pin9, n74283_6_pin9, n74283_7_pin9, not_1_out, not_3_out,
       or_1_out, or_2_out, or_3_out, PP;
  wire [3:0] n74283_1_pin4, n74283_2_pin4, n74283_2_pin5, n74283_3_pin4, n74283_4_pin4, n74283_5_pin4,
       n74283_6_pin4, n74283_7_pin4, n74283_8_pin4;
  wire [7:0] n74273_1_pin2, n74273_2_pin2, n74273_3_pin2, n74273_4_pin2;
  wire [15:0] n74161_1_pin14, n74161_5_pin14, n74244_1_pin18, n74244_3_pin18, n74244_13_pin18,
       n74244_15_pin18;
  wire [31:0] n74161_1_pin3;

  _74244 u_74244_1 (
    .pin1(JMP), .pin2(D_IN[0]), .pin3(n74244_1_pin18[7]), .pin4(D_IN[1]), .pin5(n74244_1_pin18[6]),
    .pin6(D_IN[2]), .pin7(n74244_1_pin18[5]), .pin8(D_IN[3]), .pin9(n74244_1_pin18[4]), .pin19(JMP),
    .pin18(n74244_1_pin18[0]), .pin17(D_IN[7]), .pin16(n74244_1_pin18[1]), .pin15(D_IN[6]),
    .pin14(n74244_1_pin18[2]), .pin13(D_IN[5]), .pin12(n74244_1_pin18[3]), .pin11(D_IN[4]));
  _74244 u_74244_2 (
    .pin1(JMP), .pin2(D_IN[8]), .pin3(n74244_1_pin18[15]), .pin4(D_IN[9]), .pin5(n74244_1_pin18[14]),
    .pin6(D_IN[10]), .pin7(n74244_1_pin18[13]), .pin8(D_IN[11]), .pin9(n74244_1_pin18[12]), .pin19(JMP),
    .pin18(n74244_1_pin18[8]), .pin17(D_IN[15]), .pin16(n74244_1_pin18[9]), .pin15(D_IN[14]),
    .pin14(n74244_1_pin18[10]), .pin13(D_IN[13]), .pin12(n74244_1_pin18[11]), .pin11(D_IN[12]));
  _74244 u_74244_3 (
    .pin1(JMP), .pin2(D_IN[16]), .pin3(n74244_3_pin18[7]), .pin4(D_IN[17]), .pin5(n74244_3_pin18[6]),
    .pin6(D_IN[18]), .pin7(n74244_3_pin18[5]), .pin8(D_IN[19]), .pin9(n74244_3_pin18[4]), .pin19(JMP),
    .pin18(n74244_3_pin18[0]), .pin17(D_IN[23]), .pin16(n74244_3_pin18[1]), .pin15(D_IN[22]),
    .pin14(n74244_3_pin18[2]), .pin13(D_IN[21]), .pin12(n74244_3_pin18[3]), .pin11(D_IN[20]));
  _74244 u_74244_4 (
    .pin1(JMP), .pin2(D_IN[24]), .pin3(n74244_3_pin18[15]), .pin4(D_IN[25]), .pin5(n74244_3_pin18[14]),
    .pin6(D_IN[26]), .pin7(n74244_3_pin18[13]), .pin8(D_IN[27]), .pin9(n74244_3_pin18[12]), .pin19(JMP),
    .pin18(n74244_3_pin18[8]), .pin17(D_IN[31]), .pin16(n74244_3_pin18[9]), .pin15(D_IN[30]),
    .pin14(n74244_3_pin18[10]), .pin13(D_IN[29]), .pin12(n74244_3_pin18[11]), .pin11(D_IN[28]));
  not not_1 (not_1_out, JMP);
  or or_1 (or_1_out, PP2, PP4);
  or or_2 (or_2_out, PP1, or_1_out);
  and and_1 (and_1_out, or_2_out, CLK);
  not not_2 (INC, and_1_out);
  or or_3 (or_3_out, not_1_out, not_3_out);
  not not_3 (not_3_out, INC);
  _74273 u_74273_1 (
    .pin1(RESET), .pin2(n74273_1_pin2[0]), .pin3(n74244_1_pin18[0]), .pin4(n74244_1_pin18[1]),
    .pin5(n74273_1_pin2[1]), .pin6(n74273_1_pin2[2]), .pin7(n74244_1_pin18[2]), .pin8(n74244_1_pin18[3]),
    .pin9(n74273_1_pin2[3]), .pin19(n74273_1_pin2[7]), .pin18(n74244_1_pin18[7]), .pin17(n74244_1_pin18[6]),
    .pin16(n74273_1_pin2[6]), .pin15(n74273_1_pin2[5]), .pin14(n74244_1_pin18[5]), .pin13(n74244_1_pin18[4]),
    .pin12(n74273_1_pin2[4]), .pin11(LD));
  _74273 u_74273_2 (
    .pin1(RESET), .pin2(n74273_2_pin2[0]), .pin3(n74244_1_pin18[8]), .pin4(n74244_1_pin18[9]),
    .pin5(n74273_2_pin2[1]), .pin6(n74273_2_pin2[2]), .pin7(n74244_1_pin18[10]), .pin8(n74244_1_pin18[11]),
    .pin9(n74273_2_pin2[3]), .pin19(n74273_2_pin2[7]), .pin18(n74244_1_pin18[15]),
    .pin17(n74244_1_pin18[14]), .pin16(n74273_2_pin2[6]), .pin15(n74273_2_pin2[5]),
    .pin14(n74244_1_pin18[13]), .pin13(n74244_1_pin18[12]), .pin12(n74273_2_pin2[4]), .pin11(LD));
  _74273 u_74273_3 (
    .pin1(RESET), .pin2(n74273_3_pin2[0]), .pin3(n74244_3_pin18[0]), .pin4(n74244_3_pin18[1]),
    .pin5(n74273_3_pin2[1]), .pin6(n74273_3_pin2[2]), .pin7(n74244_3_pin18[2]), .pin8(n74244_3_pin18[3]),
    .pin9(n74273_3_pin2[3]), .pin19(n74273_3_pin2[7]), .pin18(n74244_3_pin18[7]), .pin17(n74244_3_pin18[6]),
    .pin16(n74273_3_pin2[6]), .pin15(n74273_3_pin2[5]), .pin14(n74244_3_pin18[5]), .pin13(n74244_3_pin18[4]),
    .pin12(n74273_3_pin2[4]), .pin11(LD));
  _74273 u_74273_4 (
    .pin1(RESET), .pin2(n74273_4_pin2[0]), .pin3(n74244_3_pin18[8]), .pin4(n74244_3_pin18[9]),
    .pin5(n74273_4_pin2[1]), .pin6(n74273_4_pin2[2]), .pin7(n74244_3_pin18[10]), .pin8(n74244_3_pin18[11]),
    .pin9(n74273_4_pin2[3]), .pin19(n74273_4_pin2[7]), .pin18(n74244_3_pin18[15]),
    .pin17(n74244_3_pin18[14]), .pin16(n74273_4_pin2[6]), .pin15(n74273_4_pin2[5]),
    .pin14(n74244_3_pin18[13]), .pin13(n74244_3_pin18[12]), .pin12(n74273_4_pin2[4]), .pin11(LD));
  and and_2 (LD, or_3_out, CLK);
  _74244 u_74244_5 (
    .pin1(PO), .pin2(n74273_1_pin2[0]), .pin3(D_OUT[7]), .pin4(n74273_1_pin2[1]), .pin5(D_OUT[6]),
    .pin6(n74273_1_pin2[2]), .pin7(D_OUT[5]), .pin8(n74273_1_pin2[3]), .pin9(D_OUT[4]), .pin19(PO),
    .pin18(D_OUT[0]), .pin17(n74273_1_pin2[7]), .pin16(D_OUT[1]), .pin15(n74273_1_pin2[6]), .pin14(D_OUT[2]),
    .pin13(n74273_1_pin2[5]), .pin12(D_OUT[3]), .pin11(n74273_1_pin2[4]));
  _74244 u_74244_6 (
    .pin1(PO), .pin2(n74273_2_pin2[0]), .pin3(D_OUT[15]), .pin4(n74273_2_pin2[1]), .pin5(D_OUT[14]),
    .pin6(n74273_2_pin2[2]), .pin7(D_OUT[13]), .pin8(n74273_2_pin2[3]), .pin9(D_OUT[12]), .pin19(PO),
    .pin18(D_OUT[8]), .pin17(n74273_2_pin2[7]), .pin16(D_OUT[9]), .pin15(n74273_2_pin2[6]),
    .pin14(D_OUT[10]), .pin13(n74273_2_pin2[5]), .pin12(D_OUT[11]), .pin11(n74273_2_pin2[4]));
  _74244 u_74244_7 (
    .pin1(PO), .pin2(n74273_3_pin2[0]), .pin3(D_OUT[23]), .pin4(n74273_3_pin2[1]), .pin5(D_OUT[22]),
    .pin6(n74273_3_pin2[2]), .pin7(D_OUT[21]), .pin8(n74273_3_pin2[3]), .pin9(D_OUT[20]), .pin19(PO),
    .pin18(D_OUT[16]), .pin17(n74273_3_pin2[7]), .pin16(D_OUT[17]), .pin15(n74273_3_pin2[6]),
    .pin14(D_OUT[18]), .pin13(n74273_3_pin2[5]), .pin12(D_OUT[19]), .pin11(n74273_3_pin2[4]));
  _74244 u_74244_8 (
    .pin1(PO), .pin2(n74273_4_pin2[0]), .pin3(D_OUT[31]), .pin4(n74273_4_pin2[1]), .pin5(D_OUT[30]),
    .pin6(n74273_4_pin2[2]), .pin7(D_OUT[29]), .pin8(n74273_4_pin2[3]), .pin9(D_OUT[28]), .pin19(PO),
    .pin18(D_OUT[24]), .pin17(n74273_4_pin2[7]), .pin16(D_OUT[25]), .pin15(n74273_4_pin2[6]),
    .pin14(D_OUT[26]), .pin13(n74273_4_pin2[5]), .pin12(D_OUT[27]), .pin11(n74273_4_pin2[4]));
  _74283 #(.ShowInternalStructure("true")) u_74283_1 (
    .pin1(n74283_1_pin4[1]), .pin2(n74273_1_pin2[1]), .pin3(PP2), .pin4(n74283_1_pin4[0]), .pin5(PP1),
    .pin6(n74273_1_pin2[0]), .pin15(n74273_1_pin2[2]), .pin14(PP4), .pin13(n74283_1_pin4[2]),
    .pin12(n74283_1_pin12), .pin11(n74273_1_pin2[3]), .pin10(n74283_1_pin4[3]), .pin9(n74283_1_pin9));  // open: pin7
  _74283 #(.ShowInternalStructure("true")) u_74283_2 (
    .pin1(n74283_2_pin4[1]), .pin2(n74273_1_pin2[5]), .pin3(n74283_2_pin5[1]), .pin4(n74283_2_pin4[0]),
    .pin5(n74283_2_pin5[0]), .pin6(n74273_1_pin2[4]), .pin7(n74283_1_pin9), .pin15(n74273_1_pin2[6]),
    .pin14(n74283_2_pin5[2]), .pin13(n74283_2_pin4[2]), .pin12(n74283_2_pin5[3]), .pin11(n74273_1_pin2[7]),
    .pin10(n74283_2_pin4[3]), .pin9(n74283_2_pin9));
  _74283 #(.ShowInternalStructure("true")) u_74283_3 (
    .pin1(n74283_3_pin4[1]), .pin2(n74273_2_pin2[1]), .pin3(n74283_2_pin5[1]), .pin4(n74283_3_pin4[0]),
    .pin5(n74283_2_pin5[0]), .pin6(n74273_2_pin2[0]), .pin7(n74283_2_pin9), .pin15(n74273_2_pin2[2]),
    .pin14(n74283_2_pin5[2]), .pin13(n74283_3_pin4[2]), .pin12(n74283_2_pin5[3]), .pin11(n74273_2_pin2[3]),
    .pin10(n74283_3_pin4[3]), .pin9(n74283_3_pin9));
  _74283 #(.ShowInternalStructure("true")) u_74283_4 (
    .pin1(n74283_4_pin4[1]), .pin2(n74273_2_pin2[5]), .pin3(n74283_2_pin5[1]), .pin4(n74283_4_pin4[0]),
    .pin5(n74283_2_pin5[0]), .pin6(n74273_2_pin2[4]), .pin7(n74283_3_pin9), .pin15(n74273_2_pin2[6]),
    .pin14(n74283_2_pin5[2]), .pin13(n74283_4_pin4[2]), .pin12(n74283_2_pin5[3]), .pin11(n74273_2_pin2[7]),
    .pin10(n74283_4_pin4[3]), .pin9(n74283_4_pin9));
  _74283 #(.ShowInternalStructure("true")) u_74283_5 (
    .pin1(n74283_5_pin4[1]), .pin2(n74273_3_pin2[1]), .pin3(n74283_2_pin5[1]), .pin4(n74283_5_pin4[0]),
    .pin5(n74283_2_pin5[0]), .pin6(n74273_3_pin2[0]), .pin7(n74283_4_pin9), .pin15(n74273_3_pin2[2]),
    .pin14(n74283_2_pin5[2]), .pin13(n74283_5_pin4[2]), .pin12(n74283_2_pin5[3]), .pin11(n74273_3_pin2[3]),
    .pin10(n74283_5_pin4[3]), .pin9(n74283_5_pin9));
  _74283 #(.ShowInternalStructure("true")) u_74283_6 (
    .pin1(n74283_6_pin4[1]), .pin2(n74273_3_pin2[5]), .pin3(n74283_2_pin5[1]), .pin4(n74283_6_pin4[0]),
    .pin5(n74283_2_pin5[0]), .pin6(n74273_3_pin2[4]), .pin7(n74283_5_pin9), .pin15(n74273_3_pin2[6]),
    .pin14(n74283_2_pin5[2]), .pin13(n74283_6_pin4[2]), .pin12(n74283_2_pin5[3]), .pin11(n74273_3_pin2[7]),
    .pin10(n74283_6_pin4[3]), .pin9(n74283_6_pin9));
  _74283 #(.ShowInternalStructure("true")) u_74283_7 (
    .pin1(n74283_7_pin4[1]), .pin2(n74273_4_pin2[1]), .pin3(n74283_2_pin5[1]), .pin4(n74283_7_pin4[0]),
    .pin5(n74283_2_pin5[0]), .pin6(n74273_4_pin2[0]), .pin7(n74283_6_pin9), .pin15(n74273_4_pin2[2]),
    .pin14(n74283_2_pin5[2]), .pin13(n74283_7_pin4[2]), .pin12(n74283_2_pin5[3]), .pin11(n74273_4_pin2[3]),
    .pin10(n74283_7_pin4[3]), .pin9(n74283_7_pin9));
  _74283 #(.ShowInternalStructure("true")) u_74283_8 (
    .pin1(n74283_8_pin4[1]), .pin2(n74273_4_pin2[5]), .pin3(n74283_2_pin5[1]), .pin4(n74283_8_pin4[0]),
    .pin5(n74283_2_pin5[0]), .pin6(n74273_4_pin2[4]), .pin7(n74283_7_pin9), .pin15(n74273_4_pin2[6]),
    .pin14(n74283_2_pin5[2]), .pin13(n74283_8_pin4[2]), .pin12(n74283_2_pin5[3]), .pin11(n74273_4_pin2[7]),
    .pin10(n74283_8_pin4[3]));  // open: pin9
  _74244 u_74244_9 (
    .pin1(INC), .pin2(n74283_1_pin4[0]), .pin3(n74244_1_pin18[7]), .pin4(n74283_1_pin4[1]),
    .pin5(n74244_1_pin18[6]), .pin6(n74283_1_pin4[2]), .pin7(n74244_1_pin18[5]), .pin8(n74283_1_pin4[3]),
    .pin9(n74244_1_pin18[4]), .pin19(INC), .pin18(n74244_1_pin18[0]), .pin17(n74283_2_pin4[3]),
    .pin16(n74244_1_pin18[1]), .pin15(n74283_2_pin4[2]), .pin14(n74244_1_pin18[2]), .pin13(n74283_2_pin4[1]),
    .pin12(n74244_1_pin18[3]), .pin11(n74283_2_pin4[0]));
  _74244 u_74244_10 (
    .pin1(INC), .pin2(n74283_3_pin4[0]), .pin3(n74244_1_pin18[15]), .pin4(n74283_3_pin4[1]),
    .pin5(n74244_1_pin18[14]), .pin6(n74283_3_pin4[2]), .pin7(n74244_1_pin18[13]), .pin8(n74283_3_pin4[3]),
    .pin9(n74244_1_pin18[12]), .pin19(INC), .pin18(n74244_1_pin18[8]), .pin17(n74283_4_pin4[3]),
    .pin16(n74244_1_pin18[9]), .pin15(n74283_4_pin4[2]), .pin14(n74244_1_pin18[10]),
    .pin13(n74283_4_pin4[1]), .pin12(n74244_1_pin18[11]), .pin11(n74283_4_pin4[0]));
  _74244 u_74244_11 (
    .pin1(INC), .pin2(n74283_5_pin4[0]), .pin3(n74244_3_pin18[7]), .pin4(n74283_5_pin4[1]),
    .pin5(n74244_3_pin18[6]), .pin6(n74283_5_pin4[2]), .pin7(n74244_3_pin18[5]), .pin8(n74283_5_pin4[3]),
    .pin9(n74244_3_pin18[4]), .pin19(INC), .pin18(n74244_3_pin18[0]), .pin17(n74283_6_pin4[3]),
    .pin16(n74244_3_pin18[1]), .pin15(n74283_6_pin4[2]), .pin14(n74244_3_pin18[2]), .pin13(n74283_6_pin4[1]),
    .pin12(n74244_3_pin18[3]), .pin11(n74283_6_pin4[0]));
  _74244 u_74244_12 (
    .pin1(INC), .pin2(n74283_7_pin4[0]), .pin3(n74244_3_pin18[15]), .pin4(n74283_7_pin4[1]),
    .pin5(n74244_3_pin18[14]), .pin6(n74283_7_pin4[2]), .pin7(n74244_3_pin18[13]), .pin8(n74283_7_pin4[3]),
    .pin9(n74244_3_pin18[12]), .pin19(INC), .pin18(n74244_3_pin18[8]), .pin17(n74283_8_pin4[3]),
    .pin16(n74244_3_pin18[9]), .pin15(n74283_8_pin4[2]), .pin14(n74244_3_pin18[10]),
    .pin13(n74283_8_pin4[1]), .pin12(n74244_3_pin18[11]), .pin11(n74283_8_pin4[0]));
  _74161 u_74161_1 (
    .pin1(RESET), .pin2(CLK_t), .pin3(n74161_1_pin3[0]), .pin4(n74161_1_pin3[1]), .pin5(n74161_1_pin3[2]),
    .pin6(n74161_1_pin3[3]), .pin7(PP), .pin15(n74161_1_pin15), .pin14(n74161_1_pin14[0]),
    .pin13(n74161_1_pin14[1]), .pin12(n74161_1_pin14[2]), .pin11(n74161_1_pin14[3]), .pin10(PP), .pin9(JMP));
  _74161 u_74161_2 (
    .pin1(RESET), .pin2(CLK_t), .pin3(n74161_1_pin3[4]), .pin4(n74161_1_pin3[5]), .pin5(n74161_1_pin3[6]),
    .pin6(n74161_1_pin3[7]), .pin7(PP), .pin15(n74161_2_pin15), .pin14(n74161_1_pin14[4]),
    .pin13(n74161_1_pin14[5]), .pin12(n74161_1_pin14[6]), .pin11(n74161_1_pin14[7]), .pin10(n74161_1_pin15),
    .pin9(JMP));
  _74161 u_74161_3 (
    .pin1(RESET), .pin2(CLK_t), .pin3(n74161_1_pin3[8]), .pin4(n74161_1_pin3[9]), .pin5(n74161_1_pin3[10]),
    .pin6(n74161_1_pin3[11]), .pin7(PP), .pin15(n74161_3_pin15), .pin14(n74161_1_pin14[8]),
    .pin13(n74161_1_pin14[9]), .pin12(n74161_1_pin14[10]), .pin11(n74161_1_pin14[11]),
    .pin10(n74161_2_pin15), .pin9(JMP));
  _74161 u_74161_4 (
    .pin1(RESET), .pin2(CLK_t), .pin3(n74161_1_pin3[12]), .pin4(n74161_1_pin3[13]), .pin5(n74161_1_pin3[14]),
    .pin6(n74161_1_pin3[15]), .pin7(PP), .pin15(n74161_4_pin15), .pin14(n74161_1_pin14[12]),
    .pin13(n74161_1_pin14[13]), .pin12(n74161_1_pin14[14]), .pin11(n74161_1_pin14[15]),
    .pin10(n74161_3_pin15), .pin9(JMP));
  _74161 u_74161_5 (
    .pin1(RESET), .pin2(CLK_t), .pin3(n74161_1_pin3[16]), .pin4(n74161_1_pin3[17]), .pin5(n74161_1_pin3[18]),
    .pin6(n74161_1_pin3[19]), .pin7(PP), .pin15(n74161_5_pin15), .pin14(n74161_5_pin14[0]),
    .pin13(n74161_5_pin14[1]), .pin12(n74161_5_pin14[2]), .pin11(n74161_5_pin14[3]), .pin10(n74161_4_pin15),
    .pin9(JMP));
  _74161 u_74161_6 (
    .pin1(RESET), .pin2(CLK_t), .pin3(n74161_1_pin3[20]), .pin4(n74161_1_pin3[21]), .pin5(n74161_1_pin3[22]),
    .pin6(n74161_1_pin3[23]), .pin7(PP), .pin15(n74161_6_pin15), .pin14(n74161_5_pin14[4]),
    .pin13(n74161_5_pin14[5]), .pin12(n74161_5_pin14[6]), .pin11(n74161_5_pin14[7]), .pin10(n74161_5_pin15),
    .pin9(JMP));
  _74161 u_74161_7 (
    .pin1(RESET), .pin2(CLK_t), .pin3(n74161_1_pin3[24]), .pin4(n74161_1_pin3[25]), .pin5(n74161_1_pin3[26]),
    .pin6(n74161_1_pin3[27]), .pin7(PP), .pin15(n74161_7_pin15), .pin14(n74161_5_pin14[8]),
    .pin13(n74161_5_pin14[9]), .pin12(n74161_5_pin14[10]), .pin11(n74161_5_pin14[11]),
    .pin10(n74161_6_pin15), .pin9(JMP));
  _74161 u_74161_8 (
    .pin1(RESET), .pin2(CLK_t), .pin3(n74161_1_pin3[28]), .pin4(n74161_1_pin3[29]), .pin5(n74161_1_pin3[30]),
    .pin6(n74161_1_pin3[31]), .pin7(PP), .pin14(n74161_5_pin14[12]), .pin13(n74161_5_pin14[13]),
    .pin12(n74161_5_pin14[14]), .pin11(n74161_5_pin14[15]), .pin10(n74161_7_pin15), .pin9(JMP));  // open: pin15
  _74244 u_74244_13 (
    .pin1(PO), .pin2(n74161_1_pin14[0]), .pin3(n74244_13_pin18[7]), .pin4(n74161_1_pin14[1]),
    .pin5(n74244_13_pin18[6]), .pin6(n74161_1_pin14[2]), .pin7(n74244_13_pin18[5]), .pin8(n74161_1_pin14[3]),
    .pin9(n74244_13_pin18[4]), .pin19(PO), .pin18(n74244_13_pin18[0]), .pin17(n74161_1_pin14[7]),
    .pin16(n74244_13_pin18[1]), .pin15(n74161_1_pin14[6]), .pin14(n74244_13_pin18[2]),
    .pin13(n74161_1_pin14[5]), .pin12(n74244_13_pin18[3]), .pin11(n74161_1_pin14[4]));
  _74244 u_74244_14 (
    .pin1(PO), .pin2(n74161_1_pin14[8]), .pin3(n74244_13_pin18[15]), .pin4(n74161_1_pin14[9]),
    .pin5(n74244_13_pin18[14]), .pin6(n74161_1_pin14[10]), .pin7(n74244_13_pin18[13]),
    .pin8(n74161_1_pin14[11]), .pin9(n74244_13_pin18[12]), .pin19(PO), .pin18(n74244_13_pin18[8]),
    .pin17(n74161_1_pin14[15]), .pin16(n74244_13_pin18[9]), .pin15(n74161_1_pin14[14]),
    .pin14(n74244_13_pin18[10]), .pin13(n74161_1_pin14[13]), .pin12(n74244_13_pin18[11]),
    .pin11(n74161_1_pin14[12]));
  _74244 u_74244_15 (
    .pin1(PO), .pin2(n74161_5_pin14[0]), .pin3(n74244_15_pin18[7]), .pin4(n74161_5_pin14[1]),
    .pin5(n74244_15_pin18[6]), .pin6(n74161_5_pin14[2]), .pin7(n74244_15_pin18[5]), .pin8(n74161_5_pin14[3]),
    .pin9(n74244_15_pin18[4]), .pin19(PO), .pin18(n74244_15_pin18[0]), .pin17(n74161_5_pin14[7]),
    .pin16(n74244_15_pin18[1]), .pin15(n74161_5_pin14[6]), .pin14(n74244_15_pin18[2]),
    .pin13(n74161_5_pin14[5]), .pin12(n74244_15_pin18[3]), .pin11(n74161_5_pin14[4]));
  _74244 u_74244_16 (
    .pin1(PO), .pin2(n74161_5_pin14[8]), .pin3(n74244_15_pin18[15]), .pin4(n74161_5_pin14[9]),
    .pin5(n74244_15_pin18[14]), .pin6(n74161_5_pin14[10]), .pin7(n74244_15_pin18[13]),
    .pin8(n74161_5_pin14[11]), .pin9(n74244_15_pin18[12]), .pin19(PO), .pin18(n74244_15_pin18[8]),
    .pin17(n74161_5_pin14[15]), .pin16(n74244_15_pin18[9]), .pin15(n74161_5_pin14[14]),
    .pin14(n74244_15_pin18[10]), .pin13(n74161_5_pin14[13]), .pin12(n74244_15_pin18[11]),
    .pin11(n74161_5_pin14[12]));
  // also tied to GND on the sheet: {n74283_2_pin5[0], n74283_2_pin5[1], n74283_2_pin5[2], n74283_2_pin5[3], n74283_1_pin12}

  // Notes on the sheet:
  //   active high
  //   Could use a mux, but need fewer chips
  //   Put 2 sets of 244's in place into 74273, one selecting for jmp, the other selecting for inc'd
  //   Need to have the adder connected to the output of the registers (adding current PC value, not bus)
endmodule

module IR (
  input  [31:0] D_IN,
  input  IOL,
  input  IOH,
  input  II,
  input  CLK,
  output [7:0] I_OUT,
  output [31:0] D_OUT
);

  wire IOLH, n74244_2_pin2, n74244_3_pin2, n74244_4_pin2, n74244_5_pin2, n74244_6_pin2, n74244_7_pin2,
       nand_1_out;
  wire [7:0] n74244_1_pin2;

  nand nand_1 (nand_1_out, IOH, IOL);
  not not_1 (IOLH, nand_1_out);
  _74244 u_74244_1 (
    .pin1(IOLH), .pin2(n74244_1_pin2[0]), .pin3(D_OUT[7]), .pin4(n74244_1_pin2[1]), .pin5(D_OUT[6]),
    .pin6(n74244_1_pin2[2]), .pin7(D_OUT[5]), .pin8(n74244_1_pin2[3]), .pin9(D_OUT[4]), .pin19(IOLH),
    .pin18(D_OUT[0]), .pin17(n74244_1_pin2[7]), .pin16(D_OUT[1]), .pin15(n74244_1_pin2[6]), .pin14(D_OUT[2]),
    .pin13(n74244_1_pin2[5]), .pin12(D_OUT[3]), .pin11(n74244_1_pin2[4]));
  _74244 u_74244_2 (
    .pin1(IOL), .pin2(n74244_2_pin2), .pin3(D_OUT[15]), .pin4(n74244_2_pin2), .pin5(D_OUT[14]),
    .pin6(n74244_2_pin2), .pin7(D_OUT[13]), .pin8(n74244_2_pin2), .pin9(D_OUT[12]), .pin19(IOL),
    .pin18(D_OUT[8]), .pin17(n74244_2_pin2), .pin16(D_OUT[9]), .pin15(n74244_2_pin2), .pin14(D_OUT[10]),
    .pin13(n74244_2_pin2), .pin12(D_OUT[11]), .pin11(n74244_2_pin2));
  _74244 u_74244_3 (
    .pin1(IOL), .pin2(n74244_3_pin2), .pin3(D_OUT[23]), .pin4(n74244_3_pin2), .pin5(D_OUT[22]),
    .pin6(n74244_3_pin2), .pin7(D_OUT[21]), .pin8(n74244_3_pin2), .pin9(D_OUT[20]), .pin19(IOL),
    .pin18(D_OUT[16]), .pin17(n74244_3_pin2), .pin16(D_OUT[17]), .pin15(n74244_3_pin2), .pin14(D_OUT[18]),
    .pin13(n74244_3_pin2), .pin12(D_OUT[19]), .pin11(n74244_3_pin2));
  _74244 u_74244_4 (
    .pin1(IOL), .pin2(n74244_4_pin2), .pin3(D_OUT[31]), .pin4(n74244_4_pin2), .pin5(D_OUT[30]),
    .pin6(n74244_4_pin2), .pin7(D_OUT[29]), .pin8(n74244_4_pin2), .pin9(D_OUT[28]), .pin19(IOL),
    .pin18(D_OUT[24]), .pin17(n74244_4_pin2), .pin16(D_OUT[25]), .pin15(n74244_4_pin2), .pin14(D_OUT[26]),
    .pin13(n74244_4_pin2), .pin12(D_OUT[27]), .pin11(n74244_4_pin2));
  _74244 u_74244_5 (
    .pin1(IOH), .pin2(n74244_5_pin2), .pin3(D_OUT[15]), .pin4(n74244_5_pin2), .pin5(D_OUT[14]),
    .pin6(n74244_5_pin2), .pin7(D_OUT[13]), .pin8(n74244_5_pin2), .pin9(D_OUT[12]), .pin19(IOH),
    .pin18(D_OUT[8]), .pin17(n74244_5_pin2), .pin16(D_OUT[9]), .pin15(n74244_5_pin2), .pin14(D_OUT[10]),
    .pin13(n74244_5_pin2), .pin12(D_OUT[11]), .pin11(n74244_5_pin2));
  _74244 u_74244_6 (
    .pin1(IOH), .pin2(n74244_6_pin2), .pin3(D_OUT[23]), .pin4(n74244_6_pin2), .pin5(D_OUT[22]),
    .pin6(n74244_6_pin2), .pin7(D_OUT[21]), .pin8(n74244_6_pin2), .pin9(D_OUT[20]), .pin19(IOH),
    .pin18(D_OUT[16]), .pin17(n74244_6_pin2), .pin16(D_OUT[17]), .pin15(n74244_6_pin2), .pin14(D_OUT[18]),
    .pin13(n74244_6_pin2), .pin12(D_OUT[19]), .pin11(n74244_6_pin2));
  _74244 u_74244_7 (
    .pin1(IOH), .pin2(n74244_7_pin2), .pin3(D_OUT[31]), .pin4(n74244_7_pin2), .pin5(D_OUT[30]),
    .pin6(n74244_7_pin2), .pin7(D_OUT[29]), .pin8(n74244_7_pin2), .pin9(D_OUT[28]), .pin19(IOH),
    .pin18(D_OUT[24]), .pin17(n74244_7_pin2), .pin16(D_OUT[25]), .pin15(n74244_7_pin2), .pin14(D_OUT[26]),
    .pin13(n74244_7_pin2), .pin12(D_OUT[27]), .pin11(n74244_7_pin2));
  _74377 u_74377_1 (
    .pin1(II), .pin2(I_OUT[0]), .pin3(D_IN[0]), .pin4(D_IN[1]), .pin5(I_OUT[1]), .pin6(I_OUT[2]),
    .pin7(D_IN[2]), .pin8(D_IN[3]), .pin9(I_OUT[3]), .pin19(I_OUT[7]), .pin18(D_IN[7]), .pin17(D_IN[6]),
    .pin16(I_OUT[6]), .pin15(I_OUT[5]), .pin14(D_IN[5]), .pin13(D_IN[4]), .pin12(I_OUT[4]), .pin11(CLK));
  _74377 u_74377_2 (
    .pin1(II), .pin2(n74244_1_pin2[0]), .pin3(D_IN[8]), .pin4(D_IN[9]), .pin5(n74244_1_pin2[1]),
    .pin6(n74244_1_pin2[2]), .pin7(D_IN[10]), .pin8(D_IN[11]), .pin9(n74244_1_pin2[3]),
    .pin19(n74244_1_pin2[7]), .pin18(D_IN[15]), .pin17(D_IN[14]), .pin16(n74244_1_pin2[6]),
    .pin15(n74244_1_pin2[5]), .pin14(D_IN[13]), .pin13(D_IN[12]), .pin12(n74244_1_pin2[4]), .pin11(CLK));
  // also tied to GND on the sheet: {n74244_2_pin2, n74244_3_pin2, n74244_4_pin2}
  // also tied to VCC on the sheet: {n74244_5_pin2, n74244_6_pin2, n74244_7_pin2}
endmodule

module IV (
  input  CLK,
  input  IVI,
  input  VO,
  input  [31:0] D_IN,
  output [31:0] D_OUT
);

  wire [7:0] n74377_1_pin2, n74377_2_pin2, n74377_3_pin2, n74377_4_pin2;

  _74377 u_74377_1 (
    .pin1(IVI), .pin2(n74377_1_pin2[0]), .pin3(D_IN[24]), .pin4(D_IN[25]), .pin5(n74377_1_pin2[1]),
    .pin6(n74377_1_pin2[2]), .pin7(D_IN[26]), .pin8(D_IN[27]), .pin9(n74377_1_pin2[3]),
    .pin19(n74377_1_pin2[7]), .pin18(D_IN[31]), .pin17(D_IN[30]), .pin16(n74377_1_pin2[6]),
    .pin15(n74377_1_pin2[5]), .pin14(D_IN[29]), .pin13(D_IN[28]), .pin12(n74377_1_pin2[4]), .pin11(CLK));
  _74377 u_74377_2 (
    .pin1(IVI), .pin2(n74377_2_pin2[0]), .pin3(D_IN[0]), .pin4(D_IN[1]), .pin5(n74377_2_pin2[1]),
    .pin6(n74377_2_pin2[2]), .pin7(D_IN[2]), .pin8(D_IN[3]), .pin9(n74377_2_pin2[3]),
    .pin19(n74377_2_pin2[7]), .pin18(D_IN[7]), .pin17(D_IN[6]), .pin16(n74377_2_pin2[6]),
    .pin15(n74377_2_pin2[5]), .pin14(D_IN[5]), .pin13(D_IN[4]), .pin12(n74377_2_pin2[4]), .pin11(CLK));
  _74377 u_74377_3 (
    .pin1(IVI), .pin2(n74377_3_pin2[0]), .pin3(D_IN[8]), .pin4(D_IN[9]), .pin5(n74377_3_pin2[1]),
    .pin6(n74377_3_pin2[2]), .pin7(D_IN[10]), .pin8(D_IN[11]), .pin9(n74377_3_pin2[3]),
    .pin19(n74377_3_pin2[7]), .pin18(D_IN[15]), .pin17(D_IN[14]), .pin16(n74377_3_pin2[6]),
    .pin15(n74377_3_pin2[5]), .pin14(D_IN[13]), .pin13(D_IN[12]), .pin12(n74377_3_pin2[4]), .pin11(CLK));
  _74377 u_74377_4 (
    .pin1(IVI), .pin2(n74377_4_pin2[0]), .pin3(D_IN[16]), .pin4(D_IN[17]), .pin5(n74377_4_pin2[1]),
    .pin6(n74377_4_pin2[2]), .pin7(D_IN[18]), .pin8(D_IN[19]), .pin9(n74377_4_pin2[3]),
    .pin19(n74377_4_pin2[7]), .pin18(D_IN[23]), .pin17(D_IN[22]), .pin16(n74377_4_pin2[6]),
    .pin15(n74377_4_pin2[5]), .pin14(D_IN[21]), .pin13(D_IN[20]), .pin12(n74377_4_pin2[4]), .pin11(CLK));
  _74244 u_74244_1 (
    .pin1(VO), .pin2(n74377_2_pin2[0]), .pin3(D_OUT[7]), .pin4(n74377_2_pin2[1]), .pin5(D_OUT[6]),
    .pin6(n74377_2_pin2[2]), .pin7(D_OUT[5]), .pin8(n74377_2_pin2[3]), .pin9(D_OUT[4]), .pin19(VO),
    .pin18(D_OUT[0]), .pin17(n74377_2_pin2[7]), .pin16(D_OUT[1]), .pin15(n74377_2_pin2[6]), .pin14(D_OUT[2]),
    .pin13(n74377_2_pin2[5]), .pin12(D_OUT[3]), .pin11(n74377_2_pin2[4]));
  _74244 u_74244_2 (
    .pin1(VO), .pin2(n74377_3_pin2[0]), .pin3(D_OUT[15]), .pin4(n74377_3_pin2[1]), .pin5(D_OUT[14]),
    .pin6(n74377_3_pin2[2]), .pin7(D_OUT[13]), .pin8(n74377_3_pin2[3]), .pin9(D_OUT[12]), .pin19(VO),
    .pin18(D_OUT[8]), .pin17(n74377_3_pin2[7]), .pin16(D_OUT[9]), .pin15(n74377_3_pin2[6]),
    .pin14(D_OUT[10]), .pin13(n74377_3_pin2[5]), .pin12(D_OUT[11]), .pin11(n74377_3_pin2[4]));
  _74244 u_74244_3 (
    .pin1(VO), .pin2(n74377_4_pin2[0]), .pin3(D_OUT[23]), .pin4(n74377_4_pin2[1]), .pin5(D_OUT[22]),
    .pin6(n74377_4_pin2[2]), .pin7(D_OUT[21]), .pin8(n74377_4_pin2[3]), .pin9(D_OUT[20]), .pin19(VO),
    .pin18(D_OUT[16]), .pin17(n74377_4_pin2[7]), .pin16(D_OUT[17]), .pin15(n74377_4_pin2[6]),
    .pin14(D_OUT[18]), .pin13(n74377_4_pin2[5]), .pin12(D_OUT[19]), .pin11(n74377_4_pin2[4]));
  _74244 u_74244_4 (
    .pin1(VO), .pin2(n74377_1_pin2[0]), .pin3(D_OUT[31]), .pin4(n74377_1_pin2[1]), .pin5(D_OUT[30]),
    .pin6(n74377_1_pin2[2]), .pin7(D_OUT[29]), .pin8(n74377_1_pin2[3]), .pin9(D_OUT[28]), .pin19(VO),
    .pin18(D_OUT[24]), .pin17(n74377_1_pin2[7]), .pin16(D_OUT[25]), .pin15(n74377_1_pin2[6]),
    .pin14(D_OUT[26]), .pin13(n74377_1_pin2[5]), .pin12(D_OUT[27]), .pin11(n74377_1_pin2[4]));
endmodule

module SP (
  input  CLK,
  input  SI,
  input  SO,
  input  [31:0] D_IN,
  output [31:0] D_OUT
);

  wire n74193_1_pin4, n74193_1_pin5, n74193_1_pin11, n74193_1_pin12, n74193_1_pin13, n74193_1_pin14,
       n74193_2_pin12, n74193_2_pin13, n74193_3_pin12, n74193_3_pin13, n74193_4_pin12, n74193_4_pin13,
       n74193_5_pin12, n74193_5_pin13, n74193_6_pin12, n74193_6_pin13, n74193_7_pin12, n74193_7_pin13;
  wire [3:0] n74193_1_pin3, n74193_2_pin3, n74193_3_pin3, n74193_4_pin3, n74193_5_pin3, n74193_6_pin3,
       n74193_7_pin3, n74193_8_pin3;
  wire [7:0] n74377_1_pin2, n74377_2_pin2, n74377_3_pin2, n74377_4_pin2;
  wire [31:0] n74193_1_pin15, register_1_q;

  _74377 u_74377_1 (
    .pin1(SI), .pin2(n74377_1_pin2[0]), .pin3(D_IN[8]), .pin4(D_IN[9]), .pin5(n74377_1_pin2[1]),
    .pin6(n74377_1_pin2[2]), .pin7(D_IN[10]), .pin8(D_IN[11]), .pin9(n74377_1_pin2[3]),
    .pin19(n74377_1_pin2[7]), .pin18(D_IN[15]), .pin17(D_IN[14]), .pin16(n74377_1_pin2[6]),
    .pin15(n74377_1_pin2[5]), .pin14(D_IN[13]), .pin13(D_IN[12]), .pin12(n74377_1_pin2[4]), .pin11(CLK));
  _74377 u_74377_2 (
    .pin1(SI), .pin2(n74377_2_pin2[0]), .pin3(D_IN[16]), .pin4(D_IN[17]), .pin5(n74377_2_pin2[1]),
    .pin6(n74377_2_pin2[2]), .pin7(D_IN[18]), .pin8(D_IN[19]), .pin9(n74377_2_pin2[3]),
    .pin19(n74377_2_pin2[7]), .pin18(D_IN[23]), .pin17(D_IN[22]), .pin16(n74377_2_pin2[6]),
    .pin15(n74377_2_pin2[5]), .pin14(D_IN[21]), .pin13(D_IN[20]), .pin12(n74377_2_pin2[4]), .pin11(CLK));
  _74377 u_74377_3 (
    .pin1(SI), .pin2(n74377_3_pin2[0]), .pin3(D_IN[24]), .pin4(D_IN[25]), .pin5(n74377_3_pin2[1]),
    .pin6(n74377_3_pin2[2]), .pin7(D_IN[26]), .pin8(D_IN[27]), .pin9(n74377_3_pin2[3]),
    .pin19(n74377_3_pin2[7]), .pin18(D_IN[31]), .pin17(D_IN[30]), .pin16(n74377_3_pin2[6]),
    .pin15(n74377_3_pin2[5]), .pin14(D_IN[29]), .pin13(D_IN[28]), .pin12(n74377_3_pin2[4]), .pin11(CLK));
  _74377 u_74377_4 (
    .pin1(SI), .pin2(n74377_4_pin2[0]), .pin3(D_IN[0]), .pin4(D_IN[1]), .pin5(n74377_4_pin2[1]),
    .pin6(n74377_4_pin2[2]), .pin7(D_IN[2]), .pin8(D_IN[3]), .pin9(n74377_4_pin2[3]),
    .pin19(n74377_4_pin2[7]), .pin18(D_IN[7]), .pin17(D_IN[6]), .pin16(n74377_4_pin2[6]),
    .pin15(n74377_4_pin2[5]), .pin14(D_IN[5]), .pin13(D_IN[4]), .pin12(n74377_4_pin2[4]), .pin11(CLK));
  _74244 u_74244_1 (
    .pin1(SO), .pin2(n74377_4_pin2[0]), .pin3(D_OUT[7]), .pin4(n74377_4_pin2[1]), .pin5(D_OUT[6]),
    .pin6(n74377_4_pin2[2]), .pin7(D_OUT[5]), .pin8(n74377_4_pin2[3]), .pin9(D_OUT[4]), .pin19(SO),
    .pin18(D_OUT[0]), .pin17(n74377_4_pin2[7]), .pin16(D_OUT[1]), .pin15(n74377_4_pin2[6]), .pin14(D_OUT[2]),
    .pin13(n74377_4_pin2[5]), .pin12(D_OUT[3]), .pin11(n74377_4_pin2[4]));
  _74244 u_74244_2 (
    .pin1(SO), .pin2(n74377_1_pin2[0]), .pin3(D_OUT[15]), .pin4(n74377_1_pin2[1]), .pin5(D_OUT[14]),
    .pin6(n74377_1_pin2[2]), .pin7(D_OUT[13]), .pin8(n74377_1_pin2[3]), .pin9(D_OUT[12]), .pin19(SO),
    .pin18(D_OUT[8]), .pin17(n74377_1_pin2[7]), .pin16(D_OUT[9]), .pin15(n74377_1_pin2[6]),
    .pin14(D_OUT[10]), .pin13(n74377_1_pin2[5]), .pin12(D_OUT[11]), .pin11(n74377_1_pin2[4]));
  _74244 u_74244_3 (
    .pin1(SO), .pin2(n74377_2_pin2[0]), .pin3(D_OUT[23]), .pin4(n74377_2_pin2[1]), .pin5(D_OUT[22]),
    .pin6(n74377_2_pin2[2]), .pin7(D_OUT[21]), .pin8(n74377_2_pin2[3]), .pin9(D_OUT[20]), .pin19(SO),
    .pin18(D_OUT[16]), .pin17(n74377_2_pin2[7]), .pin16(D_OUT[17]), .pin15(n74377_2_pin2[6]),
    .pin14(D_OUT[18]), .pin13(n74377_2_pin2[5]), .pin12(D_OUT[19]), .pin11(n74377_2_pin2[4]));
  _74244 u_74244_4 (
    .pin1(SO), .pin2(n74377_3_pin2[0]), .pin3(D_OUT[31]), .pin4(n74377_3_pin2[1]), .pin5(D_OUT[30]),
    .pin6(n74377_3_pin2[2]), .pin7(D_OUT[29]), .pin8(n74377_3_pin2[3]), .pin9(D_OUT[28]), .pin19(SO),
    .pin18(D_OUT[24]), .pin17(n74377_3_pin2[7]), .pin16(D_OUT[25]), .pin15(n74377_3_pin2[6]),
    .pin14(D_OUT[26]), .pin13(n74377_3_pin2[5]), .pin12(D_OUT[27]), .pin11(n74377_3_pin2[4]));
  // Probe on D_OUT
  Register #(.width(32)) register_1 (.D(D_OUT), .en(SO), .clk(SO), .Q(register_1_q));  // open: clr
  // Probe on register_1_q
  _74193 #(.ShowInternalStructure("true")) u_74193_1 (
    .pin1(n74193_1_pin15[1]), .pin2(n74193_1_pin3[1]), .pin3(n74193_1_pin3[0]), .pin4(n74193_1_pin4),
    .pin5(n74193_1_pin5), .pin6(n74193_1_pin3[2]), .pin7(n74193_1_pin3[3]), .pin15(n74193_1_pin15[0]),
    .pin14(n74193_1_pin14), .pin13(n74193_1_pin13), .pin12(n74193_1_pin12), .pin11(n74193_1_pin11),
    .pin10(n74193_1_pin15[2]), .pin9(n74193_1_pin15[3]));
  _74193 #(.ShowInternalStructure("true")) u_74193_2 (
    .pin1(n74193_1_pin15[5]), .pin2(n74193_2_pin3[1]), .pin3(n74193_2_pin3[0]), .pin4(n74193_1_pin13),
    .pin5(n74193_1_pin12), .pin6(n74193_2_pin3[2]), .pin7(n74193_2_pin3[3]), .pin15(n74193_1_pin15[4]),
    .pin14(n74193_1_pin14), .pin13(n74193_2_pin13), .pin12(n74193_2_pin12), .pin11(n74193_1_pin11),
    .pin10(n74193_1_pin15[6]), .pin9(n74193_1_pin15[7]));
  _74193 #(.ShowInternalStructure("true")) u_74193_3 (
    .pin1(n74193_1_pin15[9]), .pin2(n74193_3_pin3[1]), .pin3(n74193_3_pin3[0]), .pin4(n74193_2_pin13),
    .pin5(n74193_2_pin12), .pin6(n74193_3_pin3[2]), .pin7(n74193_3_pin3[3]), .pin15(n74193_1_pin15[8]),
    .pin14(n74193_1_pin14), .pin13(n74193_3_pin13), .pin12(n74193_3_pin12), .pin11(n74193_1_pin11),
    .pin10(n74193_1_pin15[10]), .pin9(n74193_1_pin15[11]));
  _74193 #(.ShowInternalStructure("true")) u_74193_4 (
    .pin1(n74193_1_pin15[13]), .pin2(n74193_4_pin3[1]), .pin3(n74193_4_pin3[0]), .pin4(n74193_3_pin13),
    .pin5(n74193_3_pin12), .pin6(n74193_4_pin3[2]), .pin7(n74193_4_pin3[3]), .pin15(n74193_1_pin15[12]),
    .pin14(n74193_1_pin14), .pin13(n74193_4_pin13), .pin12(n74193_4_pin12), .pin11(n74193_1_pin11),
    .pin10(n74193_1_pin15[14]), .pin9(n74193_1_pin15[15]));
  _74193 #(.ShowInternalStructure("true")) u_74193_5 (
    .pin1(n74193_1_pin15[17]), .pin2(n74193_5_pin3[1]), .pin3(n74193_5_pin3[0]), .pin4(n74193_4_pin13),
    .pin5(n74193_4_pin12), .pin6(n74193_5_pin3[2]), .pin7(n74193_5_pin3[3]), .pin15(n74193_1_pin15[16]),
    .pin14(n74193_1_pin14), .pin13(n74193_5_pin13), .pin12(n74193_5_pin12), .pin11(n74193_1_pin11),
    .pin10(n74193_1_pin15[18]), .pin9(n74193_1_pin15[19]));
  _74193 #(.ShowInternalStructure("true")) u_74193_6 (
    .pin1(n74193_1_pin15[21]), .pin2(n74193_6_pin3[1]), .pin3(n74193_6_pin3[0]), .pin4(n74193_5_pin13),
    .pin5(n74193_5_pin12), .pin6(n74193_6_pin3[2]), .pin7(n74193_6_pin3[3]), .pin15(n74193_1_pin15[20]),
    .pin14(n74193_1_pin14), .pin13(n74193_6_pin13), .pin12(n74193_6_pin12), .pin11(n74193_1_pin11),
    .pin10(n74193_1_pin15[22]), .pin9(n74193_1_pin15[23]));
  _74193 #(.ShowInternalStructure("true")) u_74193_7 (
    .pin1(n74193_1_pin15[25]), .pin2(n74193_7_pin3[1]), .pin3(n74193_7_pin3[0]), .pin4(n74193_6_pin13),
    .pin5(n74193_6_pin12), .pin6(n74193_7_pin3[2]), .pin7(n74193_7_pin3[3]), .pin15(n74193_1_pin15[24]),
    .pin14(n74193_1_pin14), .pin13(n74193_7_pin13), .pin12(n74193_7_pin12), .pin11(n74193_1_pin11),
    .pin10(n74193_1_pin15[26]), .pin9(n74193_1_pin15[27]));
  _74193 #(.ShowInternalStructure("true")) u_74193_8 (
    .pin1(n74193_1_pin15[29]), .pin2(n74193_8_pin3[1]), .pin3(n74193_8_pin3[0]), .pin4(n74193_7_pin13),
    .pin5(n74193_7_pin12), .pin6(n74193_8_pin3[2]), .pin7(n74193_8_pin3[3]), .pin15(n74193_1_pin15[28]),
    .pin14(n74193_1_pin14), .pin11(n74193_1_pin11), .pin10(n74193_1_pin15[30]), .pin9(n74193_1_pin15[31]));  // open: pin13, pin12
endmodule

module microcode_load (
);

  wire and_1_out, clock_1_out, clock_2_out, controlled_buffer_1_out, controlled_buffer_2_out,
       counter_1_carry, counter_2_carry, not_1_out;
  wire [7:0] counter_1_q, counter_2_q, rom_1_data;
  wire [10:0] controlled_buffer_3_out;

  Clock #(.highDuration(2), .lowDuration(2)) clock_1 (.out(clock_1_out));
  assign controlled_buffer_1_out = not_1_out ? clock_1_out : 1'bz;  // Controlled_Buffer controlled_buffer_1
  Clock clock_2 (.out(clock_2_out));
  assign controlled_buffer_2_out = counter_2_q[3] ? clock_2_out : 1'bz;  // Controlled_Buffer controlled_buffer_2
  Counter counter_1 (
    .up(1'b1), .count(controlled_buffer_1_out), .clk(controlled_buffer_1_out), .carry(counter_1_carry),
    .Q(counter_1_q));  // open: clr, load, D
  Counter counter_2 (
    .clr(counter_2_carry), .up(1'b1), .count(counter_1_carry), .clk(controlled_buffer_1_out),
    .carry(counter_2_carry), .Q(counter_2_q));  // open: load, D
  assign controlled_buffer_3_out = not_1_out ? {counter_2_q[2:0], counter_1_q} : 11'bz;  // Controlled_Buffer controlled_buffer_3
  not not_1 (not_1_out, counter_2_q[3]);
  ROM #(.addrWidth(11)) rom_1 (.addr(controlled_buffer_3_out), .data(rom_1_data));
  and and_1 (and_1_out, controlled_buffer_1_out, controlled_buffer_1_out);
  RAM #(.addrWidth(11), .databus("bidir"), .enables("line")) ram_1 (
    .addr(controlled_buffer_3_out), .we(and_1_out), .oe(1'b0), .clk(and_1_out), .data(rom_1_data));

  // Notes on the sheet:
  //   contents of rom_1 (hex, n*v repeats v):
  //   1 2 3 4 5 66 7 8 9 10 11 12 13 14 15 16 17 15*0 18 15*0 19 15*0 20 15*0 21 15*0 22 15*0 23 15*0 24
  //   15*0 25 15*0 26 15*0 27 15*0 28 15*0 29 15*0 30 15*0 31 15*0 32 15*0 33 15*0 34 15*0 36 15*0 37 15*0
  //   38 15*0 39 15*0 40
endmodule
module scratch (
  input  [31:0] in_1,
  input  WR,
  input  RD,
  input  [31:0] in_4,
  input  SELL0,
  input  SELL1,
  input  [31:0] in_7,
  input  [31:0] in_8,
  input  [23:0] in_9,
  input  [15:0] in_10,
  input  in_11,
  input  in_12,
  input  in_13,
  input  [7:0] in_14,
  input  in_15,
  input  in_16
);

  wire AI, and_1_out, and_2_out, and_3_out, and_4_out, and_5_out, and_6_out, and_7_out, and_8_out, and_9_out,
       and_10_out, and_11_out, and_12_out, and_14_out, and_15_out, and_17_out, and_18_out, and_19_out,
       and_20_out, and_21_out, and_22_out, and_23_out, and_24_out, and_25_out, and_26_out, and_27_out,
       and_28_out, and_30_out, and_31_out, and_33_out, and_34_out, and_35_out, and_36_out, and_37_out,
       and_38_out, and_39_out, and_40_out, and_41_out, and_42_out, and_43_out, and_44_out, and_45_out,
       and_46_out, and_47_out, and_50_out, and_51_out, and_52_out, and_53_out, and_54_out, and_55_out,
       and_56_out, and_57_out, and_58_out, and_59_out, and_60_out, and_61_out, and_62_out, and_63_out,
       and_64_out, and_65_out, and_66_out, and_67_out, and_68_out, and_69_out, and_72_out, and_73_out,
       and_74_out, and_75_out, and_76_out, and_77_out, and_78_out, and_79_out, and_80_out, and_81_out,
       and_82_out, and_83_out, and_84_out, and_85_out, and_86_out, B, B0_0, B0_0W, B0_1, B0_1W, B0_2, B0_2W,
       B0_3, B0_3W, B1_0, B1_0W, B1_1, B1_1W, B1_2, B1_2W, B2_0, B2_0W, B2_1, B2_1W, B2_2, B2_2W, B3_0,
       B3_0W, B3_1, B3_1W, button_1_out, CHIP0, CHIP1, CHIP2, CHIP3, CLK, decoder_2_out0, decoder_2_out1,
       decoder_2_out2, decoder_2_out3, decoder_3_out0, decoder_3_out1, decoder_3_out2, decoder_3_out3, DI,
       DO, EO, EX, EY, F, H, IDS, IEN, II, IVI, IVO, JGT, JLT, JZ, LOAD_CLK, MEM_FAULT, MI, MI8, MI16, MI32,
       MO, MO8H, MO8L, MO16H, MO16L, MO32, n74138_1_pin4, n74138_1_pin6, n74138_1_pin7, n74138_1_pin15,
       n74138_2_pin4, n74138_3_pin4, n74138_3_pin6, n74138_3_pin15, n74138_4_pin4, n74138_4_pin7,
       n74138_4_pin9, n74138_4_pin10, n74138_4_pin11, n74138_4_pin12, n74138_4_pin13, n74138_4_pin14,
       n74138_4_pin15, n74138_5_pin4, n74138_5_pin7, n74138_5_pin9, n74138_5_pin10, n74138_5_pin11,
       n74138_5_pin12, n74138_5_pin13, n74138_5_pin14, n74138_5_pin15, n74138_6_pin4, n74138_6_pin6,
       n74138_6_pin7, n74138_6_pin9, n74138_6_pin10, n74138_6_pin11, n74138_6_pin12, n74138_6_pin13,
       n74138_6_pin14, n74138_6_pin15, nA0, nA1, nand_1_out, nand_4_out, NO, not_5_out, not_6_out, not_7_out,
       not_8_out, not_9_out, not_10_out, not_11_out, not_12_out, not_13_out, not_14_out, not_15_out,
       not_16_out, not_17_out, not_18_out, not_19_out, NX, NY, or_1_out, or_2_out, or_3_out, or_4_out,
       or_5_out, or_6_out, or_8_out, or_11_out, or_12_out, or_13_out, or_15_out, or_16_out, or_18_out,
       or_19_out, or_20_out, or_23_out, or_24_out, or_25_out, or_27_out, or_29_out, or_30_out, or_31_out,
       or_32_out, or_33_out, or_34_out, or_39_out, or_40_out, or_41_out, or_42_out, or_43_out, or_44_out,
       or_45_out, or_46_out, or_47_out, or_48_out, PO, PP1, PP2, PP4, RAM_EN, ROM_EN, RT, undriven,
       undriven_2, undriven_3, undriven_4, undriven_5, undriven_10, undriven_11, W, XI, YI;
  wire [2:0] rom_1_data;
  wire [6:0] n74138_4_pin1;
  wire [6:4] rom_2_data;
  wire [7:0] controlled_buffer_49_out, controlled_buffer_51_out, D0, D1, D2, D3, demultiplexer_2_out0,
       demultiplexer_3_out0, multiplexer_6_out, multiplexer_7_out, multiplexer_8_out, multiplexer_9_out,
       multiplexer_10_out, multiplexer_11_out, multiplexer_12_out, multiplexer_13_out, multiplexer_14_out,
       multiplexer_15_out, multiplexer_16_out, multiplexer_17_out, multiplexer_22_out, multiplexer_23_out,
       multiplexer_24_out, multiplexer_25_out, multiplexer_26_out, multiplexer_27_out, multiplexer_28_out,
       multiplexer_29_out, ram_1_data, ram_2_data, ram_3_data, ram_4_data, ram_5_data, ram_6_data,
       ram_7_data, ram_8_data, rom_3_data, rom_4_data, rom_5_data, rom_6_data, undriven_6, undriven_7,
       undriven_8, undriven_9;
  wire [18:0] multiplexer_1_out, multiplexer_2_out, multiplexer_3_out, word_addr_pp;
  wire [31:0] ADDR, BUSS;

  or or_1 (or_1_out, H, W);
  not not_1 (nA0, in_4[0]);
  // Probe on word_addr_pp
  Adder #(.width(19)) adder_1 (.a(19'h1), .b(in_4[20:2]), .out(word_addr_pp));  // open: cin, cout
  and and_1 (and_1_out, nA1, nA0);
  or or_2 (or_2_out, B, H, W);
  and and_2 (and_2_out, nA1, in_4[0], B);
  and and_3 (and_3_out, or_1_out, nA0, nA1);
  and and_4 (and_4_out, in_4[1], nA0, B);
  and and_5 (and_5_out, in_4[1], nA0, H);
  and and_6 (and_6_out, nA1, nA0, W);
  and and_7 (and_7_out, in_4[1], in_4[0], B);
  and and_8 (and_8_out, in_4[1], nA0, H);
  and and_9 (and_9_out, nA1, nA0, W);
  not not_2 (nA1, in_4[1]);
  and and_10 (and_10_out, and_1_out, or_2_out);
  or or_3 (or_3_out, and_2_out, and_3_out);
  or or_4 (or_4_out, and_4_out, and_5_out, and_6_out);
  or or_5 (or_5_out, and_7_out, and_8_out, and_9_out);
  not not_3 (nA1, in_4[1]);
  not not_4 (nA0, in_4[0]);
  not not_5 (not_5_out, CHIP3);
  and and_11 (and_11_out, CHIP0, not_5_out);
  and and_12 (and_12_out, not_10_out, and_11_out);
  or or_6 (or_6_out, and_12_out, B2_2);
  and and_13 (B0_0, or_6_out, 1'b0);
  or or_7 (B0_0W, and_12_out, B2_2W);
  Button button_1 (.out(button_1_out));
  Decoder #(.select(2)) decoder_1 (.out0(B), .out1(H), .out2(W), .sel({SELL1, SELL0}));  // open: out3, en
  and and_14 (and_14_out, CHIP3, CHIP0);
  and and_15 (and_15_out, not_10_out, and_14_out);
  or or_8 (or_8_out, and_15_out, B1_2);
  and and_16 (B0_1, or_8_out, 1'b0);
  or or_9 (B0_1W, and_15_out, B1_2W);
  or or_10 (MEM_FAULT, or_11_out, and_35_out);
  and and_17 (and_17_out, WR, CHIP2);
  and and_18 (and_18_out, CHIP2, RD);
  and and_19 (and_19_out, WR, CHIP1);
  and and_20 (and_20_out, CHIP1, RD);
  and and_21 (and_21_out, WR, CHIP0);
  and and_22 (and_22_out, CHIP0, RD);
  or or_11 (or_11_out, and_33_out, and_34_out);
  RAM #(.addrWidth(19), .databus("bidir")) ram_1 (
    .addr(in_1[20:2]), .we(and_23_out), .oe(and_24_out), .clk(button_1_out), .data(ram_1_data));
  and and_23 (and_23_out, WR, CHIP3);
  and and_24 (and_24_out, CHIP3, RD);
  RAM #(.addrWidth(19), .databus("bidir")) ram_2 (
    .addr(in_1[20:2]), .we(and_17_out), .oe(and_18_out), .clk(button_1_out), .data(ram_2_data));
  RAM #(.addrWidth(19), .databus("bidir")) ram_3 (
    .addr(in_1[20:2]), .we(and_19_out), .oe(and_20_out), .clk(button_1_out), .data(ram_3_data));
  RAM #(.addrWidth(19), .databus("bidir")) ram_4 (
    .addr(in_1[20:2]), .we(and_21_out), .oe(and_22_out), .clk(button_1_out), .data(ram_4_data));
  and and_25 (and_25_out, in_4[0], in_4[1]);
  not not_6 (not_6_out, CHIP0);
  and and_26 (and_26_out, CHIP1, not_6_out);
  and and_27 (and_27_out, CHIP1, CHIP2);
  or or_12 (or_12_out, and_27_out, and_26_out);
  and and_28 (and_28_out, not_10_out, or_12_out);
  or or_13 (or_13_out, and_28_out, B0_3);
  and and_29 (B1_0, or_13_out, 1'b0);
  or or_14 (B1_0W, and_28_out, B0_3W);
  or or_15 (or_15_out, in_4[1], in_4[0]);
  and and_30 (and_30_out, CHIP0, CHIP1);
  and and_31 (and_31_out, not_10_out, and_30_out);
  or or_16 (or_16_out, and_31_out, B2_2);
  and and_32 (B1_1, or_16_out, 1'b0);
  or or_17 (B1_1W, and_31_out, B2_2W);
  and and_33 (and_33_out, H, in_4[0]);
  and and_34 (and_34_out, W, or_18_out);
  and and_35 (and_35_out, SELL0, SELL1);
  Button button_2 (.out(CLK));
  or or_18 (or_18_out, in_4[0], in_4[1]);
  Multiplexer #(.width(19)) multiplexer_1 (
    .in0(in_4[20:2]), .in1(word_addr_pp), .out(multiplexer_1_out), .sel(or_15_out));
  and and_36 (and_36_out, 1'b1, CHIP0);
  and and_37 (and_37_out, CHIP0, 1'b0);
  Multiplexer #(.width(19)) multiplexer_2 (
    .in0(in_4[20:2]), .in1(word_addr_pp), .out(multiplexer_2_out), .sel(in_4[1]));
  and and_38 (and_38_out, 1'b1, CHIP1);
  and and_39 (and_39_out, CHIP1, 1'b0);
  RAM #(.addrWidth(19), .databus("bidir")) ram_5 (
    .addr(multiplexer_3_out), .we(and_40_out), .oe(and_41_out), .clk(CLK), .data(ram_5_data));
  Multiplexer #(.width(19)) multiplexer_3 (
    .in0(in_4[20:2]), .in1(word_addr_pp), .out(multiplexer_3_out), .sel(and_25_out));
  and and_40 (and_40_out, 1'b1, CHIP2);
  and and_41 (and_41_out, CHIP2, 1'b0);
  RAM #(.addrWidth(19), .databus("bidir")) ram_6 (
    .addr(in_4[20:2]), .we(and_42_out), .oe(and_43_out), .clk(CLK), .data(ram_6_data));
  and and_42 (and_42_out, 1'b1, CHIP3);
  and and_43 (and_43_out, CHIP3, 1'b0);
  not not_7 (not_7_out, CHIP1);
  and and_44 (and_44_out, CHIP2, not_7_out);
  and and_45 (and_45_out, CHIP2, CHIP1, not_8_out);
  and and_46 (and_46_out, not_10_out, and_44_out);
  and and_47 (and_47_out, not_10_out, and_45_out);
  or or_19 (or_19_out, and_46_out, B0_2);
  or or_20 (or_20_out, and_47_out, B0_3);
  and and_48 (B2_0, or_19_out, 1'b0);
  // Probe on multiplexer_1_out
  RAM #(.addrWidth(19), .databus("bidir")) ram_7 (
    .addr(multiplexer_1_out), .we(and_36_out), .oe(and_37_out), .clk(CLK), .data(ram_7_data));
  RAM #(.addrWidth(19), .databus("bidir")) ram_8 (
    .addr(multiplexer_2_out), .we(and_38_out), .oe(and_39_out), .clk(CLK), .data(ram_8_data));
  not not_8 (not_8_out, CHIP3);
  and and_49 (B2_1, or_20_out, 1'b0);
  or or_21 (B2_0W, and_46_out, B0_2W);
  or or_22 (B2_1W, and_47_out, B0_3W);
  assign D0 = and_55_out ? ram_1_data : 8'bz;  // Controlled_Buffer controlled_buffer_1
  assign ram_1_data = and_56_out ? D0 : 8'bz;  // Controlled_Buffer controlled_buffer_2
  assign D1 = and_57_out ? ram_1_data : 8'bz;  // Controlled_Buffer controlled_buffer_3
  assign ram_1_data = and_58_out ? D1 : 8'bz;  // Controlled_Buffer controlled_buffer_4
  assign D3 = and_59_out ? ram_1_data : 8'bz;  // Controlled_Buffer controlled_buffer_5
  assign ram_1_data = and_60_out ? D3 : 8'bz;  // Controlled_Buffer controlled_buffer_6
  assign D0 = and_61_out ? ram_2_data : 8'bz;  // Controlled_Buffer controlled_buffer_7
  assign ram_2_data = and_62_out ? D0 : 8'bz;  // Controlled_Buffer controlled_buffer_8
  assign ram_2_data = and_64_out ? D2 : 8'bz;  // Controlled_Buffer controlled_buffer_9
  and and_50 (and_50_out, RD, and_75_out);
  assign D0 = and_50_out ? ram_3_data : 8'bz;  // Controlled_Buffer controlled_buffer_10
  assign ram_3_data = and_51_out ? D0 : 8'bz;  // Controlled_Buffer controlled_buffer_11
  and and_51 (and_51_out, and_75_out, WR);
  assign D1 = and_65_out ? ram_3_data : 8'bz;  // Controlled_Buffer controlled_buffer_12
  assign ram_3_data = and_66_out ? D1 : 8'bz;  // Controlled_Buffer controlled_buffer_13
  and and_52 (and_52_out, CHIP0, RD);
  assign D0 = and_52_out ? ram_4_data : 8'bz;  // Controlled_Buffer controlled_buffer_14
  assign ram_4_data = and_53_out ? D0 : 8'bz;  // Controlled_Buffer controlled_buffer_15
  and and_53 (and_53_out, CHIP0, WR);
  and and_54 (and_54_out, not_10_out, and_67_out);
  and and_55 (and_55_out, RD, and_72_out);
  and and_56 (and_56_out, and_72_out, WR);
  and and_57 (and_57_out, RD, and_73_out);
  and and_58 (and_58_out, and_73_out, WR);
  and and_59 (and_59_out, RD, W);
  and and_60 (and_60_out, W, WR);
  and and_61 (and_61_out, RD, and_74_out);
  and and_62 (and_62_out, and_74_out, WR);
  and and_63 (and_63_out, RD, W);
  assign D2 = and_63_out ? ram_2_data : 8'bz;  // Controlled_Buffer controlled_buffer_16
  and and_64 (and_64_out, W, WR);
  and and_65 (and_65_out, RD, and_76_out);
  and and_66 (and_66_out, and_76_out, WR);
  not not_9 (not_9_out, CHIP2);
  and and_67 (and_67_out, CHIP3, not_9_out);
  and and_68 (and_68_out, CHIP3, CHIP2);
  and and_69 (and_69_out, not_10_out, and_68_out);
  or or_23 (or_23_out, and_54_out, B1_2);
  or or_24 (or_24_out, and_69_out, B0_2);
  and and_70 (B3_0, or_23_out, 1'b0);
  and and_71 (B3_1, or_24_out, 1'b0);
  and and_72 (and_72_out, B, CHIP3);
  and and_73 (and_73_out, H, CHIP3);
  and and_74 (and_74_out, CHIP2, or_27_out);
  and and_75 (and_75_out, B, CHIP1);
  or or_25 (or_25_out, W, H);
  and and_76 (and_76_out, or_25_out, CHIP1);
  and and_77 (and_77_out, CHIP3, CHIP2, CHIP1, CHIP0);
  not not_10 (not_10_out, and_77_out);
  or or_26 (B3_0W, and_54_out, B1_2W);
  or or_27 (or_27_out, B, H);
  or or_28 (B3_1W, and_69_out, B0_2W);
  assign in_7[7:0] = B0_0 ? ram_7_data : 8'bz;  // Controlled_Buffer controlled_buffer_17
  assign in_7[7:0] = B1_0 ? ram_8_data : 8'bz;  // Controlled_Buffer controlled_buffer_18
  assign in_7[7:0] = B2_0 ? ram_5_data : 8'bz;  // Controlled_Buffer controlled_buffer_19
  assign in_7[7:0] = B3_0 ? ram_6_data : 8'bz;  // Controlled_Buffer controlled_buffer_20
  assign in_7[15:8] = B0_1 ? ram_7_data : 8'bz;  // Controlled_Buffer controlled_buffer_21
  assign in_7[23:16] = B0_2 ? ram_7_data : 8'bz;  // Controlled_Buffer controlled_buffer_22
  assign in_7[15:8] = B1_1 ? ram_8_data : 8'bz;  // Controlled_Buffer controlled_buffer_23
  assign in_7[23:16] = B1_2 ? ram_8_data : 8'bz;  // Controlled_Buffer controlled_buffer_24
  assign in_7[31:24] = B0_2 ? ram_8_data : 8'bz;  // Controlled_Buffer controlled_buffer_25
  assign in_7[15:8] = B2_1 ? ram_5_data : 8'bz;  // Controlled_Buffer controlled_buffer_26
  assign in_7[23:16] = B2_2 ? ram_5_data : 8'bz;  // Controlled_Buffer controlled_buffer_27
  assign in_7[31:24] = B1_2 ? ram_5_data : 8'bz;  // Controlled_Buffer controlled_buffer_28
  assign in_7[15:8] = B3_1 ? ram_6_data : 8'bz;  // Controlled_Buffer controlled_buffer_29
  assign in_7[23:16] = B0_3 ? ram_6_data : 8'bz;  // Controlled_Buffer controlled_buffer_30
  Demultiplexer #(.select(3)) demultiplexer_1 (
    .out0(B2_2), .out1(B0_3), .out2(B0_2), .out3(B1_2), .out4(B2_2W), .out5(B0_3W), .out6(B0_2W),
    .out7(B1_2W), .in(1'b1), .sel({1'b1, in_4[1:0]}));
  // Probe on undriven
  assign in_7[31:24] = B0_3 ? ram_7_data : 8'bz;  // Controlled_Buffer controlled_buffer_31
  assign in_7[31:24] = B2_2 ? ram_6_data : 8'bz;  // Controlled_Buffer controlled_buffer_32
  assign ram_7_data = B0_2W ? in_7[23:16] : 8'bz;  // Controlled_Buffer controlled_buffer_33
  assign ram_7_data = B0_3W ? in_7[31:24] : 8'bz;  // Controlled_Buffer controlled_buffer_34
  assign ram_8_data = B1_2W ? in_7[23:16] : 8'bz;  // Controlled_Buffer controlled_buffer_35
  assign ram_8_data = B0_2W ? in_7[31:24] : 8'bz;  // Controlled_Buffer controlled_buffer_36
  assign ram_5_data = B2_2W ? in_7[23:16] : 8'bz;  // Controlled_Buffer controlled_buffer_37
  assign ram_5_data = B1_2W ? in_7[31:24] : 8'bz;  // Controlled_Buffer controlled_buffer_38
  assign ram_6_data = B0_3W ? in_7[23:16] : 8'bz;  // Controlled_Buffer controlled_buffer_39
  assign ram_6_data = B2_2W ? in_7[31:24] : 8'bz;  // Controlled_Buffer controlled_buffer_40
  assign ram_7_data = B0_0W ? in_7[7:0] : 8'bz;  // Controlled_Buffer controlled_buffer_41
  assign ram_7_data = B0_1W ? in_7[15:8] : 8'bz;  // Controlled_Buffer controlled_buffer_42
  assign ram_8_data = B1_0W ? in_7[7:0] : 8'bz;  // Controlled_Buffer controlled_buffer_43
  assign ram_8_data = B1_1W ? in_7[15:8] : 8'bz;  // Controlled_Buffer controlled_buffer_44
  assign ram_5_data = B2_0W ? in_7[7:0] : 8'bz;  // Controlled_Buffer controlled_buffer_45
  assign ram_5_data = B2_1W ? in_7[15:8] : 8'bz;  // Controlled_Buffer controlled_buffer_46
  assign ram_6_data = B3_0W ? in_7[7:0] : 8'bz;  // Controlled_Buffer controlled_buffer_47
  assign ram_6_data = B3_1W ? in_7[15:8] : 8'bz;  // Controlled_Buffer controlled_buffer_48
  // Probe on nothing
  assign controlled_buffer_49_out = and_78_out ? D3 : 8'bz;  // Controlled_Buffer controlled_buffer_49
  assign D3 = and_79_out ? controlled_buffer_49_out : 8'bz;  // Controlled_Buffer controlled_buffer_50
  assign controlled_buffer_51_out = and_80_out ? D2 : 8'bz;  // Controlled_Buffer controlled_buffer_51
  assign D2 = and_81_out ? controlled_buffer_51_out : 8'bz;  // Controlled_Buffer controlled_buffer_52
  // Probe on demultiplexer_2_out0
  and and_78 (and_78_out, WR, W);
  and and_79 (and_79_out, W, RD);
  and and_80 (and_80_out, WR, W);
  and and_81 (and_81_out, W, RD);
  // Probe on undriven_2
  not not_11 (not_11_out, SELL1);
  not not_12 (not_12_out, SELL0);
  not not_13 (not_13_out, SELL1);
  not not_14 (not_14_out, SELL0);
  Demultiplexer #(.disabled("Z"), .enable("true"), .tristate("true"), .width(8)) demultiplexer_2 (
    .out0(demultiplexer_2_out0), .out1(controlled_buffer_49_out), .in(D1), .sel(in_4[1]), .en(and_85_out));
  Multiplexer #(.disabled("Z"), .enable("true"), .width(8)) multiplexer_4 (
    .in0(demultiplexer_2_out0), .in1(controlled_buffer_49_out), .out(D1), .sel(in_4[1]), .en(and_86_out));
  Demultiplexer #(.disabled("Z"), .enable("true"), .select(2), .tristate("true"), .width(8)) demultiplexer_3 (
    .out0(demultiplexer_3_out0), .out1(demultiplexer_2_out0), .out2(controlled_buffer_51_out),
    .out3(controlled_buffer_49_out), .in(D0), .sel(in_4[1:0]), .en(WR));
  Multiplexer #(.disabled("Z"), .enable("true"), .select(2), .width(8)) multiplexer_5 (
    .in0(demultiplexer_3_out0), .in1(demultiplexer_2_out0), .in2(controlled_buffer_51_out),
    .in3(controlled_buffer_49_out), .out(D0), .sel(in_4[1:0]), .en(RD));
  and and_82 (and_82_out, SELL0, not_11_out);
  and and_83 (and_83_out, not_12_out, not_13_out);
  and and_84 (and_84_out, not_14_out, SELL1);
  and and_85 (and_85_out, or_29_out, WR);
  // Probe on D1
  and and_86 (and_86_out, RD, or_30_out);
  or or_29 (or_29_out, W, H);
  or or_30 (or_30_out, W, H);
  Decoder #(.select(2)) decoder_2 (
    .out0(decoder_2_out0), .out1(decoder_2_out1), .out2(decoder_2_out2), .out3(decoder_2_out3),
    .sel(in_4[1:0]), .en(and_82_out));
  Decoder #(.select(2)) decoder_3 (
    .out0(decoder_3_out0), .out1(decoder_3_out1), .out2(decoder_3_out2), .out3(decoder_3_out3),
    .sel(in_4[1:0]), .en(and_83_out));
  or or_31 (or_31_out, decoder_2_out0, decoder_2_out3);
  or or_32 (or_32_out, decoder_2_out0, decoder_2_out1);
  or or_33 (or_33_out, decoder_2_out1, decoder_2_out2);
  or or_34 (or_34_out, decoder_2_out2, decoder_2_out3);
  or or_35 (CHIP0, or_31_out, decoder_3_out0, and_84_out);
  or or_36 (CHIP1, or_32_out, decoder_3_out1, and_84_out);
  or or_37 (CHIP2, or_33_out, decoder_3_out2, and_84_out);
  or or_38 (CHIP3, or_34_out, decoder_3_out3, and_84_out);
  nand nand_1 (nand_1_out, in_15, in_16);
  ROM #(.addrWidth(11)) rom_1 (.addr({in_14, in_13, in_12, in_11}), .data({F, NY, EY, NX, EX, rom_1_data}));
  ROM #(.addrWidth(11)) rom_2 (.addr({in_14, in_13, in_12, in_11}), .data({EO, rom_2_data, JZ, JGT, JLT, NO}));
  Multiplexer #(.disabled("Z"), .enable("true"), .width(8)) multiplexer_6 (
    .in0(multiplexer_7_out), .in1(multiplexer_11_out), .out(multiplexer_6_out), .sel(undriven_3), .en(1'b0));
  Multiplexer #(.disabled("Z"), .enable("true"), .width(8)) multiplexer_7 (
    .in0(multiplexer_14_out), .in1(multiplexer_10_out), .out(multiplexer_7_out), .sel(undriven_3), .en(1'b1));
  Multiplexer #(.disabled("Z"), .enable("true"), .width(8)) multiplexer_8 (
    .in0(multiplexer_9_out), .in1(multiplexer_13_out), .out(multiplexer_8_out), .sel(undriven_3), .en(1'b0));
  Multiplexer #(.disabled("Z"), .enable("true"), .width(8)) multiplexer_9 (
    .in0(multiplexer_15_out), .in1(multiplexer_12_out), .out(multiplexer_9_out), .sel(undriven_3), .en(1'b1));
  Multiplexer #(.disabled("Z"), .enable("true"), .width(8)) multiplexer_10 (
    .in0(multiplexer_11_out), .in1(multiplexer_7_out), .out(multiplexer_10_out), .sel(undriven_3), .en(1'b0));
  Multiplexer #(.disabled("Z"), .enable("true"), .width(8)) multiplexer_11 (
    .in0(multiplexer_16_out), .in1(multiplexer_6_out), .out(multiplexer_11_out), .sel(undriven_3), .en(1'b1));
  Multiplexer #(.disabled("Z"), .enable("true"), .width(8)) multiplexer_12 (
    .in0(multiplexer_13_out), .in1(multiplexer_9_out), .out(multiplexer_12_out), .sel(undriven_3), .en(1'b0));
  Multiplexer #(.disabled("Z"), .enable("true"), .width(8)) multiplexer_13 (
    .in0(multiplexer_17_out), .in1(multiplexer_6_out), .out(multiplexer_13_out), .sel(undriven_3), .en(1'b1));
  Multiplexer #(.disabled("Z"), .enable("true"), .width(8)) multiplexer_14 (
    .in0(in_8[7:0]), .in1(in_8[31:24]), .out(multiplexer_14_out), .sel(undriven_4), .en(1'b1));
  Multiplexer #(.disabled("Z"), .enable("true"), .width(8)) multiplexer_15 (
    .in0(in_8[15:8]), .in1(in_8[7:0]), .out(multiplexer_15_out), .sel(undriven_4), .en(1'b1));
  Multiplexer #(.disabled("Z"), .enable("true"), .width(8)) multiplexer_16 (
    .in0(in_8[23:16]), .in1(in_8[15:8]), .out(multiplexer_16_out), .sel(undriven_4), .en(1'b1));
  Multiplexer #(.disabled("Z"), .enable("true"), .width(8)) multiplexer_17 (
    .in0(in_8[31:24]), .in1(in_8[23:16]), .out(multiplexer_17_out), .sel(undriven_4), .en(1'b1));
  Multiplexer #(.disabled("Z"), .enable("true"), .width(8)) multiplexer_18 (
    .in0(multiplexer_6_out), .in1(multiplexer_8_out), .out(in_8[7:0]), .sel(undriven_4), .en(1'b0));
  Multiplexer #(.disabled("Z"), .enable("true"), .width(8)) multiplexer_19 (
    .in0(multiplexer_8_out), .in1(multiplexer_10_out), .out(in_8[15:8]), .sel(undriven_4), .en(1'b0));
  Multiplexer #(.disabled("Z"), .enable("true"), .width(8)) multiplexer_20 (
    .in0(multiplexer_10_out), .in1(multiplexer_12_out), .out(in_8[23:16]), .sel(undriven_4), .en(1'b0));
  Multiplexer #(.disabled("Z"), .enable("true"), .width(8)) multiplexer_21 (
    .in0(multiplexer_12_out), .in1(multiplexer_6_out), .out(in_8[31:24]), .sel(undriven_4), .en(1'b0));
  // Probe on {EO, rom_2_data, JZ, JGT, JLT, NO, F, NY, EY, NX, EX, rom_1_data}
  // Probe on undriven_5
  _74138 #(.ShowInternalStructure("true")) u_74138_1 (
    .pin1(rom_1_data[0]), .pin2(rom_1_data[1]), .pin3(rom_1_data[2]), .pin4(n74138_1_pin4),
    .pin5(n74138_1_pin4), .pin6(n74138_1_pin6), .pin7(n74138_1_pin7), .pin15(n74138_1_pin15), .pin14(AI),
    .pin13(DI), .pin12(II), .pin11(XI), .pin10(YI), .pin9(IVI));
  _74138 #(.ShowInternalStructure("true")) u_74138_2 (
    .pin1(EX), .pin2(NX), .pin3(EY), .pin4(n74138_2_pin4), .pin5(n74138_2_pin4), .pin6(EO), .pin7(IVO),
    .pin15(PO), .pin14(DO), .pin13(MO8L), .pin12(MO8H), .pin11(MO16L), .pin10(MO16H), .pin9(MO32));
  _74138 #(.ShowInternalStructure("true")) u_74138_3 (
    .pin1(rom_2_data[4]), .pin2(rom_2_data[5]), .pin3(rom_2_data[6]), .pin4(n74138_3_pin4),
    .pin5(n74138_3_pin4), .pin6(n74138_3_pin6), .pin7(MI32), .pin15(n74138_3_pin15), .pin14(PP1),
    .pin13(PP2), .pin12(PP4), .pin11(RT), .pin10(MI8), .pin9(MI16));
  not not_15 (not_15_out, n74138_1_pin7);
  Multiplexer #(.width(8)) multiplexer_22 (
    .in0(undriven_6), .in1(undriven_8), .out(multiplexer_22_out), .sel(undriven_10));
  Multiplexer #(.width(8)) multiplexer_23 (
    .in0(undriven_7), .in1(undriven_9), .out(multiplexer_23_out), .sel(undriven_10));
  Multiplexer #(.width(8)) multiplexer_24 (
    .in0(undriven_8), .in1(undriven_6), .out(multiplexer_24_out), .sel(undriven_10));
  Multiplexer #(.width(8)) multiplexer_25 (
    .in0(undriven_9), .in1(undriven_7), .out(multiplexer_25_out), .sel(undriven_10));
  // NoConnect on n74138_1_pin15
  // NoConnect on n74138_3_pin15
  Multiplexer #(.width(8)) multiplexer_26 (
    .in0(multiplexer_23_out), .in1(multiplexer_24_out), .out(multiplexer_26_out), .sel(undriven_11));
  Multiplexer #(.width(8)) multiplexer_27 (
    .in0(multiplexer_24_out), .in1(multiplexer_25_out), .out(multiplexer_27_out), .sel(undriven_11));
  Multiplexer #(.width(8)) multiplexer_28 (
    .in0(multiplexer_25_out), .in1(multiplexer_22_out), .out(multiplexer_28_out), .sel(undriven_11));
  Multiplexer #(.width(8)) multiplexer_29 (
    .in0(multiplexer_22_out), .in1(multiplexer_23_out), .out(multiplexer_29_out), .sel(undriven_11));
  and and_87 (IEN, not_15_out, NY);
  and and_88 (IDS, not_15_out, F);
  // Probe on {multiplexer_28_out, multiplexer_27_out, multiplexer_26_out, multiplexer_29_out}
  not not_16 (not_16_out, n74138_4_pin1[3]);
  _74138 #(.ShowInternalStructure("true")) u_74138_4 (
    .pin1(n74138_4_pin1[0]), .pin2(n74138_4_pin1[1]), .pin3(n74138_4_pin1[2]), .pin4(n74138_4_pin4),
    .pin5(n74138_4_pin4), .pin6(not_16_out), .pin7(n74138_4_pin7), .pin15(n74138_4_pin15),
    .pin14(n74138_4_pin14), .pin13(n74138_4_pin13), .pin12(n74138_4_pin12), .pin11(n74138_4_pin11),
    .pin10(n74138_4_pin10), .pin9(n74138_4_pin9));
  _74138 #(.ShowInternalStructure("true")) u_74138_5 (
    .pin1(n74138_4_pin1[0]), .pin2(n74138_4_pin1[1]), .pin3(n74138_4_pin1[2]), .pin4(n74138_5_pin4),
    .pin5(n74138_5_pin4), .pin6(n74138_4_pin1[3]), .pin7(n74138_5_pin7), .pin15(n74138_5_pin15),
    .pin14(n74138_5_pin14), .pin13(n74138_5_pin13), .pin12(n74138_5_pin12), .pin11(n74138_5_pin11),
    .pin10(n74138_5_pin10), .pin9(n74138_5_pin9));
  _74138 #(.ShowInternalStructure("true")) u_74138_6 (
    .pin1(n74138_4_pin1[4]), .pin2(n74138_4_pin1[5]), .pin3(n74138_4_pin1[6]), .pin4(n74138_6_pin4),
    .pin5(n74138_6_pin4), .pin6(n74138_6_pin6), .pin7(n74138_6_pin7), .pin15(n74138_6_pin15),
    .pin14(n74138_6_pin14), .pin13(n74138_6_pin13), .pin12(n74138_6_pin12), .pin11(n74138_6_pin11),
    .pin10(n74138_6_pin10), .pin9(n74138_6_pin9));
  // NoConnect on n74138_4_pin15
  // NoConnect on n74138_5_pin15
  // NoConnect on n74138_6_pin15
  // Probe on ADDR
  ROM #(.addrWidth(9)) rom_3 (.addr(ADDR[8:0]), .data(rom_3_data));
  ROM #(.addrWidth(9)) rom_4 (.addr(ADDR[8:0]), .data(rom_4_data));
  ROM #(.addrWidth(9)) rom_5 (.addr(ADDR[8:0]), .data(rom_5_data));
  ROM #(.addrWidth(9)) rom_6 (.addr(ADDR[8:0]), .data(rom_6_data));
  not not_17 (not_17_out, LOAD_CLK);
  not not_18 (not_18_out, ROM_EN);
  not not_19 (not_19_out, RAM_EN);
  assign BUSS[7:0] = not_18_out ? rom_3_data : 8'bz;  // Controlled_Buffer controlled_buffer_53
  assign BUSS[15:8] = not_18_out ? rom_4_data : 8'bz;  // Controlled_Buffer controlled_buffer_54
  assign BUSS[23:16] = not_18_out ? rom_5_data : 8'bz;  // Controlled_Buffer controlled_buffer_55
  assign BUSS[31:24] = not_18_out ? rom_6_data : 8'bz;  // Controlled_Buffer controlled_buffer_56
  or or_39 (or_39_out, not_17_out, not_19_out);
  RAM #(.addrWidth(18), .asyncread("true"), .dataWidth(16), .databus("bidir")) ram_9 (
    .addr(ADDR[17:0]), .we(not_17_out), .oe(not_19_out), .clk(or_39_out), .data(BUSS[15:0]));
  RAM #(.addrWidth(18), .asyncread("true"), .dataWidth(16), .databus("bidir")) ram_10 (
    .addr(ADDR[17:0]), .we(not_17_out), .oe(not_19_out), .clk(or_39_out), .data(BUSS[31:16]));
  or or_40 (or_40_out, ADDR[10], ADDR[11]);
  or or_41 (or_41_out, ADDR[12], ADDR[13]);
  or or_42 (or_42_out, ADDR[14], ADDR[15]);
  or or_43 (or_43_out, ADDR[16], ADDR[17]);
  or or_44 (or_44_out, ADDR[18], ADDR[19]);
  // Probe on BUSS
  or or_45 (or_45_out, or_41_out, or_42_out);
  or or_46 (or_46_out, or_45_out, or_47_out);
  or or_47 (or_47_out, or_43_out, or_44_out);
  or or_48 (or_48_out, or_40_out, or_46_out);
  nand nand_2 (LOAD_CLK, MI, CLK);
  nand nand_3 (RAM_EN, MO, or_48_out);
  nand nand_4 (nand_4_out, or_48_out, or_48_out);
  nand nand_5 (ROM_EN, MO, nand_4_out);
  // also tied to GND on the sheet: {D0[0], D0[1], D0[2], D0[7], D1[0], D1[3], D1[5], D1[7], D2[0], D2[1], D2[3], D2[6], D2[7], D3[0], D3[2], D3[3], D3[5], D3[6], D3[7], n74138_1_pin4, n74138_2_pin4, n74138_3_pin4, n74138_6_pin4, n74138_4_pin4, n74138_5_pin4}
  // also tied to VCC on the sheet: {D0[3], D0[4], D0[5], D0[6], D1[1], D1[2], D1[4], D1[6], D2[2], D2[4], D2[5], D3[1], D3[4], n74138_1_pin6, n74138_3_pin6, n74138_6_pin6}

  // Other names for the same wires on the sheet: word_addr[18:0] = in_4[20:2]; S0 = SELL0; S1 = SELL1; A0 = in_4[0];
  //   A1 = in_4[1]; B1_3 = B0_2; B1_3W = B0_2W; B2_3 = B1_2; B2_3W = B1_2W; B3_2 = B0_3; B3_2W = B0_3W; B3_3 = B2_2;
  //   B3_3W = B2_2W

  // Notes on the sheet:
  //   Depending on select mode (B,H,W), need to enable multiple chips
  //   00 = 8 bit, 01 = half word, 10=word, 11 ERROR
  //   A[0:1] selects chip
  //   Another method using muxes. it's a bit picky about settings of mux, makes me concerned would need controlled buffers regardless.
  //   contents of rom_1 (hex, n*v repeats v):
  //   1 23 19 35 ac 0 0 0 1 23 6*0 1 23 6*0 1 23 6*0 1 23 6*0 1 23 6*0 1 23 6*0 1 23 6*0 1 23 6*0 1 23 6*0
  //   1 23 6*0 1 23 6*0 1 23 6*0 1 23 6*0 1 23 6*0 1 23 6*0 1 23 6*0 1 23 6*0 1 23 6*0 1 23 6*0 1 23 6*0 1
  //   23 6*0 1 23 6*0 1 23 6*0 1 23 6*0 1 23 6*0 1 23 6*0 1 23 6*0 1 23 6*0 1 23 6*0 1 23 6*0 1 23 6*0 1
  //   23 6*0 1 23 6*0 1 23 6*0 1 23 6*0 1 23 6*0 1 23 6*0 1 23 6*0 1 23 6*0 1 23 6*0 1 23 6*0 1 23 6*0 1
  //   23 6*0 1 23 6*0 1 23 6*0 1 23 6*0 1 23 6*0 1 23 6*0 1 23 6*0 1 23 6*0 1 23 6*0 1 23 6*0 1 23 6*0 1
  //   23 6*0 1 23 6*0 1 23 6*0 1 23 6*0 1 23 6*0 1 23 6*0 1 23 6*0 1 23 6*0 1 23 6*0 1 23 6*0 1 23 6*0 1
  //   23 6*0 1 23 6*0 1 23 6*0 1 23 6*0 1 23 6*0 1 23 6*0 1 23 6*0 1 23 6*0 1 23 6*0 1 23 6*0 1 23 6*0 1
  //   23 6*0 1 23 6*0 1 23 6*0 1 23 6*0 1 23 6*0 1 23 6*0 1 23 6*0 1 23 6*0 1 23 6*0 1 23 6*0 1 23 6*0 1
  //   23 6*0 1 23 6*0 1 23 6*0 1 23 6*0 1 23 6*0 1 23 6*0 1 23 6*0 1 23 6*0 1 23 6*0 1 23 6*0 1 23 6*0 1
  //   23 6*0 1 23 6*0 1 23 6*0 1 23 6*0 1 23 6*0 1 23 6*0 1 23 6*0 1 23 6*0 1 23 6*0 1 23 6*0 1 23 6*0 1
  //   23 6*0 1 23 6*0 1 23 6*0 1 23 6*0 1 23 6*0 1 23 6*0 1 23 6*0 1 23 6*0 1 23 6*0 1 23 6*0 1 23 6*0 1
  //   23 6*0 1 23 6*0 1 23 6*0 1 23 6*0 1 23 6*0 1 23 6*0 1 23 6*0 1 23 6*0 1 23 6*0 1 23 6*0 1 23 6*0 1
  //   23 6*0 1 23 6*0 1 23 6*0 1 23 6*0 1 23 6*0 1 23 6*0 1 23 6*0 1 23 6*0 1 23 6*0 1 23 6*0 1 23 6*0 1
  //   23 6*0 1 23 6*0 1 23 6*0 1 23 6*0 1 23 6*0 1 23 6*0 1 23 6*0 1 23 6*0 1 23 6*0 1 23 6*0 1 23 6*0 1
  //   23 6*0 1 23 6*0 1 23 6*0 1 23 6*0 1 23 6*0 1 23 6*0 1 23 6*0 1 23 6*0 1 23 6*0 1 23 6*0 1 23 6*0 1
  //   23 6*0 1 23 6*0 1 23 6*0 1 23 6*0 1 23 6*0 1 23 6*0 1 23 6*0 1 23 6*0 1 23 6*0 1 23 6*0 1 23 6*0 1
  //   23 6*0 1 23 6*0 1 23 6*0 1 23 6*0 1 23 6*0 1 23 6*0 1 23 6*0 1 23 6*0 1 23 6*0 1 23 6*0 1 23 6*0 1
  //   23 6*0 1 23 6*0 1 23 6*0 1 23 6*0 1 23 6*0 1 23 6*0 1 23 6*0 1 23 6*0 1 23 6*0 1 23 6*0 1 23 6*0 1
  //   23 6*0 1 23 6*0 1 23 6*0 1 23 6*0 1 23 6*0 1 23 6*0 1 23 6*0 1 23 6*0 1 23 6*0 1 23 6*0 1 23 6*0 1
  //   23 6*0 1 23 6*0 1 23 6*0 1 23 6*0 1 23 6*0 1 23 6*0 1 23 6*0 1 23 6*0 1 23 6*0 1 23 6*0 1 23 6*0 1
  //   23 6*0 1 23 6*0 1 23 6*0 1 23 6*0 1 23 6*0 1 23 6*0 1 23 6*0 1 23 6*0 1 23 6*0 1 23 6*0 1 23 6*0 1
  //   23 6*0 1 23 6*0 1 23 6*0 1 23 6*0 1 23 6*0 1 23 6*0 1 23 6*0 1 23 6*0 1 23 6*0 1 23 6*0 1 23 6*0 1
  //   23 6*0 1 23 6*0 1 23 6*0 1 23 6*0 1 23 6*0 1 23 6*0 1 23 6*0 1 23 6*0 1 23 6*0 1 23 6*0 1 23 6*0 1
  //   23 6*0 1 23 6*0 1 23 6*0 1 23
  //   contents of rom_2 (hex, n*v repeats v):
  //   80 a0 80 80 0 c0 c0 c0 80 a0 6*c0 80 a0 6*c0 80 a0 6*c0 80 a0 6*c0 80 a0 6*c0 80 a0 6*c0 80 a0 6*c0
  //   80 a0 6*c0 80 a0 6*c0 80 a0 6*c0 80 a0 6*c0 80 a0 6*c0 80 a0 6*c0 80 a0 6*c0 80 a0 6*c0 80 a0 6*c0
  //   80 a0 6*c0 80 a0 6*c0 80 a0 6*c0 80 a0 6*c0 80 a0 6*c0 80 a0 6*c0 80 a0 6*c0 80 a0 6*c0 80 a0 6*c0
  //   80 a0 6*c0 80 a0 6*c0 80 a0 6*c0 80 a0 6*c0 80 a0 6*c0 80 a0 6*c0 80 a0 6*c0 80 a0 6*c0 80 a0 6*c0
  //   80 a0 6*c0 80 a0 6*c0 80 a0 6*c0 80 a0 6*c0 80 a0 6*c0 80 a0 6*c0 80 a0 6*c0 80 a0 6*c0 80 a0 6*c0
  //   80 a0 6*c0 80 a0 6*c0 80 a0 6*c0 80 a0 6*c0 80 a0 6*c0 80 a0 6*c0 80 a0 6*c0 80 a0 6*c0 80 a0 6*c0
  //   80 a0 6*c0 80 a0 6*c0 80 a0 6*c0 80 a0 6*c0 80 a0 6*c0 80 a0 6*c0 80 a0 6*c0 80 a0 6*c0 80 a0 6*c0
  //   80 a0 6*c0 80 a0 6*c0 80 a0 6*c0 80 a0 6*c0 80 a0 6*c0 80 a0 6*c0 80 a0 6*c0 80 a0 6*c0 80 a0 6*c0
  //   80 a0 6*c0 80 a0 6*c0 80 a0 6*c0 80 a0 6*c0 80 a0 6*c0 80 a0 6*c0 80 a0 6*c0 80 a0 6*c0 80 a0 6*c0
  //   80 a0 6*c0 80 a0 6*c0 80 a0 6*c0 80 a0 6*c0 80 a0 6*c0 80 a0 6*c0 80 a0 6*c0 80 a0 6*c0 80 a0 6*c0
  //   80 a0 6*c0 80 a0 6*c0 80 a0 6*c0 80 a0 6*c0 80 a0 6*c0 80 a0 6*c0 80 a0 6*c0 80 a0 6*c0 80 a0 6*c0
  //   80 a0 6*c0 80 a0 6*c0 80 a0 6*c0 80 a0 6*c0 80 a0 6*c0 80 a0 6*c0 80 a0 6*c0 80 a0 6*c0 80 a0 6*c0
  //   80 a0 6*c0 80 a0 6*c0 80 a0 6*c0 80 a0 6*c0 80 a0 6*c0 80 a0 6*c0 80 a0 6*c0 80 a0 6*c0 80 a0 6*c0
  //   80 a0 6*c0 80 a0 6*c0 80 a0 6*c0 80 a0 6*c0 80 a0 6*c0 80 a0 6*c0 80 a0 6*c0 80 a0 6*c0 80 a0 6*c0
  //   80 a0 6*c0 80 a0 6*c0 80 a0 6*c0 80 a0 6*c0 80 a0 6*c0 80 a0 6*c0 80 a0 6*c0 80 a0 6*c0 80 a0 6*c0
  //   80 a0 6*c0 80 a0 6*c0 80 a0 6*c0 80 a0 6*c0 80 a0 6*c0 80 a0 6*c0 80 a0 6*c0 80 a0 6*c0 80 a0 6*c0
  //   80 a0 6*c0 80 a0 6*c0 80 a0 6*c0 80 a0 6*c0 80 a0 6*c0 80 a0 6*c0 80 a0 6*c0 80 a0 6*c0 80 a0 6*c0
  //   80 a0 6*c0 80 a0 6*c0 80 a0 6*c0 80 a0 6*c0 80 a0 6*c0 80 a0 6*c0 80 a0 6*c0 80 a0 6*c0 80 a0 6*c0
  //   80 a0 6*c0 80 a0 6*c0 80 a0 6*c0 80 a0 6*c0 80 a0 6*c0 80 a0 6*c0 80 a0 6*c0 80 a0 6*c0 80 a0 6*c0
  //   80 a0 6*c0 80 a0 6*c0 80 a0 6*c0 80 a0 6*c0 80 a0 6*c0 80 a0 6*c0 80 a0 6*c0 80 a0 6*c0 80 a0 6*c0
  //   80 a0 6*c0 80 a0 6*c0 80 a0 6*c0 80 a0 6*c0 80 a0 6*c0 80 a0 6*c0 80 a0 6*c0 80 a0 6*c0 80 a0 6*c0
  //   80 a0 6*c0 80 a0 6*c0 80 a0 6*c0 80 a0 6*c0 80 a0 6*c0 80 a0 6*c0 80 a0 6*c0 80 a0 6*c0 80 a0 6*c0
  //   80 a0 6*c0 80 a0 6*c0 80 a0 6*c0 80 a0 6*c0 80 a0 6*c0 80 a0 6*c0 80 a0 6*c0 80 a0 6*c0 80 a0 6*c0
  //   80 a0 6*c0 80 a0 6*c0 80 a0 6*c0 80 a0 6*c0 80 a0 6*c0 80 a0 6*c0 80 a0 6*c0 80 a0 6*c0 80 a0 6*c0
  //   80 a0 6*c0 80 a0 6*c0 80 a0 6*c0 80 a0 6*c0 80 a0 6*c0 80 a0 6*c0 80 a0 6*c0 80 a0 6*c0 80 a0 6*c0
  //   80 a0 6*c0 80 a0 6*c0 80 a0 6*c0 80 a0 6*c0 80 a0 6*c0 80 a0 6*c0 80 a0 6*c0 80 a0 6*c0 80 a0 6*c0
  //   80 a0 6*c0 80 a0 6*c0 80 a0 6*c0 80 a0 6*c0 80 a0 6*c0 80 a0 6*c0 80 a0 6*c0 80 a0 6*c0 80 a0 6*c0
  //   80 a0 6*c0 80 a0 6*c0 80 a0 6*c0 80 a0 6*c0 80 a0 6*c0 80 a0 6*c0 80 a0 6*c0 80 a0 6*c0 80 a0 6*c0
  //   80 a0 6*c0 80 a0 6*c0 80 a0 6*c0 80 a0 6*c0 80 a0 6*c0
  //   contents of rom_3 (hex, n*v repeats v):
  //   0 0 1 0 2 0 3 0 1 3 0 64 5f 0 5 0 0 8 0 0 4 0 0 8 1 0 e b 0 1d 0 16 0 0 ff 0 d c 2a 4*0 e 0 2f 2a 0
  //   0 0 f 0 0 0 33 5*0 fe 0 0 80 0 0 40 0 0 20 0 0 10 0 0 8 0 0 4 0 0 2 0 0 1 fe 0 0 52 0 0 43 0 0 12 0
  //   2 4*0 a 0 1 1 2 2 5 3 0 4 0 5 3 6 3 7 4 8 0 9 1 a c 1 0 c 0 0 7e 0 a 2a 0 ab 6*0 af 0 0 16 28 2 0 a
  //   5 8 0 c0 6*0 8 3 0 d2 0 0 0 e5 0 0 c9 1 6*0 fe fd 0 fe fe 0 0 1 0 0 b5 fe 0 0 fd 0 0 1 0 2 0 3 0 3 0
  //   0 0 2 0 0 0 cb 0 0 2 0 1 0 0 1 3 2 3 0 e0 0 1 1 3 0 da 0 48 65 6c 6c 6f 2c 20 77 6f 72 6c 64 21 a
  //   contents of rom_6 (hex, n*v repeats v):
  //   67 e8 67 e8 67 e8 67 e8 67 6 e8 67 16 e8 67 a0 e8 67 b0 e8 67 53 e8 67 46 e8 67 36 e8 67 8e 0 50 e8
  //   85 2 5b 5b 67 5d e8 5d e8 67 b9 0 67 e8 6b ff 67 a1 b0 bb 0 eb 0 85 10 6b ff 58 80 59 58 40 59 58 20
  //   59 58 10 59 58 8 59 58 4 59 58 2 59 58 1 59 eb 0 62 69 8c 62 69 50 e8 6b ff a5 6b ff eb 0 6b ff 6b
  //   ff 6b ff 6b ff 6b ff 6b ff 6b ff 6b ff 6b ff 6b ff 6b ff 85 ff 67 4 b1 bb 0 e8 5b 67 4f 0 eb 0 62 15
  //   5a 4f 0 eb 0 5b 5b 78 e8 5b 5b 5b 62 0 6a 1 1f 1 eb 0 5b 5b 4f 0 eb 0 62 0 5a 4f 0 a6 5d 69 56 93 5d
  //   69 84 ff 6b ff 56 58 80 59 56 bb 0 84 ff c9 ff 6b ff 78 8 78 8 78 8 94 5d 69 ec 0 a1 e3 bb 0 93 5d
  //   69 5d 69 6b ff 6b ff 61 30 ba 0 e ff 56 56 bb 0 93
endmodule

module memory (
  input  MI,
  input  MO,
  input  CLK,
  input  [31:0] ADDR,
  input  [31:0] BUSS,
  input  SELL0,
  input  SELL1
);

  wire and_1_out, and_2_out, and_3_out, and_4_out, and_5_out, and_6_out, and_7_out, and_8_out, and_9_out,
       and_10_out, and_11_out, and_12_out, and_13_out, and_14_out, and_16_out, and_17_out, and_21_out,
       and_22_out, and_23_out, and_26_out, and_27_out, and_30_out, and_31_out, and_32_out, and_34_out,
       and_38_out, and_39_out, and_40_out, and_41_out, and_44_out, B, B0_0, B0_0W, B0_1, B0_1W, B0_2, B0_2W,
       B0_3, B0_3W, B1_0, B1_0W, B1_1, B1_1W, B1_2, B1_2W, B2_0, B2_0W, B2_1, B2_1W, B2_2, B2_2W, B3_0,
       B3_0W, B3_1, B3_1W, CHIP0, CHIP1, CHIP2, CHIP3, decoder_2_out0, decoder_2_out1, decoder_2_out2,
       decoder_2_out3, decoder_3_out0, decoder_3_out1, decoder_3_out2, decoder_3_out3, H, LOAD_CLK, nA0, nA1,
       nand_1_out, nand_2_out, nand_3_out, nand_4_out, not_6_out, not_7_out, not_8_out, not_9_out,
       not_10_out, not_11_out, not_12_out, not_13_out, not_14_out, not_15_out, or_1_out, or_2_out, or_3_out,
       or_4_out, or_5_out, or_6_out, or_7_out, or_8_out, or_9_out, or_10_out, or_12_out, or_13_out,
       or_14_out, or_15_out, or_20_out, or_21_out, or_22_out, or_23_out, or_24_out, or_25_out, or_26_out,
       or_27_out, or_28_out, or_29_out, or_30_out, or_31_out, or_32_out, or_33_out, or_34_out, or_35_out,
       or_36_out, RAM_CLK, RAM_EN, ROM_EN, W;
  wire [7:0] ram_1_data, ram_2_data, ram_3_data, ram_4_data, rom_1_data, rom_2_data, rom_3_data, rom_4_data;
  wire [18:0] multiplexer_1_out, multiplexer_2_out, multiplexer_3_out, word_addr_pp;

  Adder #(.width(19)) adder_1 (.a(19'h1), .b(ADDR[20:2]), .out(word_addr_pp));  // open: cin, cout
  // Probe on word_addr_pp
  not not_1 (nA1, ADDR[1]);
  not not_2 (nA0, ADDR[0]);
  or or_1 (or_1_out, ADDR[1], ADDR[0]);
  and and_1 (and_1_out, ADDR[0], ADDR[1]);
  Multiplexer #(.width(19)) multiplexer_1 (
    .in0(ADDR[20:2]), .in1(word_addr_pp), .out(multiplexer_1_out), .sel(or_1_out));
  and and_2 (and_2_out, RAM_CLK, CHIP0);
  Multiplexer #(.width(19)) multiplexer_2 (
    .in0(ADDR[20:2]), .in1(word_addr_pp), .out(multiplexer_2_out), .sel(ADDR[1]));
  and and_3 (and_3_out, RAM_CLK, CHIP1);
  Multiplexer #(.width(19)) multiplexer_3 (
    .in0(ADDR[20:2]), .in1(word_addr_pp), .out(multiplexer_3_out), .sel(and_1_out));
  and and_4 (and_4_out, RAM_CLK, CHIP2);
  and and_5 (and_5_out, RAM_CLK, CHIP3);
  RAM #(.addrWidth(19), .databus("bidir")) ram_1 (
    .addr(multiplexer_1_out), .we(LOAD_CLK), .oe(RAM_EN), .clk(and_2_out), .data(ram_1_data));
  ROM #(.addrWidth(9)) rom_1 (.addr(multiplexer_1_out[8:0]), .data(rom_1_data));
  RAM #(.addrWidth(19), .databus("bidir")) ram_2 (
    .addr(multiplexer_2_out), .we(LOAD_CLK), .oe(RAM_EN), .clk(and_3_out), .data(ram_2_data));
  ROM #(.addrWidth(9)) rom_2 (.addr(multiplexer_2_out[8:0]), .data(rom_2_data));
  RAM #(.addrWidth(19), .databus("bidir")) ram_3 (
    .addr(multiplexer_3_out), .we(LOAD_CLK), .oe(RAM_EN), .clk(and_4_out), .data(ram_3_data));
  ROM #(.addrWidth(9)) rom_3 (.addr(multiplexer_3_out[8:0]), .data(rom_3_data));
  RAM #(.addrWidth(19), .databus("bidir")) ram_4 (
    .addr(ADDR[20:2]), .we(LOAD_CLK), .oe(RAM_EN), .clk(and_5_out), .data(ram_4_data));
  ROM #(.addrWidth(9)) rom_4 (.addr(ADDR[10:2]), .data(rom_4_data));
  or or_2 (or_2_out, ADDR[10], ADDR[11]);
  or or_3 (or_3_out, ADDR[12], ADDR[13]);
  or or_4 (or_4_out, or_3_out, or_5_out);
  or or_5 (or_5_out, ADDR[14], ADDR[15]);
  or or_6 (or_6_out, ADDR[16], ADDR[17]);
  or or_7 (or_7_out, or_6_out, or_8_out);
  or or_8 (or_8_out, ADDR[18], ADDR[19]);
  or or_9 (or_9_out, or_2_out, or_10_out);
  or or_10 (or_10_out, or_4_out, or_7_out);
  assign ram_1_data = and_6_out ? rom_1_data : 8'bz;  // Controlled_Buffer controlled_buffer_1
  assign ram_2_data = and_7_out ? rom_2_data : 8'bz;  // Controlled_Buffer controlled_buffer_2
  assign ram_3_data = and_8_out ? rom_3_data : 8'bz;  // Controlled_Buffer controlled_buffer_3
  assign ram_4_data = and_9_out ? rom_4_data : 8'bz;  // Controlled_Buffer controlled_buffer_4
  and and_6 (and_6_out, ROM_EN, CHIP0);
  and and_7 (and_7_out, ROM_EN, CHIP1);
  and and_8 (and_8_out, ROM_EN, CHIP2);
  and and_9 (and_9_out, ROM_EN, CHIP3);
  nand nand_1 (nand_1_out, MI, CLK);
  nand nand_2 (nand_2_out, MO, or_9_out);
  nand nand_3 (nand_3_out, or_9_out, or_9_out);
  not not_3 (LOAD_CLK, nand_1_out);
  not not_4 (RAM_EN, nand_2_out);
  nand nand_4 (nand_4_out, MO, nand_3_out);
  not not_5 (ROM_EN, nand_4_out);
  Decoder #(.select(2)) decoder_1 (.out0(B), .out1(H), .out2(W), .sel({SELL1, SELL0}));  // open: out3, en
  assign BUSS[7:0] = B0_0 ? ram_1_data : 8'bz;  // Controlled_Buffer controlled_buffer_5
  assign BUSS[15:8] = B0_1 ? ram_1_data : 8'bz;  // Controlled_Buffer controlled_buffer_6
  assign BUSS[7:0] = B1_0 ? ram_2_data : 8'bz;  // Controlled_Buffer controlled_buffer_7
  assign BUSS[15:8] = B1_1 ? ram_2_data : 8'bz;  // Controlled_Buffer controlled_buffer_8
  assign BUSS[23:16] = B1_2 ? ram_2_data : 8'bz;  // Controlled_Buffer controlled_buffer_9
  assign BUSS[7:0] = B2_0 ? ram_3_data : 8'bz;  // Controlled_Buffer controlled_buffer_10
  assign BUSS[15:8] = B2_1 ? ram_3_data : 8'bz;  // Controlled_Buffer controlled_buffer_11
  assign BUSS[23:16] = B2_2 ? ram_3_data : 8'bz;  // Controlled_Buffer controlled_buffer_12
  assign BUSS[7:0] = B3_0 ? ram_4_data : 8'bz;  // Controlled_Buffer controlled_buffer_13
  assign BUSS[15:8] = B3_1 ? ram_4_data : 8'bz;  // Controlled_Buffer controlled_buffer_14
  or or_11 (RAM_CLK, LOAD_CLK, RAM_EN);
  assign BUSS[23:16] = B0_2 ? ram_1_data : 8'bz;  // Controlled_Buffer controlled_buffer_15
  assign BUSS[31:24] = B0_3 ? ram_1_data : 8'bz;  // Controlled_Buffer controlled_buffer_16
  assign BUSS[31:24] = B0_2 ? ram_2_data : 8'bz;  // Controlled_Buffer controlled_buffer_17
  assign BUSS[31:24] = B1_2 ? ram_3_data : 8'bz;  // Controlled_Buffer controlled_buffer_18
  assign BUSS[23:16] = B0_3 ? ram_4_data : 8'bz;  // Controlled_Buffer controlled_buffer_19
  assign BUSS[31:24] = B2_2 ? ram_4_data : 8'bz;  // Controlled_Buffer controlled_buffer_20
  assign ram_1_data = B0_3W ? BUSS[31:24] : 8'bz;  // Controlled_Buffer controlled_buffer_21
  assign ram_2_data = B0_2W ? BUSS[31:24] : 8'bz;  // Controlled_Buffer controlled_buffer_22
  assign ram_3_data = B1_2W ? BUSS[31:24] : 8'bz;  // Controlled_Buffer controlled_buffer_23
  assign ram_4_data = B2_2W ? BUSS[31:24] : 8'bz;  // Controlled_Buffer controlled_buffer_24
  assign ram_1_data = B0_1W ? BUSS[15:8] : 8'bz;  // Controlled_Buffer controlled_buffer_25
  assign ram_1_data = B0_2W ? BUSS[23:16] : 8'bz;  // Controlled_Buffer controlled_buffer_26
  assign ram_2_data = B1_0W ? BUSS[7:0] : 8'bz;  // Controlled_Buffer controlled_buffer_27
  assign ram_2_data = B1_1W ? BUSS[15:8] : 8'bz;  // Controlled_Buffer controlled_buffer_28
  assign ram_2_data = B1_2W ? BUSS[23:16] : 8'bz;  // Controlled_Buffer controlled_buffer_29
  assign ram_3_data = B2_0W ? BUSS[7:0] : 8'bz;  // Controlled_Buffer controlled_buffer_30
  assign ram_3_data = B2_1W ? BUSS[15:8] : 8'bz;  // Controlled_Buffer controlled_buffer_31
  assign ram_3_data = B2_2W ? BUSS[23:16] : 8'bz;  // Controlled_Buffer controlled_buffer_32
  assign ram_4_data = B3_1W ? BUSS[15:8] : 8'bz;  // Controlled_Buffer controlled_buffer_33
  assign ram_4_data = B0_3W ? BUSS[23:16] : 8'bz;  // Controlled_Buffer controlled_buffer_34
  // Probe on BUSS
  assign ram_1_data = B0_0W ? BUSS[7:0] : 8'bz;  // Controlled_Buffer controlled_buffer_35
  assign ram_4_data = B3_0W ? BUSS[7:0] : 8'bz;  // Controlled_Buffer controlled_buffer_36
  not not_6 (not_6_out, SELL1);
  not not_7 (not_7_out, SELL0);
  not not_8 (not_8_out, SELL1);
  not not_9 (not_9_out, SELL0);
  and and_10 (and_10_out, SELL0, not_6_out);
  and and_11 (and_11_out, not_7_out, not_8_out);
  and and_12 (and_12_out, not_9_out, SELL1);
  Decoder #(.select(2)) decoder_2 (
    .out0(decoder_2_out0), .out1(decoder_2_out1), .out2(decoder_2_out2), .out3(decoder_2_out3),
    .sel(ADDR[1:0]), .en(and_10_out));
  Decoder #(.select(2)) decoder_3 (
    .out0(decoder_3_out0), .out1(decoder_3_out1), .out2(decoder_3_out2), .out3(decoder_3_out3),
    .sel(ADDR[1:0]), .en(and_11_out));
  or or_12 (or_12_out, decoder_2_out0, decoder_2_out3);
  or or_13 (or_13_out, decoder_2_out0, decoder_2_out1);
  or or_14 (or_14_out, decoder_2_out1, decoder_2_out2);
  or or_15 (or_15_out, decoder_2_out2, decoder_2_out3);
  or or_16 (CHIP0, or_12_out, decoder_3_out0, and_12_out);
  or or_17 (CHIP1, or_13_out, decoder_3_out1, and_12_out);
  or or_18 (CHIP2, or_14_out, decoder_3_out2, and_12_out);
  or or_19 (CHIP3, or_15_out, decoder_3_out3, and_12_out);
  and and_13 (and_13_out, CHIP0, not_10_out);
  and and_14 (and_14_out, not_15_out, and_13_out);
  or or_20 (or_20_out, and_14_out, B2_2);
  or or_21 (or_21_out, and_14_out, B2_2W);
  and and_15 (B0_0W, MI, or_21_out);
  not not_10 (not_10_out, CHIP3);
  and and_16 (and_16_out, CHIP3, CHIP0);
  and and_17 (and_17_out, not_15_out, and_16_out);
  or or_22 (or_22_out, and_17_out, B1_2);
  and and_18 (B0_0, or_20_out, MO);
  and and_19 (B0_1, or_22_out, MO);
  or or_23 (or_23_out, and_17_out, B1_2W);
  and and_20 (B0_1W, MI, or_23_out);
  not not_11 (not_11_out, CHIP0);
  and and_21 (and_21_out, CHIP1, not_11_out);
  and and_22 (and_22_out, CHIP1, CHIP2);
  or or_24 (or_24_out, and_22_out, and_21_out);
  and and_23 (and_23_out, not_15_out, or_24_out);
  or or_25 (or_25_out, and_23_out, B0_3);
  and and_24 (B1_0, or_25_out, MO);
  or or_26 (or_26_out, and_23_out, B0_3W);
  and and_25 (B1_0W, MI, or_26_out);
  and and_26 (and_26_out, CHIP0, CHIP1);
  and and_27 (and_27_out, not_15_out, and_26_out);
  or or_27 (or_27_out, and_27_out, B2_2);
  and and_28 (B1_1, or_27_out, MO);
  or or_28 (or_28_out, and_27_out, B2_2W);
  and and_29 (B1_1W, MI, or_28_out);
  not not_12 (not_12_out, CHIP1);
  and and_30 (and_30_out, CHIP2, not_12_out);
  and and_31 (and_31_out, not_15_out, and_30_out);
  and and_32 (and_32_out, not_15_out, and_34_out);
  or or_29 (or_29_out, and_31_out, B0_2);
  and and_33 (B2_0, or_29_out, MO);
  not not_13 (not_13_out, CHIP3);
  and and_34 (and_34_out, CHIP2, CHIP1, not_13_out);
  or or_30 (or_30_out, and_32_out, B0_3);
  and and_35 (B2_1, or_30_out, MO);
  or or_31 (or_31_out, and_31_out, B0_2W);
  or or_32 (or_32_out, and_32_out, B0_3W);
  and and_36 (B2_0W, MI, or_31_out);
  and and_37 (B2_1W, MI, or_32_out);
  not not_14 (not_14_out, CHIP2);
  and and_38 (and_38_out, CHIP3, not_14_out);
  and and_39 (and_39_out, CHIP3, CHIP2);
  and and_40 (and_40_out, not_15_out, and_38_out);
  and and_41 (and_41_out, not_15_out, and_39_out);
  or or_33 (or_33_out, and_40_out, B1_2);
  or or_34 (or_34_out, and_41_out, B0_2);
  and and_42 (B3_0, or_33_out, MO);
  and and_43 (B3_1, or_34_out, MO);
  and and_44 (and_44_out, CHIP3, CHIP2, CHIP1, CHIP0);
  not not_15 (not_15_out, and_44_out);
  or or_35 (or_35_out, and_40_out, B1_2W);
  and and_45 (B3_0W, MI, or_35_out);
  or or_36 (or_36_out, and_41_out, B0_2W);
  and and_46 (B3_1W, MI, or_36_out);
  Demultiplexer #(.select(3)) demultiplexer_1 (
    .out0(B2_2), .out1(B0_3), .out2(B0_2), .out3(B1_2), .out4(B2_2W), .out5(B0_3W), .out6(B0_2W),
    .out7(B1_2W), .in(1'b1), .sel({MI, ADDR[1:0]}));

  // Other names for the same wires on the sheet: S0 = SELL0; S1 = SELL1; A0 = ADDR[0]; A1 = ADDR[1]; B1_3 = B0_2;
  //   B1_3W = B0_2W; B2_3 = B1_2; B2_3W = B1_2W; B3_2 = B0_3; B3_2W = B0_3W; B3_3 = B2_2; B3_3W = B2_2W;
  //   word_addr[18:0] = ADDR[20:2]

  // Notes on the sheet:
  //   MI = write to memory
  //   MO = output from meory
  //   00 = 8 bit, 01 = half word, 10=word, 11 ERROR
  //   contents of rom_1 (hex, n*v repeats v):
  //   1 5
  //   contents of rom_2 (hex, n*v repeats v):
  //   2 6
  //   contents of rom_3 (hex, n*v repeats v):
  //   3 7
  //   contents of rom_4 (hex, n*v repeats v):
  //   4 8
endmodule

module TReg (
  input  CLK,
  input  TRI,
  input  TRO,
  input  [31:0] D_IN,
  output [31:0] D_OUT
);

  wire [7:0] n74377_1_pin2, n74377_2_pin2, n74377_3_pin2, n74377_4_pin2;

  _74377 u_74377_1 (
    .pin1(TRI), .pin2(n74377_1_pin2[0]), .pin3(D_IN[16]), .pin4(D_IN[17]), .pin5(n74377_1_pin2[1]),
    .pin6(n74377_1_pin2[2]), .pin7(D_IN[18]), .pin8(D_IN[19]), .pin9(n74377_1_pin2[3]),
    .pin19(n74377_1_pin2[7]), .pin18(D_IN[23]), .pin17(D_IN[22]), .pin16(n74377_1_pin2[6]),
    .pin15(n74377_1_pin2[5]), .pin14(D_IN[21]), .pin13(D_IN[20]), .pin12(n74377_1_pin2[4]), .pin11(CLK));
  _74377 u_74377_2 (
    .pin1(TRI), .pin2(n74377_2_pin2[0]), .pin3(D_IN[24]), .pin4(D_IN[25]), .pin5(n74377_2_pin2[1]),
    .pin6(n74377_2_pin2[2]), .pin7(D_IN[26]), .pin8(D_IN[27]), .pin9(n74377_2_pin2[3]),
    .pin19(n74377_2_pin2[7]), .pin18(D_IN[31]), .pin17(D_IN[30]), .pin16(n74377_2_pin2[6]),
    .pin15(n74377_2_pin2[5]), .pin14(D_IN[29]), .pin13(D_IN[28]), .pin12(n74377_2_pin2[4]), .pin11(CLK));
  _74377 u_74377_3 (
    .pin1(TRI), .pin2(n74377_3_pin2[0]), .pin3(D_IN[0]), .pin4(D_IN[1]), .pin5(n74377_3_pin2[1]),
    .pin6(n74377_3_pin2[2]), .pin7(D_IN[2]), .pin8(D_IN[3]), .pin9(n74377_3_pin2[3]),
    .pin19(n74377_3_pin2[7]), .pin18(D_IN[7]), .pin17(D_IN[6]), .pin16(n74377_3_pin2[6]),
    .pin15(n74377_3_pin2[5]), .pin14(D_IN[5]), .pin13(D_IN[4]), .pin12(n74377_3_pin2[4]), .pin11(CLK));
  _74377 u_74377_4 (
    .pin1(TRI), .pin2(n74377_4_pin2[0]), .pin3(D_IN[8]), .pin4(D_IN[9]), .pin5(TRI), .pin6(n74377_4_pin2[2]),
    .pin7(D_IN[10]), .pin8(D_IN[11]), .pin9(n74377_4_pin2[3]), .pin19(n74377_4_pin2[7]), .pin18(D_IN[15]),
    .pin17(D_IN[14]), .pin16(n74377_4_pin2[6]), .pin15(n74377_4_pin2[5]), .pin14(D_IN[13]), .pin13(D_IN[12]),
    .pin12(TRO), .pin11(CLK));
  _74244 u_74244_1 (
    .pin1(TRO), .pin2(n74377_3_pin2[0]), .pin3(D_OUT[7]), .pin4(n74377_3_pin2[1]), .pin5(D_OUT[6]),
    .pin6(n74377_3_pin2[2]), .pin7(D_OUT[5]), .pin8(n74377_3_pin2[3]), .pin9(D_OUT[4]), .pin19(TRO),
    .pin18(D_OUT[0]), .pin17(n74377_3_pin2[7]), .pin16(D_OUT[1]), .pin15(n74377_3_pin2[6]), .pin14(D_OUT[2]),
    .pin13(n74377_3_pin2[5]), .pin12(D_OUT[3]), .pin11(n74377_3_pin2[4]));
  _74244 u_74244_2 (
    .pin1(TRO), .pin2(n74377_4_pin2[0]), .pin3(D_OUT[15]), .pin4(TRI), .pin5(D_OUT[14]),
    .pin6(n74377_4_pin2[2]), .pin7(D_OUT[13]), .pin8(n74377_4_pin2[3]), .pin9(D_OUT[12]), .pin19(TRO),
    .pin18(D_OUT[8]), .pin17(n74377_4_pin2[7]), .pin16(D_OUT[9]), .pin15(n74377_4_pin2[6]),
    .pin14(D_OUT[10]), .pin13(n74377_4_pin2[5]), .pin12(D_OUT[11]), .pin11(TRO));
  _74244 u_74244_3 (
    .pin1(TRO), .pin2(n74377_1_pin2[0]), .pin3(D_OUT[23]), .pin4(n74377_1_pin2[1]), .pin5(D_OUT[22]),
    .pin6(n74377_1_pin2[2]), .pin7(D_OUT[21]), .pin8(n74377_1_pin2[3]), .pin9(D_OUT[20]), .pin19(TRO),
    .pin18(D_OUT[16]), .pin17(n74377_1_pin2[7]), .pin16(D_OUT[17]), .pin15(n74377_1_pin2[6]),
    .pin14(D_OUT[18]), .pin13(n74377_1_pin2[5]), .pin12(D_OUT[19]), .pin11(n74377_1_pin2[4]));
  _74244 u_74244_4 (
    .pin1(TRO), .pin2(n74377_2_pin2[0]), .pin3(D_OUT[31]), .pin4(n74377_2_pin2[1]), .pin5(D_OUT[30]),
    .pin6(n74377_2_pin2[2]), .pin7(D_OUT[29]), .pin8(n74377_2_pin2[3]), .pin9(D_OUT[28]), .pin19(TRO),
    .pin18(D_OUT[24]), .pin17(n74377_2_pin2[7]), .pin16(D_OUT[25]), .pin15(n74377_2_pin2[6]),
    .pin14(D_OUT[26]), .pin13(n74377_2_pin2[5]), .pin12(D_OUT[27]), .pin11(n74377_2_pin2[4]));
endmodule
